// Logisim project lab1.1.circ as structural Verilog: 3 circuits, main circuit main
// Truth
module main (
  input  X,
  input  Y,
  input  Z,
  output F
);

  wire and_1_out, and_2_out, and_3_out;

  and and_1 (and_1_out, X, Z);
  and and_2 (and_2_out, Y, X);
  and and_3 (and_3_out, Z, Y);
  or or_1 (F, and_1_out, and_2_out, and_3_out);

  // Notes on the sheet:
  //   输入引脚
  //   请勿增加、删除引脚，用隧道标签构建电路，
  //   3输入多数表决器电路
  //   请勿更改电路封装外观。
  //   输出引脚
endmodule

module ec2 (
  input  in_1,
  input  in_2,
  input  in_3,
  input  in_4,
  output out_5,
  output out_6,
  output out_7,
  output out_8
);

  xor xor_1 (out_5, in_1, in_2);
  xor xor_2 (out_6, in_2, in_3);
  xor xor_3 (out_7, in_3, in_4);

  assign out_8 = in_4;
endmodule

module ec3 (
  input  I0,
  input  I1,
  input  I2,
  input  I3,
  output P_even,
  output P_odd
);

  wire xor_1_out, xor_2_out;

  xor xor_1 (xor_1_out, I0, I1);
  xor xor_2 (xor_2_out, xor_1_out, I2);
  xor xor_3 (P_even, xor_2_out, I3);
  not not_1 (P_odd, P_even);
endmodule
