// Logisim project lab2.1.circ as structural Verilog: 1 circuit, main circuit main
module main (
  input  G1,
  input  G2A_L,
  input  G2B_L,
  input  A,
  input  B,
  input  C,
  output Y0_L,
  output Y1_L,
  output Y2_L,
  output Y3_L,
  output Y4_L,
  output Y5_L,
  output Y6_L,
  output Y7_L
);

  wire nor_1_out, not_1_out, not_2_out, not_3_out, not_4_out, not_5_out, not_6_out, not_7_out, not_8_out,
       not_9_out, not_10_out, not_11_out, not_12_out, not_13_out;

  not not_1 (not_1_out, G1);
  nor nor_1 (nor_1_out, not_1_out, G2A_L, G2B_L);
  not not_2 (not_2_out, A);
  nand nand_1 (Y0_L, nor_1_out, not_2_out, not_3_out, not_4_out);
  not not_3 (not_3_out, B);
  not not_4 (not_4_out, C);
  nand nand_2 (Y1_L, nor_1_out, A, not_5_out, not_6_out);
  not not_5 (not_5_out, B);
  not not_6 (not_6_out, C);
  not not_7 (not_7_out, A);
  nand nand_3 (Y2_L, nor_1_out, not_7_out, B, not_8_out);
  not not_8 (not_8_out, C);
  nand nand_4 (Y3_L, nor_1_out, A, B, not_9_out);
  not not_9 (not_9_out, C);
  not not_10 (not_10_out, A);
  nand nand_5 (Y4_L, nor_1_out, not_10_out, not_11_out, C);
  not not_11 (not_11_out, B);
  nand nand_6 (Y5_L, nor_1_out, A, not_12_out, C);
  not not_12 (not_12_out, B);
  not not_13 (not_13_out, A);
  nand nand_7 (Y6_L, nor_1_out, not_13_out, B, C);
  nand nand_8 (Y7_L, nor_1_out, A, B, C);

  // Notes on the sheet:
  //   输入引脚
  //   请勿修改引脚名称、电路名称及电路封装外观
  //   提示：使用独立逻辑门实现3-8译码器，禁止直接使用译码器组件。
  //   输出引脚
endmodule
