// Logisim project lab2.2.circ as structural Verilog: 1 circuit, main circuit main
module main (
  input  I0,
  input  I1,
  input  I2,
  input  I4,
  input  I5,
  input  I3,
  input  I6,
  input  I7,
  output O0,
  output O1,
  output O2
);

  wire and_1_out, and_2_out, and_3_out, and_4_out, and_5_out, and_6_out, and_7_out, not_1_out, not_2_out,
       not_3_out, not_4_out, not_5_out, not_6_out, not_7_out, not_8_out;

  not not_1 (not_1_out, I0);
  not not_2 (not_2_out, I1);
  not not_3 (not_3_out, I2);
  not not_4 (not_4_out, I3);
  not not_5 (not_5_out, I4);
  not not_6 (not_6_out, I5);
  not not_7 (not_7_out, I6);
  not not_8 (not_8_out, I7);
  and and_1 (and_1_out, not_1_out, ~not_2_out);  // AND_Gate
  and and_2 (and_2_out, not_1_out, not_2_out, ~not_3_out);  // AND_Gate
  and and_3 (and_3_out, not_1_out, not_2_out, not_3_out, ~not_4_out);  // AND_Gate
  and and_4 (and_4_out, not_1_out, not_2_out, not_3_out, not_4_out, ~not_5_out);  // AND_Gate
  and and_5 (and_5_out, not_1_out, not_2_out, not_3_out, not_4_out, not_5_out, ~not_6_out);  // AND_Gate
  and and_6 (and_6_out, not_1_out, not_2_out, not_3_out, not_4_out, not_5_out, not_6_out, ~not_7_out);  // AND_Gate
  and and_7 (and_7_out, not_1_out, not_2_out, not_3_out, not_4_out, not_5_out, not_6_out, not_7_out, ~not_8_out);  // AND_Gate
  or or_1 (O0, and_4_out, and_5_out, and_6_out, and_7_out);
  or or_2 (O1, and_2_out, and_3_out, and_6_out, and_7_out);
  or or_3 (O2, and_1_out, and_3_out, and_5_out, and_7_out);
  Hex_Digit_Display hex_digit_display_1 (.value({1'b0, O0, O1, O2}), .dp(1'b0));

  // Notes on the sheet:
  //   输入引脚
  //   请勿修改引脚名称、电路名称及电路封装外观
  //   提示：使用独立逻辑门实现8-3优先级编码器，禁止直接使用编码器组件。
  //   输出引脚
endmodule
