// Logisim project ec3.circ as structural Verilog: 1 circuit, main circuit main
module main (
  input  in_1,
  input  in_2,
  output O0,
  output O1,
  output O2,
  output O3,
  output O4,
  output O5,
  output O6,
  output O7
);

  wire CLK, xor_1_out;

  SHRG4U shrg4u_1 (
    .CLK(CLK), .CLR_L(in_1), .Q3(O7), .Q2(O6), .D3(1'b0), .D2(1'b0), .D1(1'b0), .Q1(O5), .Q0(O4), .D0(1'b0),
    .LIN(O3), .S1(in_2), .S0(1'b1));  // open: RIN
  SHRG4U shrg4u_2 (
    .CLK(CLK), .CLR_L(in_1), .Q3(O3), .Q2(O2), .D3(1'b0), .D2(1'b0), .D1(1'b0), .Q1(O1), .Q0(O0), .D0(1'b1),
    .LIN(xor_1_out), .S1(in_2), .S0(1'b1));  // open: RIN
  ExactlyOne xor_1 (.out(xor_1_out), .in0(O0), .in1(O1), .in2(O3), .in3(O7));
  Hex_Digit_Display hex_digit_display_1 (.value({O0, O1, O2, O3}));  // open: dp
  Clock clock_1 (.out(CLK));
  Hex_Digit_Display hex_digit_display_2 (.value({O4, O5, O6, O7}));  // open: dp

  // Other names for the same wires on the sheet: CLR_L = in_1; S1 = in_2
endmodule
