// Logisim project ec1.circ as structural Verilog: 2 circuits, main circuit main
module main (
  input  in_1,
  input  [31:0] in_2,
  input  [31:0] in_3,
  input  [31:0] in_4,
  input  [31:0] in_5,
  output out_6,
  output out_7,
  output [31:0] out_8,
  output [31:0] out_9,
  output out_10
);

  wire C1, C2, C3, C4, G0, G1, G2, G3, P0, P1, P2, P3;

  lab4_2_main main_1 (.X(in_3[31:16]), .Y(in_5[31:16]), .C0(C3), .S(out_9[31:16]), .C16(out_10), .Pg(P3), .Gg(G3));
  lab4_2_main main_2 (.X(in_3[15:0]), .Y(in_5[15:0]), .C0(C2), .S(out_9[15:0]), .Pg(P2), .Gg(G2));  // open: C16
  CLU4 clu4_1 (
    .P0(P0), .P1(P1), .P2(P2), .P3(P3), .C1(C1), .C3(C3), .G0(G0), .G1(G1), .G2(G2), .G3(G3), .C2(C2),
    .C4(C4), .C0(in_1), .Pg(out_6), .Gg(out_7));
  lab4_2_main main_3 (.X(in_2[31:16]), .Y(in_4[31:16]), .C0(C1), .S(out_8[31:16]), .Pg(P1), .Gg(G1));  // open: C16
  lab4_2_main main_4 (.X(in_2[15:0]), .Y(in_4[15:0]), .C0(in_1), .S(out_8[15:0]), .Pg(P0), .Gg(G0));  // open: C16

  // Other names for the same wires on the sheet: C0 = in_1; C64 = out_10; Gg = out_7; Pg = out_6; X_high[31:0] = in_3;
  //   X_low[31:0] = in_2; Y_high[31:0] = in_5; Y_low[31:0] = in_4; Z_high[31:0] = out_9; Z_low[31:0] = out_8
endmodule

module sub (
  input  in_1,
  input  [31:0] in_2,
  input  [31:0] in_3,
  input  [31:0] in_4,
  input  [31:0] in_5,
  output out_6,
  output [31:0] out_7,
  output [31:0] out_8
);

  wire main_2_c16, main_3_c16, main_4_c16;

  lab4_2_main main_1 (
    .X(in_3[31:16]), .Y(in_5[31:16]), .C0(main_2_c16), .S(out_8[31:16]), .C16(out_6));  // open: Pg, Gg
  lab4_2_main main_2 (
    .X(in_3[15:0]), .Y(in_5[15:0]), .C0(main_3_c16), .S(out_8[15:0]), .C16(main_2_c16));  // open: Pg, Gg
  lab4_2_main main_3 (
    .X(in_2[31:16]), .Y(in_4[31:16]), .C0(main_4_c16), .S(out_7[31:16]), .C16(main_3_c16));  // open: Pg, Gg
  lab4_2_main main_4 (.X(in_2[15:0]), .Y(in_4[15:0]), .C0(in_1), .S(out_7[15:0]), .C16(main_4_c16));  // open: Pg, Gg

  // Other names for the same wires on the sheet: C0 = in_1; C64 = out_6; X_high[31:0] = in_3; X_low[31:0] = in_2;
  //   Y_high[31:0] = in_5; Y_low[31:0] = in_4; Z_high[31:0] = out_8; Z_low[31:0] = out_7
endmodule
