// Logisim project ec2.circ as structural Verilog: 1 circuit, main circuit MUL
module MUL (
  input  in_1,
  input  in_2,
  input  [31:0] X,
  input  [31:0] in_4,
  output [31:0] out_5,
  output [31:0] out_6
);

  wire Load, not_1_out, Stop;
  wire [5:0] counter_1_q;
  wire [31:0] adder32_1_s, multiplexer_1_out, multiplexer_2_out;
  wire [31:31] adder32_1_cout;

  not not_1 (not_1_out, Stop);
  Multiplexer #(.width(32), .enable("false")) multiplexer_1 (
    .in0({32{1'b0}}), .in1(X), .out(multiplexer_1_out), .sel(out_5[0]));
  Adder32 adder32_1 (
    .Cin(1'b0), .Cout(adder32_1_cout[31]), .X(multiplexer_1_out), .Y(out_6), .S(adder32_1_s));  // open: OF, CF, ZF, SF
  Register #(.width(32), .Select("low")) register_1 (
    .D({adder32_1_cout[31], adder32_1_s[31:1]}), .en(not_1_out), .Q(out_6), .clk(in_1), .clr(in_2));
  Register #(.width(32), .Select("low")) register_2 (
    .D(multiplexer_2_out), .en(not_1_out), .Q(out_5), .clk(in_1), .clr(in_2));
  Multiplexer #(.width(32), .enable("false")) multiplexer_2 (
    .in0({adder32_1_s[0], out_5[31:1]}), .in1(in_4), .out(multiplexer_2_out), .sel(Load));
  Counter #(.width(6), .max('h21), .ongoal("stay")) counter_1 (
    .Q(counter_1_q), .carry(Stop), .clk(in_1), .clr(in_2));  // open: load, D, count, preset, down
  Comparator #(.width(6), .mode("unsigned")) comparator_1 (.a(counter_1_q), .b({6{1'b0}}), .eq(Load));  // open: gt, lt

  // Other names for the same wires on the sheet: Z_low[31:0] = out_5; CLK = in_1; RST = in_2; Y[31:0] = in_4;
  //   Z_high[31:0] = out_6
endmodule
