// Logisim project ec3.circ as structural Verilog: 3 circuits, main circuit ALUctl-ec
module ALUctl_ec (
  input  [3:0] ALUctr,
  output SUBctr,
  output LRctr,
  output Mul_start,
  output SIGctr,
  output ALctr,
  output [2:0] OPctr,
  output Mul_H
);

  wire _3, _4, _5, _6, _7, _8, _9, _15;

  Decoder #(.select(4), .enable("false")) decoder_1 (
    .out1(LRctr), .out2(SIGctr), .out3(_3), .out4(_4), .out5(_5), .out6(_6), .out7(_7), .out8(_8), .out9(_9),
    .out10(Mul_H), .out13(ALctr), .out15(_15), .sel(ALUctr));  // open: out0, out11, out12, out14
  or or_1 (Mul_start, Mul_H, _9);
  or or_2 (SUBctr, SIGctr, _3, _8);
  or or_3 (OPctr[2], LRctr, SIGctr, _3, _9, _5, ALctr, _15, Mul_H);
  or or_4 (OPctr[1], SIGctr, _3, _9, _4, _6, Mul_H);
  or or_5 (OPctr[0], _4, _7, Mul_H, _15, _9);

  // Other names for the same wires on the sheet: _1 = LRctr; _2 = SIGctr; _10 = Mul_H; _13 = ALctr

  // Notes on the sheet:
  //   输入引脚
  //   ALU操作控制信号生成部件
  //   输出引脚
endmodule

module ALU_ec (
  input  [3:0] ALUctr,
  input  in_2,
  input  [31:0] A,
  input  [31:0] B,
  output Zero,
  output [31:0] S
);

  wire adder32_1_cout, adder32_1_of, adder32_1_sf, aluctl_ec_1_alctr, aluctl_ec_1_lrctr, aluctl_ec_1_mul_h,
       aluctl_ec_1_sigctr, aluctl_ec_1_subctr, d_ff_1_qn, Done, Mul_start, multiplexer_3_out, not_1_out,
       or_2_out, or_3_out, RST, xor_3_out, xor_4_out;
  wire [2:0] aluctl_ec_1_opctr;
  wire [3:0] register_1_q;
  wire [31:0] adder32_1_s, and_1_out, bit_extender_1_out, bit_extender_2_out, mul_1_out_5, mul_1_out_6,
       multiplexer_1_out, multiplexer_2_out, or_1_out, shifter32_1_dataout, xor_1_out, xor_2_out;

  assign xor_1_out = B ^ bit_extender_1_out;  // XOR_Gate xor_1, 32 bits wide
  assign bit_extender_1_out = {{31{aluctl_ec_1_subctr}}, aluctl_ec_1_subctr};  // Bit_Extender bit_extender_1
  assign and_1_out = A & B;  // AND_Gate and_1, 32 bits wide
  assign or_1_out = A | B;  // OR_Gate or_1, 32 bits wide
  assign xor_2_out = A ^ B;  // XOR_Gate xor_2, 32 bits wide
  Shifter32 shifter32_1 (
    .DataIn(A), .shamt(B[4:0]), .L_R(aluctl_ec_1_lrctr), .A_L(aluctl_ec_1_alctr),
    .DataOut(shifter32_1_dataout));
  MUL mul_1 (.in_1(in_2), .in_2(RST), .X(A), .in_4(B), .out_5(mul_1_out_5), .out_6(mul_1_out_6), .out_7(Done));
  not not_1 (not_1_out, aluctl_ec_1_mul_h);
  Adder32 adder32_1 (
    .OF(adder32_1_of), .SF(adder32_1_sf), .ZF(Zero), .X(A), .Y(xor_1_out), .Cin(aluctl_ec_1_subctr),
    .S(adder32_1_s), .Cout(adder32_1_cout));  // open: CF
  // Probe on multiplexer_1_out
  Multiplexer #(.width(32), .enable("false")) multiplexer_1 (
    .in0(mul_1_out_6), .in1(mul_1_out_5), .out(multiplexer_1_out), .sel(not_1_out));
  ALUctl_ec aluctl_ec_1 (
    .SUBctr(aluctl_ec_1_subctr), .LRctr(aluctl_ec_1_lrctr), .Mul_start(Mul_start),
    .SIGctr(aluctl_ec_1_sigctr), .ALctr(aluctl_ec_1_alctr), .OPctr(aluctl_ec_1_opctr),
    .Mul_H(aluctl_ec_1_mul_h), .ALUctr(register_1_q));
  xor xor_3 (xor_3_out, aluctl_ec_1_subctr, adder32_1_cout);
  xor xor_4 (xor_4_out, adder32_1_of, adder32_1_sf);
  Multiplexer #(.select(3), .width(32), .enable("false")) multiplexer_2 (
    .in0(adder32_1_s), .in1(and_1_out), .in2(or_1_out), .in3(xor_2_out), .in4(shifter32_1_dataout), .in5(B),
    .in6(bit_extender_2_out), .in7(multiplexer_1_out), .out(multiplexer_2_out), .sel(aluctl_ec_1_opctr));
  assign bit_extender_2_out = {{31{1'b0}}, multiplexer_3_out};  // Bit_Extender bit_extender_2
  // Probe on aluctl_ec_1_opctr
  Register #(.width(4), .Select("low")) register_1 (
    .D(ALUctr), .en(or_2_out), .Q(register_1_q), .clk(in_2));  // open: clr
  or or_2 (or_2_out, Done, ~Mul_start);  // OR_Gate
  Multiplexer #(.enable("false")) multiplexer_3 (
    .in0(xor_3_out), .in1(xor_4_out), .out(multiplexer_3_out), .sel(aluctl_ec_1_sigctr));
  or or_3 (or_3_out, Done, ~Mul_start);  // OR_Gate
  // Probe on A
  // Probe on B
  // Probe on S
  Register #(.width(32), .Select("low")) register_2 (
    .D(multiplexer_2_out), .en(or_3_out), .Q(S), .clk(in_2));  // open: clr
  D_Flip_Flop #(.Pre_Clr_Positions("LEGACY"), .NewFFLayout("false")) d_ff_1 (
    .clk(in_2), .D(Mul_start), .Qn(d_ff_1_qn));  // open: Q, preset, reset
  and and_2 (RST, d_ff_1_qn, Mul_start);

  // Other names for the same wires on the sheet: CLK = in_2; Result[31:0] = S

  // Notes on the sheet:
  //   A: pull=down
  //   B: pull=down
  //   ALUctr: pull=down
  //   输入引脚
  //   输出引脚
  //   操作数和结果
endmodule

module MUL (
  input  in_1,
  input  in_2,
  input  [31:0] X,
  input  [31:0] in_4,
  output [31:0] out_5,
  output [31:0] out_6,
  output out_7
);

  wire Load, not_1_out;
  wire [5:0] counter_1_q;
  wire [31:0] adder32_1_s, multiplexer_1_out, multiplexer_2_out;
  wire [31:31] adder32_1_cout;

  not not_1 (not_1_out, out_7);
  Multiplexer #(.width(32), .enable("false")) multiplexer_1 (
    .in0({32{1'b0}}), .in1(X), .out(multiplexer_1_out), .sel(out_5[0]));
  Adder32 adder32_1 (
    .X(multiplexer_1_out), .Y(out_6), .Cin(1'b0), .S(adder32_1_s), .Cout(adder32_1_cout[31]));  // open: CF, OF, SF, ZF
  Register #(.width(32), .Select("low")) register_1 (
    .D({adder32_1_cout[31], adder32_1_s[31:1]}), .en(not_1_out), .Q(out_6), .clk(in_1), .clr(in_2));
  Register #(.width(32), .Select("low")) register_2 (
    .D(multiplexer_2_out), .en(not_1_out), .Q(out_5), .clk(in_1), .clr(in_2));
  Multiplexer #(.width(32), .enable("false")) multiplexer_2 (
    .in0({adder32_1_s[0], out_5[31:1]}), .in1(in_4), .out(multiplexer_2_out), .sel(Load));
  Counter #(.width(6), .max('h21), .ongoal("stay")) counter_1 (
    .Q(counter_1_q), .carry(out_7), .clk(in_1), .clr(in_2));  // open: load, D, count, preset, down
  Comparator #(.width(6), .mode("unsigned")) comparator_1 (.a(counter_1_q), .b({6{1'b0}}), .eq(Load));  // open: gt, lt

  // Other names for the same wires on the sheet: Z_low[31:0] = out_5; CLK = in_1; RST = in_2; Done = out_7;
  //   Stop = out_7; Y[31:0] = in_4; Z_high[31:0] = out_6
endmodule
