// Logisim project lab4.2.circ as structural Verilog: 3 circuits, main circuit main
// 16-CLA
module main (
  input  C0,
  input  [15:0] X,
  input  [15:0] Y,
  output C16,
  output Pg,
  output Gg,
  output [15:0] S
);

  wire C1, C2, C3, C4, G0, G1, G2, G3, P0, P1, P2, P3;

  lab4_1_main main_1 (.X(X[15:12]), .F(S[15:12]), .Cout(C16), .Y(Y[15:12]), .Pg(P3), .Cin(C3), .Gg(G3));
  lab4_1_main main_2 (.X(X[11:8]), .F(S[11:8]), .Y(Y[11:8]), .Pg(P2), .Cin(C2), .Gg(G2));  // open: Cout
  CLU4 clu4_1 (
    .P0(P0), .P1(P1), .P2(P2), .P3(P3), .C1(C1), .C3(C3), .G0(G0), .G1(G1), .G2(G2), .G3(G3), .C2(C2),
    .C4(C4), .C0(C0), .Pg(Pg), .Gg(Gg));
  lab4_1_main main_3 (.X(X[7:4]), .F(S[7:4]), .Y(Y[7:4]), .Pg(P1), .Cin(C1), .Gg(G1));  // open: Cout
  lab4_1_main main_4 (.X(X[3:0]), .F(S[3:0]), .Y(Y[3:0]), .Pg(P0), .Cin(C0), .Gg(G0));  // open: Cout
  // Probe on X
  // Probe on Y
  // Probe on S

  // Notes on the sheet:
  //   Y: pull=down
  //   X: pull=down
  //   C0: pull=down
  //   输入引脚区
  //   请勿修改引脚名称、电路名称及电路封装外观
  //   提示：使用4位先行进位加法器和CLU子电路实现16位并行加法器
  //   功能说明:16位Adder  S=X+Y，C16为最高位进位位，C0为进位输入， Pg、Gg为成组进位生成传递函数
  //   输出引脚区
  //   +
  //   =
  //   无符号加法
endmodule

module ec1 (
  input  in_1,
  input  [31:0] in_2,
  input  [31:0] in_3,
  input  [31:0] in_4,
  input  [31:0] in_5,
  output out_6,
  output out_7,
  output [31:0] out_8,
  output [31:0] out_9,
  output out_10
);

  wire C1, C2, C3, C4, G0, G1, G2, G3, P0, P1, P2, P3;

  main main_1 (.X(in_3[31:16]), .Y(in_5[31:16]), .C0(C3), .S(out_9[31:16]), .C16(out_10), .Pg(P3), .Gg(G3));
  main main_2 (.X(in_3[15:0]), .Y(in_5[15:0]), .C0(C2), .S(out_9[15:0]), .Pg(P2), .Gg(G2));  // open: C16
  CLU4 clu4_1 (
    .P0(P0), .P1(P1), .P2(P2), .P3(P3), .C1(C1), .C3(C3), .G0(G0), .G1(G1), .G2(G2), .G3(G3), .C2(C2),
    .C4(C4), .C0(in_1), .Pg(out_6), .Gg(out_7));
  main main_3 (.X(in_2[31:16]), .Y(in_4[31:16]), .C0(C1), .S(out_8[31:16]), .Pg(P1), .Gg(G1));  // open: C16
  main main_4 (.X(in_2[15:0]), .Y(in_4[15:0]), .C0(in_1), .S(out_8[15:0]), .Pg(P0), .Gg(G0));  // open: C16

  // Other names for the same wires on the sheet: C0 = in_1; C64 = out_10; Gg = out_7; Pg = out_6; X_high[31:0] = in_3;
  //   X_low[31:0] = in_2; Y_high[31:0] = in_5; Y_low[31:0] = in_4; Z_high[31:0] = out_9; Z_low[31:0] = out_8
endmodule

module ec1_1 (
  input  in_1,
  input  [31:0] in_2,
  input  [31:0] in_3,
  input  [31:0] in_4,
  input  [31:0] in_5,
  input  [31:0] in_6,
  input  [31:0] in_7,
  output out_8
);

  wire main_2_c16, main_3_c16, main_4_c16;

  main main_1 (.X(in_3[31:16]), .Y(in_5[31:16]), .C0(main_2_c16), .S(in_7[31:16]), .C16(out_8));  // open: Pg, Gg
  main main_2 (.X(in_3[15:0]), .Y(in_5[15:0]), .C0(main_3_c16), .S(in_7[15:0]), .C16(main_2_c16));  // open: Pg, Gg
  main main_3 (.X(in_2[31:16]), .Y(in_4[31:16]), .C0(main_4_c16), .S(in_6[31:16]), .C16(main_3_c16));  // open: Pg, Gg
  main main_4 (.X(in_2[15:0]), .Y(in_4[15:0]), .C0(in_1), .S(in_6[15:0]), .C16(main_4_c16));  // open: Pg, Gg

  // Other names for the same wires on the sheet: C0 = in_1; C64 = out_8; X_high[31:0] = in_3; X_low[31:0] = in_2;
  //   Y_high[31:0] = in_5; Y_low[31:0] = in_4; Z_high[31:0] = in_7; Z_low[31:0] = in_6
endmodule
