// Logisim project lab4.3.circ as structural Verilog: 2 circuits, main circuit Adder32
// 加法器
module Adder32 (
  input  Cin,
  input  [31:0] X,
  input  [31:0] Y,
  output CF,
  output Cout,
  output OF,
  output SF,
  output [31:0] S,
  output ZF
);

  wire and_1_out, and_2_out, main_2_c16;

  lab4_2_main main_1 (.X(X[31:16]), .Y(Y[31:16]), .C0(main_2_c16), .S(S[31:16]), .C16(Cout));  // open: Pg, Gg
  lab4_2_main main_2 (.X(X[15:0]), .Y(Y[15:0]), .C0(Cin), .S(S[15:0]), .C16(main_2_c16));  // open: Pg, Gg
  and and_1 (and_1_out, ~X[31], ~Y[31], S[31]);  // AND_Gate
  and and_2 (and_2_out, X[31], Y[31], ~S[31]);  // AND_Gate
  // Probe on X
  // Probe on Y
  // Probe on S
  or or_1 (OF, and_1_out, and_2_out);
  xor xor_1 (CF, Cout, Cin);
  Comparator #(.width(32), .mode("unsigned")) comparator_1 (.a(S), .b({32{1'b0}}), .eq(ZF));  // open: gt, lt

  assign SF = S[31];

  // Notes on the sheet:
  //   Y: pull=down
  //   Cin: pull=down
  //   X: pull=down
  //   输入引脚区
  //   输出引脚区
  //   请勿修改引脚名称、电路名称及电路封装外观
  //   提示：使用16位并行加法器子电路实现32位快速加法器
  //   功能说明:32位Adder  S=X+Y，Cout为最高位进位位，Cin为进位输入， S为和，溢出OF、进位CF、零ZF、符号SF。
  //   +
  //   =
  //   无符号加法
endmodule

module ec2 (
  input  in_1,
  input  in_2,
  input  [31:0] X,
  input  [31:0] in_4,
  output [31:0] out_5,
  output [31:0] out_6,
  output out_7
);

  wire Load, not_1_out;
  wire [5:0] counter_1_q;
  wire [31:0] adder32_1_s, multiplexer_1_out, multiplexer_2_out;
  wire [31:31] adder32_1_cout;

  not not_1 (not_1_out, out_7);
  Multiplexer #(.width(32), .enable("false")) multiplexer_1 (
    .in0({32{1'b0}}), .in1(X), .out(multiplexer_1_out), .sel(out_5[0]));
  Adder32 adder32_1 (
    .Cin(1'b0), .Cout(adder32_1_cout[31]), .X(multiplexer_1_out), .Y(out_6), .S(adder32_1_s));  // open: OF, CF, ZF, SF
  Register #(.width(32), .Select("low")) register_1 (
    .D({adder32_1_cout[31], adder32_1_s[31:1]}), .en(not_1_out), .Q(out_6), .clk(in_1), .clr(in_2));
  Register #(.width(32), .Select("low")) register_2 (
    .D(multiplexer_2_out), .en(not_1_out), .Q(out_5), .clk(in_1), .clr(in_2));
  Multiplexer #(.width(32), .enable("false")) multiplexer_2 (
    .in0({adder32_1_s[0], out_5[31:1]}), .in1(in_4), .out(multiplexer_2_out), .sel(Load));
  Counter #(.width(6), .max('h21), .ongoal("stay")) counter_1 (
    .Q(counter_1_q), .carry(out_7), .clk(in_1), .clr(in_2));  // open: load, D, count, preset, down
  Comparator #(.width(6), .mode("unsigned")) comparator_1 (.a(counter_1_q), .b({6{1'b0}}), .eq(Load));  // open: gt, lt

  // Other names for the same wires on the sheet: Z_low[31:0] = out_5; CLK = in_1; RST = in_2; Done = out_7;
  //   Stop = out_7; Y[31:0] = in_4; Z_high[31:0] = out_6
endmodule
