// Logisim project ec2.circ as structural Verilog: 2 circuits, main circuit main
module main (
  input  in_1,
  input  in_2
);

  wire clk;
  wire [7:0] _1_1, _1_2, _1_3, _1_4, _1_5, _1_6, _1_7, _1_8, _1_9, _1_10, _1_11, _1_12, _1_13, _1_14, _1_15,
       _1_16, _2_1, _2_2, _2_3, _2_4, _2_5, _2_6, _2_7, _2_8, _2_9, _2_10, _2_11, _2_12, _2_13, _2_14, _2_15,
       _2_16, _3_1, _3_2, _3_3, _3_4, _3_5, _3_6, _3_7, _3_8, _3_9, _3_10, _3_11, _3_12, _3_13, _3_14, _3_15,
       _3_16;

  Clock clock_1 (.out(clk));
  read read_1 (.rst(in_1), .clk(clk), .in({7{1'b0}}), .in_4(in_2), .out_5(_3_1), .out_6(_2_1), .out_7(_1_1));
  read read_2 (.rst(in_1), .clk(clk), .in(7'b0000001), .in_4(in_2), .out_5(_3_2), .out_6(_2_2), .out_7(_1_2));
  read read_3 (.rst(in_1), .clk(clk), .in(7'b0001000), .in_4(in_2), .out_5(_3_9), .out_6(_2_9), .out_7(_1_9));
  read read_4 (.rst(in_1), .clk(clk), .in(7'b0001001), .in_4(in_2), .out_5(_3_10), .out_6(_2_10), .out_7(_1_10));
  read read_5 (.rst(in_1), .clk(clk), .in(7'b0000010), .in_4(in_2), .out_5(_3_3), .out_6(_2_3), .out_7(_1_3));
  read read_6 (.rst(in_1), .clk(clk), .in(7'b0000011), .in_4(in_2), .out_5(_3_4), .out_6(_2_4), .out_7(_1_4));
  read read_7 (.rst(in_1), .clk(clk), .in(7'b0001010), .in_4(in_2), .out_5(_3_11), .out_6(_2_11), .out_7(_1_11));
  read read_8 (.rst(in_1), .clk(clk), .in(7'b0001011), .in_4(in_2), .out_5(_3_12), .out_6(_2_12), .out_7(_1_12));
  DotMatrix #(.inputtype("row"), .matrixcols(8), .matrixrows(16)) dotmatrix_1 (
    .row0(_3_1), .row1(_3_2), .row2(_3_3), .row3(_3_4), .row4(_3_5), .row5(_3_6), .row6(_3_7), .row7(_3_8),
    .row8(_3_9), .row9(_3_10), .row10(_3_11), .row11(_3_12), .row12(_3_13), .row13(_3_14), .row14(_3_15),
    .row15(_3_16));
  read read_9 (.rst(in_1), .clk(clk), .in(7'b0000100), .in_4(in_2), .out_5(_3_5), .out_6(_2_5), .out_7(_1_5));
  read read_10 (.rst(in_1), .clk(clk), .in(7'b0000101), .in_4(in_2), .out_5(_3_6), .out_6(_2_6), .out_7(_1_6));
  read read_11 (.rst(in_1), .clk(clk), .in(7'b0001100), .in_4(in_2), .out_5(_3_13), .out_6(_2_13), .out_7(_1_13));
  read read_12 (.rst(in_1), .clk(clk), .in(7'b0001101), .in_4(in_2), .out_5(_3_14), .out_6(_2_14), .out_7(_1_14));
  DotMatrix #(.inputtype("row"), .matrixcols(8), .matrixrows(16)) dotmatrix_2 (
    .row0(_2_1), .row1(_2_2), .row2(_2_3), .row3(_2_4), .row4(_2_5), .row5(_2_6), .row6(_2_7), .row7(_2_8),
    .row8(_2_9), .row9(_2_10), .row10(_2_11), .row11(_2_12), .row12(_2_13), .row13(_2_14), .row14(_2_15),
    .row15(_2_16));
  read read_13 (.rst(in_1), .clk(clk), .in(7'b0000110), .in_4(in_2), .out_5(_3_7), .out_6(_2_7), .out_7(_1_7));
  read read_14 (.rst(in_1), .clk(clk), .in(7'b0000111), .in_4(in_2), .out_5(_3_8), .out_6(_2_8), .out_7(_1_8));
  read read_15 (.rst(in_1), .clk(clk), .in(7'b0001110), .in_4(in_2), .out_5(_3_15), .out_6(_2_15), .out_7(_1_15));
  read read_16 (.rst(in_1), .clk(clk), .in(7'b0001111), .in_4(in_2), .out_5(_3_16), .out_6(_2_16), .out_7(_1_16));
  DotMatrix #(.inputtype("row"), .matrixcols(8), .matrixrows(16)) dotmatrix_3 (
    .row0(_1_1), .row1(_1_2), .row2(_1_3), .row3(_1_4), .row4(_1_5), .row5(_1_6), .row6(_1_7), .row7(_1_8),
    .row8(_1_9), .row9(_1_10), .row10(_1_11), .row11(_1_12), .row12(_1_13), .row13(_1_14), .row14(_1_15),
    .row15(_1_16));

  // Other names for the same wires on the sheet: rst = in_1; sel = in_2
endmodule

module read (
  input  rst,
  input  clk,
  input  [6:0] in,
  input  in_4,
  output [7:0] out_5,
  output [7:0] out_6,
  output [7:0] out_7
);

  wire and_1_out, not_1_out;
  wire [2:0] counter_2_q, subtractor_1_out;
  wire [6:0] adder_1_out, adder_2_out, adder_3_out, adder_4_out, counter_1_q, counter_3_q;
  wire [7:0] rom_1_data, rom_2_data, rom_3_data, rom_4_data, shifter_1_out;
  wire [23:0] multiplexer_1_out;

  Counter #(.width(7), .max('h7f)) counter_1 (
    .Q(counter_1_q), .clk(clk), .clr(rst));  // open: load, D, count, carry, preset, down
  Adder #(.width(7)) adder_1 (.a({counter_1_q[5:3], 4'b0000}), .b(in), .out(adder_1_out));  // open: cin, cout
  Adder #(.width(7)) adder_2 (.a(adder_1_out), .b(7'b0010000), .out(adder_2_out));  // open: cin, cout
  Adder #(.width(7)) adder_3 (.a(adder_2_out), .b(7'b0010000), .out(adder_3_out));  // open: cin, cout
  Adder #(.width(7)) adder_4 (.a(adder_3_out), .b(7'b0010000), .out(adder_4_out));  // open: cin, cout
  ROM #(.addrWidth(7), .Select("high")) rom_1 (.addr(adder_1_out), .data(rom_1_data), .sel(in_4));
  ROM #(.addrWidth(7), .Select("high")) rom_2 (.addr(adder_2_out), .data(rom_2_data), .sel(in_4));
  ROM #(.addrWidth(7), .Select("high")) rom_3 (.addr(adder_3_out), .data(rom_3_data), .sel(in_4));
  ROM #(.addrWidth(7), .Select("high")) rom_4 (.addr(adder_4_out), .data(rom_4_data), .sel(in_4));
  Counter #(.width(3), .max('h0)) counter_2 (
    .Q(counter_2_q), .clk(clk), .clr(rst));  // open: load, D, count, carry, preset, down
  Subtractor #(.width(3)) subtractor_1 (.a(counter_2_q), .b(3'b001), .out(subtractor_1_out));  // open: bin, bout
  Counter #(.width(7), .max('h7f)) counter_3 (
    .Q(counter_3_q), .clk(clk), .clr(rst));  // open: load, D, count, carry, preset, down
  Shifter shifter_1 (.in(rom_4_data), .\dist (subtractor_1_out), .out(shifter_1_out));
  Multiplexer #(.width(24), .enable("false")) multiplexer_1 (
    .in0({rom_1_data, rom_2_data, rom_3_data}), .in1({out_5[6:0], out_6, out_7, shifter_1_out[7]}),
    .out(multiplexer_1_out), .sel(not_1_out));
  not not_1 (not_1_out, and_1_out);
  and and_1 (and_1_out, ~counter_3_q[2], ~counter_3_q[1], ~counter_3_q[0]);  // AND_Gate
  Register #(.width(24), .Select("low")) register_1 (
    .D(multiplexer_1_out), .Q({out_5, out_6, out_7}), .clk(clk), .clr(rst));  // open: en

  // Other names for the same wires on the sheet: out[23:0] = {out_5, out_6, out_7}; out1[7:0] = out_7;
  //   out2[7:0] = out_6; out3[7:0] = out_5; sel = in_4

  // Notes on the sheet:
  //   contents of rom_1 (hex, n*v repeats v):
  //   18*0 63 63 73 7b 7f 6f 67 63 63 63 6*0 f 6*6 66 66 3c 6*0 9*63 3e 6*0 1e 33 61 4*60 61 33 1e 6*0 3e
  //   63 63 30 1c 6 3 63 63 3e
  //   contents of rom_2 (hex, n*v repeats v):
  //   18*0 63 63 73 7b 7f 6f 67 63 63 63 6*0 f 6*6 66 66 3c 6*0 9*63 3e 6*0 1e 33 61 4*60 61 33 1e 6*0 3e
  //   63 63 30 1c 6 3 63 63 3e
  //   contents of rom_3 (hex, n*v repeats v):
  //   18*0 63 63 73 7b 7f 6f 67 63 63 63 6*0 f 6*6 66 66 3c 6*0 9*63 3e 6*0 1e 33 61 4*60 61 33 1e 6*0 3e
  //   63 63 30 1c 6 3 63 63 3e
  //   contents of rom_4 (hex, n*v repeats v):
  //   18*0 63 63 73 7b 7f 6f 67 63 63 63 6*0 f 6*6 66 66 3c 6*0 9*63 3e 6*0 1e 33 61 4*60 61 33 1e 6*0 3e
  //   63 63 30 1c 6 3 63 63 3e
endmodule
