// Logisim project ec1.circ as structural Verilog: 3 circuits, main circuit main
module main (
  input  RESET
);

  wire clock_1_out;
  wire [6:0] adder_1_out, adder_2_out, counter_1_q;
  wire [7:0] ascii_1_row1, ascii_1_row2, ascii_1_row3, ascii_1_row4, ascii_1_row5, ascii_1_row6,
       ascii_1_row7, ascii_1_row8, ascii_1_row9, ascii_1_row10, ascii_1_row11, ascii_1_row12, ascii_1_row13,
       ascii_1_row14, ascii_1_row15, ascii_1_row16, ascii_2_row1, ascii_2_row2, ascii_2_row3, ascii_2_row4,
       ascii_2_row5, ascii_2_row6, ascii_2_row7, ascii_2_row8, ascii_2_row9, ascii_2_row10, ascii_2_row11,
       ascii_2_row12, ascii_2_row13, ascii_2_row14, ascii_2_row15, ascii_2_row16, ascii_3_row1, ascii_3_row2,
       ascii_3_row3, ascii_3_row4, ascii_3_row5, ascii_3_row6, ascii_3_row7, ascii_3_row8, ascii_3_row9,
       ascii_3_row10, ascii_3_row11, ascii_3_row12, ascii_3_row13, ascii_3_row14, ascii_3_row15,
       ascii_3_row16;

  Clock clock_1 (.out(clock_1_out));
  Counter #(.width(7), .max('h7f)) counter_1 (
    .Q(counter_1_q), .clk(clock_1_out), .clr(RESET));  // open: load, D, count, carry, preset, down
  Adder #(.width(7)) adder_1 (.a(counter_1_q), .b(7'b0010000), .out(adder_1_out));  // open: cin, cout
  Adder #(.width(7)) adder_2 (.a(adder_1_out), .b(7'b0010000), .out(adder_2_out));  // open: cin, cout
  ascii ascii_1 (
    .row1(ascii_1_row1), .row2(ascii_1_row2), .row3(ascii_1_row3), .row4(ascii_1_row4), .row5(ascii_1_row5),
    .row6(ascii_1_row6), .row7(ascii_1_row7), .row8(ascii_1_row8), .row9(ascii_1_row9),
    .row10(ascii_1_row10), .row11(ascii_1_row11), .row12(ascii_1_row12), .row13(ascii_1_row13),
    .row14(ascii_1_row14), .row15(ascii_1_row15), .row16(ascii_1_row16), .ASCII_CODE(counter_1_q));  // open: CodeErr
  DotMatrix #(.inputtype("row"), .matrixcols(8), .matrixrows(16)) dotmatrix_1 (
    .row0(ascii_1_row1), .row1(ascii_1_row2), .row2(ascii_1_row3), .row3(ascii_1_row4), .row4(ascii_1_row5),
    .row5(ascii_1_row6), .row6(ascii_1_row7), .row7(ascii_1_row8), .row8(ascii_1_row9), .row9(ascii_1_row10),
    .row10(ascii_1_row11), .row11(ascii_1_row12), .row12(ascii_1_row13), .row13(ascii_1_row14),
    .row14(ascii_1_row15), .row15(ascii_1_row16));
  ascii ascii_2 (
    .row1(ascii_2_row1), .row2(ascii_2_row2), .row3(ascii_2_row3), .row4(ascii_2_row4), .row5(ascii_2_row5),
    .row6(ascii_2_row6), .row7(ascii_2_row7), .row8(ascii_2_row8), .row9(ascii_2_row9),
    .row10(ascii_2_row10), .row11(ascii_2_row11), .row12(ascii_2_row12), .row13(ascii_2_row13),
    .row14(ascii_2_row14), .row15(ascii_2_row15), .row16(ascii_2_row16), .ASCII_CODE(adder_1_out));  // open: CodeErr
  DotMatrix #(.inputtype("row"), .matrixcols(8), .matrixrows(16)) dotmatrix_2 (
    .row0(ascii_2_row1), .row1(ascii_2_row2), .row2(ascii_2_row3), .row3(ascii_2_row4), .row4(ascii_2_row5),
    .row5(ascii_2_row6), .row6(ascii_2_row7), .row7(ascii_2_row8), .row8(ascii_2_row9), .row9(ascii_2_row10),
    .row10(ascii_2_row11), .row11(ascii_2_row12), .row12(ascii_2_row13), .row13(ascii_2_row14),
    .row14(ascii_2_row15), .row15(ascii_2_row16));
  ascii ascii_3 (
    .row1(ascii_3_row1), .row2(ascii_3_row2), .row3(ascii_3_row3), .row4(ascii_3_row4), .row5(ascii_3_row5),
    .row6(ascii_3_row6), .row7(ascii_3_row7), .row8(ascii_3_row8), .row9(ascii_3_row9),
    .row10(ascii_3_row10), .row11(ascii_3_row11), .row12(ascii_3_row12), .row13(ascii_3_row13),
    .row14(ascii_3_row14), .row15(ascii_3_row15), .row16(ascii_3_row16), .ASCII_CODE(adder_2_out));  // open: CodeErr
  DotMatrix #(.inputtype("row"), .matrixcols(8), .matrixrows(16)) dotmatrix_3 (
    .row0(ascii_3_row1), .row1(ascii_3_row2), .row2(ascii_3_row3), .row3(ascii_3_row4), .row4(ascii_3_row5),
    .row5(ascii_3_row6), .row6(ascii_3_row7), .row7(ascii_3_row8), .row8(ascii_3_row9), .row9(ascii_3_row10),
    .row10(ascii_3_row11), .row11(ascii_3_row12), .row12(ascii_3_row13), .row13(ascii_3_row14),
    .row14(ascii_3_row15), .row15(ascii_3_row16));
endmodule

module read (
  input  [6:0] in,
  input  in_2,
  input  [6:0] Addr,
  output [7:0] out_4,
  output [6:0] Addr_2
);

  Adder #(.width(7)) adder_1 (.a(Addr), .b(in), .out(Addr_2));  // open: cin, cout
  ROM #(.addrWidth(7), .Select("high")) rom_1 (.addr(Addr_2), .data(out_4), .sel(in_2));

  // Other names for the same wires on the sheet: Addr_out[6:0] = Addr_2; Out[7:0] = out_4; sel = in_2

  // Notes on the sheet:
  //   contents of rom_1 (hex, n*v repeats v):
  //   18*0 63 63 73 7b 7f 6f 67 63 63 63 6*0 f 6*6 66 66 3c 6*0 9*63 3e 6*0 1e 33 61 4*60 61 33 1e 6*0 3e
  //   63 63 30 1c 6 3 63 63 3e
endmodule

module ascii (
  input  [6:0] ASCII_CODE,
  output [7:0] row1,
  output [7:0] row2,
  output [7:0] row3,
  output [7:0] row4,
  output [7:0] row5,
  output [7:0] row6,
  output [7:0] row7,
  output [7:0] row8,
  output [7:0] row9,
  output [7:0] row10,
  output [7:0] row11,
  output [7:0] row12,
  output [7:0] row13,
  output [7:0] row14,
  output [7:0] row15,
  output [7:0] row16,
  output CodeErr
);

  wire [6:0] read_1_addr_2, read_2_addr_2, read_3_addr_2, read_4_addr_2, read_5_addr_2, read_6_addr_2,
       read_7_addr_2, read_8_addr_2, read_9_addr_2, read_10_addr_2, read_11_addr_2, read_12_addr_2,
       read_13_addr_2, read_14_addr_2, read_15_addr_2;

  read read_1 (.in({7{1'b0}}), .in_2(1'b1), .Addr(ASCII_CODE), .out_4(row1), .Addr_2(read_1_addr_2));
  read read_2 (.in(7'b0000001), .in_2(1'b1), .Addr(read_3_addr_2), .out_4(row3), .Addr_2(read_2_addr_2));
  read read_3 (.in(7'b0000001), .in_2(1'b1), .Addr(read_1_addr_2), .out_4(row2), .Addr_2(read_3_addr_2));
  read read_4 (.in(7'b0000001), .in_2(1'b1), .Addr(read_2_addr_2), .out_4(row4), .Addr_2(read_4_addr_2));
  read read_5 (.in(7'b0000001), .in_2(1'b1), .Addr(read_4_addr_2), .out_4(row5), .Addr_2(read_5_addr_2));
  read read_6 (.in(7'b0000001), .in_2(1'b1), .Addr(read_5_addr_2), .out_4(row6), .Addr_2(read_6_addr_2));
  read read_7 (.in(7'b0000001), .in_2(1'b1), .Addr(read_6_addr_2), .out_4(row7), .Addr_2(read_7_addr_2));
  read read_8 (.in(7'b0000001), .in_2(1'b1), .Addr(read_7_addr_2), .out_4(row8), .Addr_2(read_8_addr_2));
  read read_9 (.in(7'b0000001), .in_2(1'b1), .Addr(read_8_addr_2), .out_4(row9), .Addr_2(read_9_addr_2));
  read read_10 (.in(7'b0000001), .in_2(1'b1), .Addr(read_11_addr_2), .out_4(row11), .Addr_2(read_10_addr_2));
  read read_11 (.in(7'b0000001), .in_2(1'b1), .Addr(read_9_addr_2), .out_4(row10), .Addr_2(read_11_addr_2));
  read read_12 (.in(7'b0000001), .in_2(1'b1), .Addr(read_10_addr_2), .out_4(row12), .Addr_2(read_12_addr_2));
  read read_13 (.in(7'b0000001), .in_2(1'b1), .Addr(read_14_addr_2), .out_4(row14), .Addr_2(read_13_addr_2));
  read read_14 (.in(7'b0000001), .in_2(1'b1), .Addr(read_12_addr_2), .out_4(row13), .Addr_2(read_14_addr_2));
  DotMatrix #(.inputtype("row"), .matrixcols(8), .matrixrows(16)) dotmatrix_1 (
    .row0(row1), .row1(row2), .row2(row3), .row3(row4), .row4(row5), .row5(row6), .row6(row7), .row7(row8),
    .row8(row9), .row9(row10), .row10(row11), .row11(row12), .row12(row13), .row13(row14), .row14(row15),
    .row15(row16));
  read read_15 (.in(7'b0000001), .in_2(1'b1), .Addr(read_13_addr_2), .out_4(row15), .Addr_2(read_15_addr_2));
  read read_16 (.in(7'b0000001), .in_2(1'b1), .Addr(read_15_addr_2), .out_4(row16));  // open: Addr_2

  // Other names for the same wires on the sheet: Code[6:0] = ASCII_CODE

  // Notes on the sheet:
  //   ASCII编码
  //   输入引脚
  //   请勿修改引脚名称、电路名称及电路封装外观
  //   提示：使用只读存储器ROM加载ASCII码点阵字库、ROM片选信号高电平有效
  //   输出引脚
endmodule
