// Logisim project lab5.1.circ as structural Verilog: 3 circuits, main circuit main
// ASCII-ZK
module main (
  input  [6:0] ASCII_CODE,
  output [7:0] row1,
  output [7:0] row2,
  output [7:0] row3,
  output [7:0] row4,
  output [7:0] row5,
  output [7:0] row6,
  output [7:0] row7,
  output [7:0] row8,
  output [7:0] row9,
  output [7:0] row10,
  output [7:0] row11,
  output [7:0] row12,
  output [7:0] row13,
  output [7:0] row14,
  output [7:0] row15,
  output [7:0] row16,
  output CodeErr
);

  wire not_1_out;
  wire [10:0] Addr, read_1_addr_2, read_2_addr_2, read_3_addr_2, read_4_addr_2, read_5_addr_2, read_6_addr_2,
       read_7_addr_2, read_8_addr_2, read_9_addr_2, read_10_addr_2, read_11_addr_2, read_12_addr_2,
       read_13_addr_2, read_14_addr_2, read_16_addr_2;

  addr_cal addr_cal_1 (.ASCII_CODE(ASCII_CODE), .CodeErr(CodeErr), .Addr(Addr));
  read read_1 (.in_2(not_1_out), .Addr(read_2_addr_2), .out_4(row2), .Addr_2(read_1_addr_2), .in(11'h1));
  read read_2 (.in_2(not_1_out), .Addr(Addr), .out_4(row1), .Addr_2(read_2_addr_2), .in({11{1'b0}}));
  not not_1 (not_1_out, CodeErr);
  read read_3 (.in_2(not_1_out), .Addr(read_1_addr_2), .out_4(row3), .Addr_2(read_3_addr_2), .in(11'h1));
  read read_4 (.in_2(not_1_out), .Addr(read_3_addr_2), .out_4(row4), .Addr_2(read_4_addr_2), .in(11'h1));
  read read_5 (.in_2(not_1_out), .Addr(read_4_addr_2), .out_4(row5), .Addr_2(read_5_addr_2), .in(11'h1));
  read read_6 (.in_2(not_1_out), .Addr(read_5_addr_2), .out_4(row6), .Addr_2(read_6_addr_2), .in(11'h1));
  read read_7 (.in_2(not_1_out), .Addr(read_8_addr_2), .out_4(row8), .Addr_2(read_7_addr_2), .in(11'h1));
  read read_8 (.in_2(not_1_out), .Addr(read_6_addr_2), .out_4(row7), .Addr_2(read_8_addr_2), .in(11'h1));
  read read_9 (.in_2(not_1_out), .Addr(read_7_addr_2), .out_4(row9), .Addr_2(read_9_addr_2), .in(11'h1));
  read read_10 (.in_2(not_1_out), .Addr(read_9_addr_2), .out_4(row10), .Addr_2(read_10_addr_2), .in(11'h1));
  read read_11 (.in_2(not_1_out), .Addr(read_10_addr_2), .out_4(row11), .Addr_2(read_11_addr_2), .in(11'h1));
  DotMatrix #(.inputtype("row"), .matrixcols(8), .matrixrows(16)) dotmatrix_1 (
    .row0(row1), .row1(row2), .row2(row3), .row3(row4), .row4(row5), .row5(row6), .row6(row7), .row7(row8),
    .row8(row9), .row9(row10), .row10(row11), .row11(row12), .row12(row13), .row13(row14), .row14(row15),
    .row15(row16));
  read read_12 (.in_2(not_1_out), .Addr(read_13_addr_2), .out_4(row13), .Addr_2(read_12_addr_2), .in(11'h1));
  read read_13 (.in_2(not_1_out), .Addr(read_11_addr_2), .out_4(row12), .Addr_2(read_13_addr_2), .in(11'h1));
  read read_14 (.in_2(not_1_out), .Addr(read_12_addr_2), .out_4(row14), .Addr_2(read_14_addr_2), .in(11'h1));
  read read_15 (.in_2(not_1_out), .Addr(read_16_addr_2), .out_4(row16), .in(11'h1));  // open: Addr_2
  read read_16 (.in_2(not_1_out), .Addr(read_14_addr_2), .out_4(row15), .Addr_2(read_16_addr_2), .in(11'h1));

  // Other names for the same wires on the sheet: Code[6:0] = ASCII_CODE

  // Notes on the sheet:
  //   ASCII编码
  //   输入引脚
  //   请勿修改引脚名称、电路名称及电路封装外观
  //   提示：使用只读存储器ROM加载ASCII码点阵字库、ROM片选信号高电平有效
  //   输出引脚
endmodule

module addr_cal (
  input  [6:0] ASCII_CODE,
  output CodeErr,
  output [10:0] Addr
);

  Subtractor #(.width(7)) subtractor_1 (.a(ASCII_CODE), .b(7'b0100000), .out(Addr[10:4]), .bout(CodeErr));  // open: bin

  assign Addr[3:0] = 4'b0000;

  // Other names for the same wires on the sheet: Code[6:0] = ASCII_CODE
endmodule

module read (
  input  [10:0] in,
  input  in_2,
  input  [10:0] Addr,
  output [7:0] out_4,
  output [10:0] Addr_2
);

  Adder #(.width(11)) adder_1 (.a(Addr), .b(in), .out(Addr_2));  // open: cin, cout
  ROM #(.addrWidth(11), .Select("high")) rom_1 (.addr(Addr_2), .data(out_4), .sel(in_2));

  // Other names for the same wires on the sheet: Addr_out[10:0] = Addr_2; Out[7:0] = out_4; sel = in_2

  // Notes on the sheet:
  //   contents of rom_1 (hex, n*v repeats v):
  //   18*0 18 3c 3c 3c 18 18 18 0 18 18 5*0 63 63 63 22 14*0 36 36 7f 36 36 36 7f 36 36 4*0 c c 3e 63 61
  //   60 3e 3 3 43 63 3e c c 7*0 61 63 6 c 18 33 63 7*0 1c 36 36 1c 3b 6e 66 66 3b 5*0 30 30 30 60 13*0 c
  //   18 18 4*30 18 18 c 6*0 18 c c 4*6 c c 18 8*0 42 66 3c ff 3c 66 42 9*0 18 18 18 ff 18 18 18 15*0 18
  //   18 18 30 9*0 ff 18*0 18 18 6*0 1 3 7 e 1c 38 70 e0 c0 80 6*0 3e 63 63 63 6b 6b 63 63 63 3e 6*0 c 1c
  //   3c 6*c 3f 6*0 3e 63 3 6 c 18 30 61 63 7f 6*0 3e 63 3 3 1e 3 3 3 63 3e 6*0 6 e 1e 36 66 66 7f 6 6 f
  //   6*0 7f 60 60 60 7e 3 3 63 73 3e 6*0 1c 30 60 60 7e 4*63 3e 6*0 7f 63 3 6 6 c c 18 18 18 6*0 3e 63 63
  //   63 3e 4*63 3e 6*0 3e 4*63 3f 3 3 6 3c 9*0 18 18 0 0 0 18 18 9*0 18 18 0 0 0 18 18 18 30 5*0 6 c 18
  //   30 60 30 18 c 6 10*0 7e 0 0 7e 9*0 60 30 18 c 6 c 18 30 60 6*0 3e 63 63 6 c c c 0 c c 6*0 3e 63 63
  //   6f 6b 6b 6e 60 60 3e 6*0 8 1c 36 63 63 63 7f 63 63 63 6*0 7e 33 33 33 3e 4*33 7e 6*0 1e 33 61 4*60
  //   61 33 1e 6*0 7c 36 6*33 36 7c 6*0 7f 33 31 34 3c 34 30 31 33 7f 6*0 7f 33 31 34 3c 34 30 30 30 78
  //   6*0 1e 33 61 60 60 6f 63 63 37 1d 6*0 4*63 7f 5*63 6*0 3c 8*18 3c 6*0 f 6*6 66 66 3c 6*0 73 33 36 36
  //   3c 36 36 33 33 73 6*0 78 6*30 31 33 7f 6*0 63 77 7f 6b 6*63 6*0 63 63 73 7b 7f 6f 67 63 63 63 6*0 1c
  //   36 6*63 36 1c 6*0 7e 33 33 33 3e 4*30 78 6*0 3e 6*63 6b 6f 3e 6 7 4*0 7e 33 33 33 3e 36 36 33 33 73
  //   6*0 3e 63 63 30 1c 6 3 63 63 3e 6*0 ff db 99 6*18 3c 6*0 9*63 3e 6*0 7*63 36 1c 8 6*0 5*63 6b 6b 7f
  //   36 36 6*0 c3 c3 66 3c 18 18 3c 66 c3 c3 6*0 c3 c3 c3 66 3c 4*18 3c 6*0 7f 63 43 6 c 18 30 61 63 7f
  //   6*0 3c 8*30 3c 6*0 80 c0 e0 70 38 1c e 7 3 1 6*0 3c 8*c 3c 4*0 8 1c 36 63 24*0 ff 0 0 0 18 18 c 18*0
  //   3c 46 6 3e 66 66 3b 6*0 70 30 30 3c 36 4*33 6e 9*0 3e 63 60 60 60 63 3e 6*0 e 6 6 1e 36 4*66 3b 9*0
  //   3e 63 63 7e 60 63 3e 6*0 1c 36 32 30 7c 4*30 78 9*0 3b 4*66 3e 6 66 3c 4*0 70 30 30 36 3b 4*33 73
  //   6*0 c c 0 1c 5*c 1e 6*0 6 6 0 e 5*6 66 66 3c 4*0 70 30 30 33 33 36 3c 36 33 73 6*0 1c 8*c 1e 9*0 6e
  //   7f 5*6b 9*0 6e 6*33 9*0 3e 5*63 3e 9*0 6e 4*33 3e 30 30 78 7*0 3b 4*66 3e 6 6 f 7*0 6e 3b 33 30 30
  //   30 78 9*0 3e 63 38 e 3 63 3e 6*0 8 18 18 7e 4*18 1b e 9*0 6*66 3b 9*0 63 63 36 36 1c 1c 8 9*0 63 63
  //   63 6b 6b 7f 36 9*0 63 36 1c 1c 1c 36 63 9*0 5*63 3f 3 6 3c 7*0 7f 66 c 18 30 63 7f 6*0 e 18 18 18 70
  //   4*18 e 6*0 5*18 0 5*18 5*0 70 18 18 18 e 4*18 70 6*0 3b 6e 13*0 70 d8 d8 70
endmodule
