// Logisim project lab5.2'.circ as structural Verilog: 3 circuits, main circuit DataRam
// DataRAM
module DataRam (
  input  CLK,
  input  CLR,
  input  WE,
  input  [2:0] MemOp,
  input  [17:0] Addr,
  input  [31:0] Din,
  output AlignErr,
  output [31:0] DataOut
);

  wire decode_1_out_4, decode_1_out_5, decode_1_out_6, decode_1_out_7;
  wire [7:0] _0_data, _1_data, _2_data, _3_data, io_1_out_9, io_1_out_10, io_1_out_11, io_1_out_12;

  decode decode_1 (
    .Addr(Addr), .MemOp(MemOp), .AlignErr(AlignErr), .out_4(decode_1_out_4), .out_5(decode_1_out_5),
    .out_6(decode_1_out_6), .out_7(decode_1_out_7));
  io io_1 (
    .Addr(Addr), .DataOut(DataOut), .Din(Din), .out_9(io_1_out_9), .in_5(_0_data), .out_10(io_1_out_10),
    .in_6(_1_data), .out_11(io_1_out_11), .in_7(_2_data), .out_12(io_1_out_12), .in_8(_3_data),
    .MemOp(MemOp), .AlignErr(AlignErr));
  RAM #(.addrWidth(16), .bus("separate"), .Select("high"), .simpleMode("false")) _0 (
    .addr(Addr[17:2]), .din(io_1_out_9), .data(_0_data), .str(WE), .sel(decode_1_out_4), .clk(CLK), .clr(CLR));  // open: ld
  // Probe on _0_data
  RAM #(.addrWidth(16), .bus("separate"), .Select("high"), .simpleMode("false")) _1 (
    .addr(Addr[17:2]), .din(io_1_out_10), .data(_1_data), .str(WE), .sel(decode_1_out_5), .clk(CLK), .clr(CLR));  // open: ld
  // Probe on _1_data
  RAM #(.addrWidth(16), .bus("separate"), .Select("high"), .simpleMode("false")) _2 (
    .addr(Addr[17:2]), .din(io_1_out_11), .data(_2_data), .str(WE), .sel(decode_1_out_6), .clk(CLK), .clr(CLR));  // open: ld
  // Probe on _2_data
  RAM #(.addrWidth(16), .bus("separate"), .Select("high"), .simpleMode("false")) _3 (
    .addr(Addr[17:2]), .din(io_1_out_12), .data(_3_data), .str(WE), .sel(decode_1_out_7), .clk(CLK), .clr(CLR));  // open: ld
  // Probe on _3_data

  // Other names for the same wires on the sheet: Dout[31:0] = DataOut

  // Notes on the sheet:
  //   输入引脚
  //   请勿修改引脚名称、电路名称及电路封装外观
  //   为了后续实验中的引用，不要修改MemOp的编码定义、引脚名称和在布局中的位置。
  //   32位数据存储器，按字节分4片存储，可按照字节、半字和字进行存储；读取字节或半字时，支持0扩展和符号位扩展。
  //   输出引脚
endmodule

module decode (
  input  [17:0] Addr,
  input  [2:0] MemOp,
  output AlignErr,
  output out_4,
  output out_5,
  output out_6,
  output out_7
);

  wire and_3_out, E_0, multiplexer_1_out, not_1_out, not_2_out;
  wire [3:0] _01, multiplexer_2_out;
  wire [3:1] _10;
  wire [3:3] _00;

  Decoder #(.select(2), .enable("false")) decoder_1 (.out0(_00[3]), .sel(Addr[1:0]));  // open: out1, out2, out3
  Decoder #(.select(2), .enable("false")) decoder_2 (
    .out0(_01[0]), .out1(_01[1]), .out2(_01[2]), .out3(_01[3]), .sel(Addr[1:0]));
  not not_1 (not_1_out, Addr[1]);
  not not_2 (not_2_out, Addr[0]);
  not not_3 (E_0, _00[3]);
  and and_1 (_10[1], not_1_out, not_2_out);
  and and_2 (_10[3], Addr[1], not_2_out);
  Multiplexer #(.select(2), .enable("false")) multiplexer_1 (
    .in0(E_0), .in1(1'b0), .in2(Addr[0]), .in3(1'b1), .out(multiplexer_1_out), .sel(MemOp[1:0]));
  Multiplexer #(.select(2), .width(4), .enable("false")) multiplexer_2 (
    .in0({4{_00[3]}}), .in1(_01), .in2({{2{_10[3]}}, {2{_10[1]}}}), .in3(4'b0000), .out(multiplexer_2_out),
    .sel(MemOp[1:0]));
  Multiplexer #(.enable("false")) multiplexer_3 (.in0(multiplexer_1_out), .in1(1'b1), .out(AlignErr), .sel(and_3_out));
  Multiplexer #(.width(4), .enable("false")) multiplexer_4 (
    .in0(multiplexer_2_out), .in1(4'b0000), .out({out_7, out_6, out_5, out_4}), .sel(and_3_out));
  and and_3 (and_3_out, ~MemOp[0], ~MemOp[1], MemOp[2]);  // AND_Gate

  // Other names for the same wires on the sheet: _00[2:0] = {3{_00[3]}}; _10 (some bits) = {_10[3], _10[1]};
  //   E_2 = Addr[0]; SEL[3:0] = {out_7, out_6, out_5, out_4}; SEL_0 = out_4; SEL_1 = out_5; SEL_2 = out_6;
  //   SEL_3 = out_7
endmodule

module io (
  input  [17:0] Addr,
  input  [31:0] Din,
  input  AlignErr,
  input  [2:0] MemOp,
  input  [7:0] in_5,
  input  [7:0] in_6,
  input  [7:0] in_7,
  input  [7:0] in_8,
  output [7:0] out_9,
  output [7:0] out_10,
  output [7:0] out_11,
  output [7:0] out_12,
  output [31:0] DataOut
);

  wire [31:0] aligned, multiplexer_1_out, Op1, Op2, Op5, Op6;

  assign Op1 = {{24{1'b0}}, aligned[7:0]};  // Bit_Extender bit_extender_1
  assign Op5 = {{24{aligned[7]}}, aligned[7:0]};  // Bit_Extender bit_extender_2
  assign Op2 = {{16{1'b0}}, aligned[15:0]};  // Bit_Extender bit_extender_3
  assign Op6 = {{16{aligned[15]}}, aligned[15:0]};  // Bit_Extender bit_extender_4
  Shifter #(.width(32)) shifter_1 (.in(Din), .\dist ({Addr[1:0], 3'b000}), .out({out_12, out_11, out_10, out_9}));
  Shifter #(.width(32), .shift("lr")) shifter_2 (
    .in({in_8, in_7, in_6, in_5}), .\dist ({Addr[1:0], 3'b000}), .out(aligned));
  Multiplexer #(.select(3), .width(32), .enable("false")) multiplexer_1 (
    .in0(aligned), .in1(Op1), .in2(Op2), .in5(Op5), .in6(Op6), .out(multiplexer_1_out), .sel(MemOp));  // open: in3, in4, in7
  Multiplexer #(.width(32), .enable("false")) multiplexer_2 (
    .in0(multiplexer_1_out), .in1({in_8, in_7, in_6, in_5}), .out(DataOut), .sel(AlignErr));

  // Other names for the same wires on the sheet: Op0[31:0] = aligned; Dout[31:0] = DataOut;
  //   in[31:0] = {out_12, out_11, out_10, out_9}; in0[7:0] = out_9; in1[7:0] = out_10; in2[7:0] = out_11;
  //   in3[7:0] = out_12; out[31:0] = {in_8, in_7, in_6, in_5}; out0[7:0] = in_5; out1[7:0] = in_6; out2[7:0] = in_7;
  //   out3[7:0] = in_8
endmodule
