// Logisim project lab5.3.circ as structural Verilog: 1 circuit, main circuit IFU
module IFU (
  input  [31:0] Initial_Address,
  input  [31:0] Imm,
  input  [31:0] BusA,
  input  CLK,
  input  Reset,
  input  NPCASrc,
  input  NPCBSrc,
  output [31:0] PC,
  output [31:0] IR
);


  // Other names for the same wires on the sheet: Init_Addr[31:0] = Initial_Address

  // Notes on the sheet:
  //   BusA: pull=down
  //   NPCBSrc: pull=down
  //   Imm: pull=down
  //   NPCASrc: pull=down
  //   请勿修改引脚名称、电路名称及电路封装外观
  //   指令存储器256KB，数据位为32位，地址位为16位。PC寄存器数据宽度32位，片选信号高电平有效
  //   输入信号
  //   输出信号
endmodule
