// Logisim project lab5.5.circ as structural Verilog: 17 circuits, main circuit main
module main (
  input  [2:0] ExtOp,
  input  [2:0] MemOp,
  input  RegWr,
  input  ALUASrc,
  input  MemWr,
  input  [1:0] ALUBSrc,
  input  [31:0] Initial_Address,
  input  [3:0] ALUctr,
  input  MemtoReg,
  input  [2:0] BandJ,
  input  clk,
  input  ReSet,
  output [31:0] PC,
  output [31:0] BusW,
  output [31:0] Din,
  output NPCASrc,
  output NPCBSrc
);

  wire alu_1_zero;
  wire [31:0] alu_1_s, idu_1_busa, idu_1_dataa, idu_1_datab, idu_1_imm, \指令存储器_data , \数据存储器_dataout ;

  IFU ifu_1 (
    .CLK(clk), .Reset(ReSet), .NxtASrc(NPCASrc), .NxtBSrc(NPCBSrc), .Initial_Address(Initial_Address),
    .Imm(idu_1_imm), .BusA(idu_1_busa), .PC(PC));
  ROM #(.addrWidth(16), .dataWidth(32), .Select("high"), .simpleMode("false")) \u_指令存储器  (
    .addr(PC[17:2]), .data(\指令存储器_data ), .sel(1'b1));
  IDU idu_1 (
    .ExtOp(ExtOp), .RegWr(RegWr), .Imm(idu_1_imm), .ALUASrc(ALUASrc), .ALUBSrc(ALUBSrc), .CLK(clk),
    .IR(\指令存储器_data ), .BusW(BusW), .PC(PC), .DataA(idu_1_dataa), .DataB(idu_1_datab), .BusA(idu_1_busa),
    .BusB(Din));  // open: OpCode, Funct3, Funct7
  // Probe on PC
  // Probe on BusW
  ALU alu_1 (.A(idu_1_dataa), .B(idu_1_datab), .ALUctr(ALUctr), .S(alu_1_s), .Zero(alu_1_zero));
  // Probe on Din
  DataRAM \u_数据存储器  (
    .Addr(alu_1_s[17:0]), .Din(Din), .CLK(clk), .CLR(ReSet), .WE(MemWr), .MemOp(MemOp),
    .DataOut(\数据存储器_dataout ));  // open: AlignErr
  BandJ bandj_1 (.Branch(BandJ), .NxtASrc(NPCASrc), .Zero(alu_1_zero), .NxtBSrc(NPCBSrc), .Result0(alu_1_s[0]));
  Multiplexer #(.width(32), .enable("false")) multiplexer_1 (
    .in0(alu_1_s), .in1(\数据存储器_dataout ), .out(BusW), .sel(MemtoReg));

  // Other names for the same wires on the sheet: Init_Addr[31:0] = Initial_Address

  // Notes on the sheet:
  //   NPCASrc: pull=down
  //   ALUASrc: pull=down
  //   ALUBSrc: pull=down
  //   BandJ: pull=down
  //   NPCBSrc: pull=down
  //   ALUctr: pull=down
  //   RegWr: pull=down
  //   ExtOp: pull=down
  //   输入信号
  //   contents of 指令存储器 (hex, n*v repeats v):
  //   8000ef ffdff06f 100013 deadc2b7 eef28293 c10337 fee30313 62be33 62aeb3 1000513 552023 652223 452f03
  //   550f83 654583 1f2f633 4102d693 1031713 fdde00e3 73
  //   请勿修改引脚名称、电路名称及电路封装外观
  //   为了后续实验中的引用，不要修改控制信号的编码定义、引脚名称和在布局中的位置。
  //   指令存储器和数据存储器数据位都是32位，指令存储器编址以字为单位，数据存储器编址以字节为单位。
  //   32位数据存储器，按字节分4片存储，可按照字节、半字和字进行存储；读取字节或半字时，支持0扩展和符号位扩展。
  //   输出信号
endmodule

module BandJ (
  input  [2:0] Branch,
  input  Zero,
  input  Result0,
  output NxtASrc,
  output NxtBSrc
);

  wire not_1_out, or_1_out;

  and and_1 (NxtASrc, ~Branch[0], Branch[1], ~Branch[2]);  // AND_Gate
  Multiplexer #(.select(3), .enable("false")) multiplexer_1 (
    .in0(1'b0), .in1(1'b1), .in2(1'b1), .in4(Zero), .in5(not_1_out), .in6(Result0), .in7(or_1_out),
    .out(NxtBSrc), .sel(Branch));  // open: in3
  not not_1 (not_1_out, Zero);
  or or_1 (or_1_out, ~Result0, Zero);  // OR_Gate

  // Notes on the sheet:
  //   Zero: pull=down
  //   Branch: pull=down
  //   输入信号
  //   请勿修改引脚名称、电路名称及电路封装外观
  //   不要修改控制信号的编码定义、引脚名称和在布局中的位置。
  //   输出信号
endmodule

module IFU (
  input  [31:0] Initial_Address,
  input  [31:0] Imm,
  input  [31:0] BusA,
  input  CLK,
  input  Reset,
  input  NxtASrc,
  input  NxtBSrc,
  output [31:0] PC
);

  wire [31:0] adder_1_out, multiplexer_1_out, multiplexer_2_out, multiplexer_3_out;

  Multiplexer #(.width(32), .enable("false")) multiplexer_1 (
    .in0(PC), .in1(BusA), .out(multiplexer_1_out), .sel(NxtASrc));
  Adder #(.width(32)) adder_1 (.a(multiplexer_1_out), .b(multiplexer_2_out), .out(adder_1_out));  // open: cin, cout
  Multiplexer #(.width(32), .enable("false")) multiplexer_2 (
    .in0(32'h4), .in1(Imm), .out(multiplexer_2_out), .sel(NxtBSrc));
  Multiplexer #(.width(32), .enable("false")) multiplexer_3 (
    .in0(adder_1_out), .in1(Initial_Address), .out(multiplexer_3_out), .sel(Reset));
  Register #(.width(32), .Select("low")) register_1 (.D(multiplexer_3_out), .en(1'b1), .Q(PC), .clk(CLK));  // open: clr

  // Other names for the same wires on the sheet: Init_Addr[31:0] = Initial_Address

  // Notes on the sheet:
  //   BusA: pull=down
  //   NxtASrc: pull=down
  //   Imm: pull=down
  //   NxtBSrc: pull=down
  //   请勿修改引脚名称、电路名称及电路封装外观
  //   指令存储器256KB，数据位为32位，地址位为16位。PC寄存器数据宽度32位，片选信号高电平有效
  //   输入信号
  //   输出信号
endmodule

module IDU (
  input  [31:0] IR,
  input  [31:0] BusW,
  input  [31:0] PC,
  input  [2:0] ExtOp,
  input  RegWr,
  input  ALUASrc,
  input  [1:0] ALUBSrc,
  input  CLK,
  output [31:0] DataA,
  output [31:0] DataB,
  output [31:0] BusA,
  output [31:0] BusB,
  output [6:0] OpCode,
  output [31:0] Imm,
  output [2:0] Funct3,
  output [6:0] Funct7
);

  \立即数扩展器  \u_立即数扩展器_1  (.Instr(IR), .Extop(ExtOp), .imm(Imm));
  RegFile regfile_1 (
    .R1_num(IR[24:20]), .R2_num(IR[19:15]), .Write_Reg_num(IR[11:7]), .Write_Enable(RegWr), .Clock(CLK),
    .Din(BusW), .Reg1Out(BusB), .Reg2Out(BusA));
  // Probe on DataA
  Multiplexer #(.select(2), .width(32), .enable("false")) multiplexer_1 (
    .in0(BusB), .in1(32'h4), .in2(Imm), .out(DataB), .sel(ALUBSrc));  // open: in3
  Multiplexer #(.width(32), .enable("false")) multiplexer_2 (.in0(BusA), .in1(PC), .out(DataA), .sel(ALUASrc));
  // Probe on DataB
  // Probe on Imm
  // Probe on BusA
  // Probe on BusB

  assign Funct3 = IR[14:12];
  assign Funct7 = IR[31:25];
  assign OpCode = IR[6:0];

  // Other names for the same wires on the sheet: op[6:0] = IR[6:0]

  // Notes on the sheet:
  //   BusW: pull=down
  //   ALUASrc: pull=down
  //   RegWr: pull=down
  //   ExtOp: pull=down
  //   ALUBSrc: pull=down
  //   PC: pull=down
  //   输入信号
  //   为了后续实验中的引用，不要修改ALUASrc、ALUBSrc和EXtOP编码定义。
  //   请勿修改引脚名称、电路名称及电路封装外观
  //   输出信号
  //   修改寄存器堆电路设计，0号寄存器始终为0。
endmodule

module RegFile (
  input  [4:0] R1_num,
  input  [4:0] R2_num,
  input  [4:0] Write_Reg_num,
  input  [31:0] Din,
  input  Write_Enable,
  input  Clock,
  output [31:0] Reg1Out,
  output [31:0] Reg2Out
);

  wire and_1_out, and_2_out, and_3_out, and_4_out, and_5_out, and_6_out, and_7_out, and_8_out, and_9_out,
       and_10_out, and_11_out, and_12_out, and_13_out, and_14_out, and_15_out, and_16_out, and_17_out,
       and_18_out, and_19_out, and_20_out, and_21_out, and_22_out, and_23_out, and_24_out, and_25_out,
       and_26_out, and_27_out, and_28_out, and_29_out, and_30_out, and_31_out, decoder_1_out1,
       decoder_1_out2, decoder_1_out3, decoder_1_out4, decoder_1_out5, decoder_1_out6, decoder_1_out7,
       decoder_1_out8, decoder_1_out9, decoder_1_out10, decoder_1_out11, decoder_1_out12, decoder_1_out13,
       decoder_1_out14, decoder_1_out15, decoder_1_out16, decoder_1_out17, decoder_1_out18, decoder_1_out19,
       decoder_1_out20, decoder_1_out21, decoder_1_out22, decoder_1_out23, decoder_1_out24, decoder_1_out25,
       decoder_1_out26, decoder_1_out27, decoder_1_out28, decoder_1_out29, decoder_1_out30, decoder_1_out31;
  wire [31:0] register_1_q, register_2_q, register_3_q, register_4_q, register_6_q, register_7_q,
       register_8_q, register_9_q, register_10_q, register_11_q, register_12_q, register_13_q, register_14_q,
       register_15_q, register_16_q, register_17_q, register_18_q, register_19_q, register_20_q,
       register_21_q, register_22_q, register_23_q, register_24_q, register_25_q, register_26_q,
       register_27_q, register_28_q, register_29_q, register_30_q, register_31_q, register_32_q;

  Decoder #(.select(5), .enable("false")) decoder_1 (
    .out1(decoder_1_out1), .out2(decoder_1_out2), .out3(decoder_1_out3), .out4(decoder_1_out4),
    .out5(decoder_1_out5), .out6(decoder_1_out6), .out7(decoder_1_out7), .out8(decoder_1_out8),
    .out9(decoder_1_out9), .out10(decoder_1_out10), .out11(decoder_1_out11), .out12(decoder_1_out12),
    .out13(decoder_1_out13), .out14(decoder_1_out14), .out15(decoder_1_out15), .out16(decoder_1_out16),
    .out17(decoder_1_out17), .out18(decoder_1_out18), .out19(decoder_1_out19), .out20(decoder_1_out20),
    .out21(decoder_1_out21), .out22(decoder_1_out22), .out23(decoder_1_out23), .out24(decoder_1_out24),
    .out25(decoder_1_out25), .out26(decoder_1_out26), .out27(decoder_1_out27), .out28(decoder_1_out28),
    .out29(decoder_1_out29), .out30(decoder_1_out30), .out31(decoder_1_out31), .sel(Write_Reg_num));  // open: out0
  and and_1 (and_1_out, Write_Enable, decoder_1_out1);
  and and_2 (and_2_out, Write_Enable, decoder_1_out2);
  and and_3 (and_3_out, Write_Enable, decoder_1_out3);
  and and_4 (and_4_out, Write_Enable, decoder_1_out4);
  and and_5 (and_5_out, Write_Enable, decoder_1_out5);
  and and_6 (and_6_out, Write_Enable, decoder_1_out6);
  and and_7 (and_7_out, Write_Enable, decoder_1_out7);
  and and_8 (and_8_out, Write_Enable, decoder_1_out8);
  and and_9 (and_9_out, Write_Enable, decoder_1_out9);
  and and_10 (and_10_out, Write_Enable, decoder_1_out10);
  and and_11 (and_11_out, Write_Enable, decoder_1_out11);
  and and_12 (and_12_out, Write_Enable, decoder_1_out12);
  and and_13 (and_13_out, Write_Enable, decoder_1_out13);
  and and_14 (and_14_out, Write_Enable, decoder_1_out14);
  and and_15 (and_15_out, Write_Enable, decoder_1_out15);
  and and_16 (and_16_out, Write_Enable, decoder_1_out16);
  and and_17 (and_17_out, Write_Enable, decoder_1_out17);
  and and_18 (and_18_out, Write_Enable, decoder_1_out18);
  and and_19 (and_19_out, Write_Enable, decoder_1_out19);
  and and_20 (and_20_out, Write_Enable, decoder_1_out20);
  and and_21 (and_21_out, Write_Enable, decoder_1_out21);
  and and_22 (and_22_out, Write_Enable, decoder_1_out22);
  and and_23 (and_23_out, Write_Enable, decoder_1_out23);
  and and_24 (and_24_out, Write_Enable, decoder_1_out24);
  and and_25 (and_25_out, Write_Enable, decoder_1_out25);
  and and_26 (and_26_out, Write_Enable, decoder_1_out26);
  and and_27 (and_27_out, Write_Enable, decoder_1_out27);
  and and_28 (and_28_out, Write_Enable, decoder_1_out28);
  and and_29 (and_29_out, Write_Enable, decoder_1_out29);
  and and_30 (and_30_out, Write_Enable, decoder_1_out30);
  and and_31 (and_31_out, Write_Enable, decoder_1_out31);
  Register #(.width(32), .Select("low")) register_1 (.D(Din), .en(1'b0), .Q(register_1_q), .clk(Clock), .clr(1'b1));
  Register #(.width(32), .Select("low")) register_2 (
    .D(Din), .en(and_1_out), .Q(register_2_q), .clk(Clock));  // open: clr
  Register #(.width(32), .Select("low")) register_3 (
    .D(Din), .en(and_2_out), .Q(register_3_q), .clk(Clock));  // open: clr
  Register #(.width(32), .Select("low")) register_4 (
    .D(Din), .en(and_3_out), .Q(register_4_q), .clk(Clock));  // open: clr
  Register #(.width(32), .Select("low")) register_5 (
    .D(Din), .en(and_4_out), .Q(register_4_q), .clk(Clock));  // open: clr
  Register #(.width(32), .Select("low")) register_6 (
    .D(Din), .en(and_5_out), .Q(register_6_q), .clk(Clock));  // open: clr
  Register #(.width(32), .Select("low")) register_7 (
    .D(Din), .en(and_6_out), .Q(register_7_q), .clk(Clock));  // open: clr
  Register #(.width(32), .Select("low")) register_8 (
    .D(Din), .en(and_7_out), .Q(register_8_q), .clk(Clock));  // open: clr
  Register #(.width(32), .Select("low")) register_9 (
    .D(Din), .en(and_8_out), .Q(register_9_q), .clk(Clock));  // open: clr
  Register #(.width(32), .Select("low")) register_10 (
    .D(Din), .en(and_9_out), .Q(register_10_q), .clk(Clock));  // open: clr
  Register #(.width(32), .Select("low")) register_11 (
    .D(Din), .en(and_10_out), .Q(register_11_q), .clk(Clock));  // open: clr
  Register #(.width(32), .Select("low")) register_12 (
    .D(Din), .en(and_11_out), .Q(register_12_q), .clk(Clock));  // open: clr
  Register #(.width(32), .Select("low")) register_13 (
    .D(Din), .en(and_12_out), .Q(register_13_q), .clk(Clock));  // open: clr
  Register #(.width(32), .Select("low")) register_14 (
    .D(Din), .en(and_13_out), .Q(register_14_q), .clk(Clock));  // open: clr
  Register #(.width(32), .Select("low")) register_15 (
    .D(Din), .en(and_14_out), .Q(register_15_q), .clk(Clock));  // open: clr
  Register #(.width(32), .Select("low")) register_16 (
    .D(Din), .en(and_15_out), .Q(register_16_q), .clk(Clock));  // open: clr
  Register #(.width(32), .Select("low")) register_17 (
    .D(Din), .en(and_16_out), .Q(register_17_q), .clk(Clock));  // open: clr
  Register #(.width(32), .Select("low")) register_18 (
    .D(Din), .en(and_17_out), .Q(register_18_q), .clk(Clock));  // open: clr
  Register #(.width(32), .Select("low")) register_19 (
    .D(Din), .en(and_18_out), .Q(register_19_q), .clk(Clock));  // open: clr
  Register #(.width(32), .Select("low")) register_20 (
    .D(Din), .en(and_19_out), .Q(register_20_q), .clk(Clock));  // open: clr
  Register #(.width(32), .Select("low")) register_21 (
    .D(Din), .en(and_20_out), .Q(register_21_q), .clk(Clock));  // open: clr
  Register #(.width(32), .Select("low")) register_22 (
    .D(Din), .en(and_21_out), .Q(register_22_q), .clk(Clock));  // open: clr
  Register #(.width(32), .Select("low")) register_23 (
    .D(Din), .en(and_22_out), .Q(register_23_q), .clk(Clock));  // open: clr
  Register #(.width(32), .Select("low")) register_24 (
    .D(Din), .en(and_23_out), .Q(register_24_q), .clk(Clock));  // open: clr
  Register #(.width(32), .Select("low")) register_25 (
    .D(Din), .en(and_24_out), .Q(register_25_q), .clk(Clock));  // open: clr
  Register #(.width(32), .Select("low")) register_26 (
    .D(Din), .en(and_25_out), .Q(register_26_q), .clk(Clock));  // open: clr
  Register #(.width(32), .Select("low")) register_27 (
    .D(Din), .en(and_26_out), .Q(register_27_q), .clk(Clock));  // open: clr
  Register #(.width(32), .Select("low")) register_28 (
    .D(Din), .en(and_27_out), .Q(register_28_q), .clk(Clock));  // open: clr
  Register #(.width(32), .Select("low")) register_29 (
    .D(Din), .en(and_28_out), .Q(register_29_q), .clk(Clock));  // open: clr
  Register #(.width(32), .Select("low")) register_30 (
    .D(Din), .en(and_29_out), .Q(register_30_q), .clk(Clock));  // open: clr
  Register #(.width(32), .Select("low")) register_31 (
    .D(Din), .en(and_30_out), .Q(register_31_q), .clk(Clock));  // open: clr
  Register #(.width(32), .Select("low")) register_32 (
    .D(Din), .en(and_31_out), .Q(register_32_q), .clk(Clock));  // open: clr
  Multiplexer #(.select(5), .width(32), .enable("false")) multiplexer_1 (
    .in0(register_1_q), .in1(register_2_q), .in2(register_3_q), .in3(register_4_q), .in4(register_4_q),
    .in5(register_6_q), .in6(register_7_q), .in7(register_8_q), .in8(register_9_q), .in9(register_10_q),
    .in10(register_11_q), .in11(register_12_q), .in12(register_13_q), .in13(register_14_q),
    .in14(register_15_q), .in15(register_16_q), .in16(register_17_q), .in17(register_18_q),
    .in18(register_19_q), .in19(register_20_q), .in20(register_21_q), .in21(register_22_q),
    .in22(register_23_q), .in23(register_24_q), .in24(register_25_q), .in25(register_26_q),
    .in26(register_27_q), .in27(register_28_q), .in28(register_29_q), .in29(register_30_q),
    .in30(register_31_q), .in31(register_32_q), .out(Reg1Out), .sel(R1_num));
  Multiplexer #(.select(5), .width(32), .enable("false")) multiplexer_2 (
    .in0(register_1_q), .in1(register_2_q), .in2(register_3_q), .in3(register_4_q), .in4(register_4_q),
    .in5(register_6_q), .in6(register_7_q), .in7(register_8_q), .in8(register_9_q), .in9(register_10_q),
    .in10(register_11_q), .in11(register_12_q), .in12(register_13_q), .in13(register_14_q),
    .in14(register_15_q), .in15(register_16_q), .in16(register_17_q), .in17(register_18_q),
    .in18(register_19_q), .in19(register_20_q), .in20(register_21_q), .in21(register_22_q),
    .in22(register_23_q), .in23(register_24_q), .in24(register_25_q), .in25(register_26_q),
    .in26(register_27_q), .in27(register_28_q), .in28(register_29_q), .in29(register_30_q),
    .in30(register_31_q), .in31(register_32_q), .out(Reg2Out), .sel(R2_num));

  // Other names for the same wires on the sheet: CLK = Clock; RA[4:0] = R1_num; RB[4:0] = R2_num; RDA[31:0] = Reg1Out;
  //   RDB[31:0] = Reg2Out; RW[4:0] = Write_Reg_num; WE = Write_Enable

  // Notes on the sheet:
  //   输入引脚
  //   请勿修改引脚名称、电路名称及电路封装外观
  //   提示：使用译码器、多路选择器和32位寄存器及逻辑门实现寄存器堆，禁止直接使用存储器组件。
  //   输出引脚
endmodule

module \立即数扩展器  (
  input  [31:0] Instr,
  input  [2:0] Extop,
  output [31:0] imm
);

  wire [11:0] bit_extender_4_out;
  wire [19:0] bit_extender_3_out;
  wire [26:0] bit_extender_2_out;
  wire [31:0] bit_extender_1_out;

  assign bit_extender_1_out = {{20{Instr[31]}}, Instr[31:20]};  // Bit_Extender bit_extender_1
  assign bit_extender_2_out = {{20{Instr[31]}}, Instr[31:25]};  // Bit_Extender bit_extender_2
  assign bit_extender_3_out = {{19{Instr[31]}}, Instr[31]};  // Bit_Extender bit_extender_3
  assign bit_extender_4_out = {{11{Instr[31]}}, Instr[31]};  // Bit_Extender bit_extender_4
  Multiplexer #(.select(3), .width(32), .enable("false")) multiplexer_1 (
    .in0(bit_extender_1_out), .in1({Instr[31:12], {12{1'b0}}}), .in2({bit_extender_2_out, Instr[11:7]}),
    .in3({bit_extender_3_out, Instr[7], Instr[30:25], Instr[11:8], 1'b0}),
    .in4({bit_extender_4_out, Instr[19:12], Instr[20], Instr[30:21], 1'b0}), .out(imm), .sel(Extop));  // open: in5, in6, in7

  // Notes on the sheet:
  //   Extop: pull=down
  //   Instr: pull=down
  //   输入引脚
  //   输出引脚
endmodule

module DataRAM (
  input  CLK,
  input  CLR,
  input  WE,
  input  [2:0] MemOp,
  input  [17:0] Addr,
  input  [31:0] Din,
  output AlignErr,
  output [31:0] DataOut
);

  wire decode_1_p1, decode_1_p4, decode_1_p5, decode_1_p6;
  wire [7:0] _0_data, _1_data, _2_data, _3_data, io_1_out_8, io_1_out_9, io_1_out_10, io_1_out_11;

  // decode decode_1: pin names not known; wires that end beside it: decode_1_p1, Addr, MemOp, decode_1_p4, decode_1_p5, decode_1_p6, AlignErr
  io io_1 (
    .MemOp(MemOp), .Addr(Addr), .DataOut(DataOut), .Din(Din), .out_8(io_1_out_8), .in_4(_0_data),
    .out_9(io_1_out_9), .in_5(_1_data), .out_10(io_1_out_10), .in_6(_2_data), .out_11(io_1_out_11),
    .in_7(_3_data));
  RAM #(.addrWidth(16), .bus("separate"), .Select("high"), .simpleMode("false")) _0 (
    .addr(Addr[17:2]), .din(io_1_out_8), .data(_0_data), .str(WE), .sel(decode_1_p1), .clk(CLK), .clr(CLR));  // open: ld
  // Probe on _0_data
  RAM #(.addrWidth(16), .bus("separate"), .Select("high"), .simpleMode("false")) _1 (
    .addr(Addr[17:2]), .din(io_1_out_9), .data(_1_data), .str(WE), .sel(decode_1_p4), .clk(CLK), .clr(CLR));  // open: ld
  // Probe on _1_data
  RAM #(.addrWidth(16), .bus("separate"), .Select("high"), .simpleMode("false")) _2 (
    .addr(Addr[17:2]), .din(io_1_out_10), .data(_2_data), .str(WE), .sel(decode_1_p5), .clk(CLK), .clr(CLR));  // open: ld
  // Probe on _2_data
  RAM #(.addrWidth(16), .bus("separate"), .Select("high"), .simpleMode("false")) _3 (
    .addr(Addr[17:2]), .din(io_1_out_11), .data(_3_data), .str(WE), .sel(decode_1_p6), .clk(CLK), .clr(CLR));  // open: ld
  // Probe on _3_data

  // Other names for the same wires on the sheet: Dout[31:0] = DataOut

  // Notes on the sheet:
  //   输入引脚
  //   请勿修改引脚名称、电路名称及电路封装外观
  //   为了后续实验中的引用，不要修改MemOp的编码定义、引脚名称和在布局中的位置。
  //   32位数据存储器，按字节分4片存储，可按照字节、半字和字进行存储；读取字节或半字时，支持0扩展和符号位扩展。
  //   输出引脚
endmodule

module ALU (
  input  [3:0] ALUctr,
  input  [31:0] A,
  input  [31:0] B,
  output Zero,
  output [31:0] S
);

  wire adder32_1_cout, adder32_1_of, adder32_1_sf, aluctrl_1_alctr, aluctrl_1_sftctr, aluctrl_1_sigctr,
       aluctrl_1_subctr, multiplexer_1_out, xor_3_out, xor_4_out;
  wire [2:0] aluctrl_1_opctr;
  wire [31:0] adder32_1_s, and_1_out, bit_extender_1_out, bit_extender_2_out, or_1_out, shifter32_1_dataout,
       xor_1_out, xor_2_out;

  assign xor_1_out = B ^ bit_extender_1_out;  // XOR_Gate xor_1, 32 bits wide
  assign bit_extender_1_out = {{31{aluctrl_1_subctr}}, aluctrl_1_subctr};  // Bit_Extender bit_extender_1
  assign and_1_out = A & B;  // AND_Gate and_1, 32 bits wide
  assign or_1_out = A | B;  // OR_Gate or_1, 32 bits wide
  Adder32 adder32_1 (
    .OF(adder32_1_of), .SF(adder32_1_sf), .ZF(Zero), .X(A), .Y(xor_1_out), .Cin(aluctrl_1_subctr),
    .S(adder32_1_s), .Cout(adder32_1_cout));  // open: CF
  assign xor_2_out = A ^ B;  // XOR_Gate xor_2, 32 bits wide
  Shifter32 shifter32_1 (
    .DataIn(A), .shamt(B[4:0]), .L_R(aluctrl_1_sftctr), .A_L(aluctrl_1_alctr), .DataOut(shifter32_1_dataout));
  assign bit_extender_2_out = {{31{1'b0}}, multiplexer_1_out};  // Bit_Extender bit_extender_2
  xor xor_3 (xor_3_out, aluctrl_1_subctr, adder32_1_cout);
  Multiplexer #(.enable("false")) multiplexer_1 (
    .in0(xor_3_out), .in1(xor_4_out), .out(multiplexer_1_out), .sel(aluctrl_1_sigctr));
  xor xor_4 (xor_4_out, adder32_1_of, adder32_1_sf);
  Multiplexer #(.select(3), .width(32), .enable("false")) multiplexer_2 (
    .in0(adder32_1_s), .in1(and_1_out), .in2(or_1_out), .in3(xor_2_out), .in4(shifter32_1_dataout), .in5(B),
    .in6(bit_extender_2_out), .out(S), .sel(aluctrl_1_opctr));  // open: in7
  ALUctrl aluctrl_1 (
    .SUBctr(aluctrl_1_subctr), .SFTctr(aluctrl_1_sftctr), .SIGctr(aluctrl_1_sigctr), .ALctr(aluctrl_1_alctr),
    .OPctr(aluctrl_1_opctr), .ALUctr(ALUctr));
  // Probe on A
  // Probe on B
  // Probe on S

  // Other names for the same wires on the sheet: Result[31:0] = S

  // Notes on the sheet:
  //   ALUctr: pull=down
  //   B: pull=down
  //   A: pull=down
  //   输入引脚
  //   请勿修改引脚名称、电路名称及电路封装外观
  //   提示：使用32位并行加法器子电路、桶形移位器、ALU控制子电路实现32位ALU
  //   功能说明:32位ALU，输入32位操作数A、B，4位控制信号ALUctr，输出32位结果Reseult和1位Zero标志位
  //   输出引脚
  //   操作数和结果
endmodule

module ALUctrl (
  input  [3:0] ALUctr,
  output SUBctr,
  output SFTctr,
  output SIGctr,
  output ALctr,
  output [2:0] OPctr
);

  wire _3, _4, _5, _6, _7, _8, _15;

  Decoder #(.select(4), .enable("false")) decoder_1 (
    .out1(SFTctr), .out2(SIGctr), .out3(_3), .out4(_4), .out5(_5), .out6(_6), .out7(_7), .out8(_8),
    .out13(ALctr), .out15(_15), .sel(ALUctr));  // open: out0, out9, out10, out11, out12, out14
  or or_1 (SUBctr, SIGctr, _3, _8);
  or or_2 (OPctr[2], SFTctr, SIGctr, _3, _5, ALctr, _15);
  or or_3 (OPctr[1], SIGctr, _3, _4, _6);
  or or_4 (OPctr[0], _4, _7, _15);

  // Other names for the same wires on the sheet: _2 = SIGctr; _13 = ALctr; _1 = SFTctr; LRctr = SFTctr

  // Notes on the sheet:
  //   输入引脚
  //   ALU操作控制信号生成部件
  //   输出引脚
endmodule

module Adder32 (
  input  Cin,
  input  [31:0] X,
  input  [31:0] Y,
  output CF,
  output Cout,
  output OF,
  output SF,
  output [31:0] S,
  output ZF
);

  wire adder16_2_c16, and_1_out, and_2_out;

  Adder16 adder16_1 (.X(X[31:16]), .Y(Y[31:16]), .C0(adder16_2_c16), .S(S[31:16]), .C16(Cout));  // open: Pg, Gg
  Adder16 adder16_2 (.X(X[15:0]), .Y(Y[15:0]), .C0(Cin), .S(S[15:0]), .C16(adder16_2_c16));  // open: Pg, Gg
  and and_1 (and_1_out, ~X[31], ~Y[31], S[31]);  // AND_Gate
  and and_2 (and_2_out, X[31], Y[31], ~S[31]);  // AND_Gate
  Comparator #(.width(32), .mode("unsigned")) comparator_1 (.a(S), .b({32{1'b0}}), .eq(ZF));  // open: gt, lt
  xor xor_1 (CF, Cout, Cin);
  or or_1 (OF, and_1_out, and_2_out);
  // Probe on X
  // Probe on Y
  // Probe on S

  assign SF = S[31];

  // Notes on the sheet:
  //   Y: pull=down
  //   Cin: pull=down
  //   X: pull=down
  //   输入引脚区
  //   输出引脚区
  //   请勿修改引脚名称、电路名称及电路封装外观
  //   提示：使用16位并行加法器子电路实现32位快速加法器
  //   功能说明:32位Adder  S=X+Y，Cout为最高位进位位，Cin为进位输入， S为和，溢出OF、进位CF、零ZF、符号SF。
  //   +
  //   =
  //   无符号加法
endmodule

// 移位器
module Shifter32 (
  input  [4:0] shamt,
  input  L_R,
  input  A_L,
  input  [31:0] DataIn,
  output [31:0] DataOut
);

  wire [0:0] multiplexer_1_out;
  wire [1:0] bit_extender_1_out, bit_extender_2_out, multiplexer_3_out, multiplexer_3_out_2,
       multiplexer_4_out;
  wire [3:0] bit_extender_3_out, bit_extender_4_out, multiplexer_6_out;
  wire [7:0] bit_extender_5_out, bit_extender_6_out, multiplexer_8_out;
  wire [15:0] bit_extender_7_out, bit_extender_8_out, multiplexer_9_out, multiplexer_9_out_2,
       multiplexer_10_out;
  wire [27:0] multiplexer_3_out_3;
  wire [31:0] multiplexer_5_out, multiplexer_7_out;
  wire [31:31] multiplexer_2_out;

  Multiplexer #(.enable("false")) multiplexer_1 (.in0(1'b0), .in1(DataIn[31]), .out(multiplexer_1_out[0]), .sel(A_L));
  Multiplexer #(.enable("false")) multiplexer_2 (.in0(1'b0), .in1(DataIn[31]), .out(multiplexer_2_out[31]), .sel(A_L));
  Multiplexer #(.select(2), .width(32), .enable("false")) multiplexer_3 (
    .in0(DataIn), .in1({multiplexer_2_out[31], DataIn[31:1]}), .in2(DataIn),
    .in3({DataIn[30:0], multiplexer_1_out[0]}),
    .out({multiplexer_3_out, multiplexer_3_out_3, multiplexer_3_out_2}), .sel({L_R, shamt[0]}));
  assign bit_extender_1_out = {{1{multiplexer_2_out[31]}}, multiplexer_2_out[31]};  // Bit_Extender bit_extender_1
  Multiplexer #(.width(2), .enable("false")) multiplexer_4 (
    .in0(bit_extender_2_out), .in1(multiplexer_3_out), .out(multiplexer_4_out), .sel(A_L));
  assign bit_extender_2_out = {{1{1'b0}}, 1'b0};  // Bit_Extender bit_extender_2
  assign bit_extender_3_out = {{2{bit_extender_1_out[1]}}, bit_extender_1_out};  // Bit_Extender bit_extender_3
  Multiplexer #(.select(2), .width(32), .enable("false")) multiplexer_5 (
    .in0({multiplexer_3_out, multiplexer_3_out_3, multiplexer_3_out_2}),
    .in1({bit_extender_1_out, multiplexer_3_out, multiplexer_3_out_3}),
    .in2({multiplexer_3_out, multiplexer_3_out_3, multiplexer_3_out_2}),
    .in3({multiplexer_3_out_3, multiplexer_3_out_2, multiplexer_4_out}), .out(multiplexer_5_out),
    .sel({L_R, shamt[1]}));
  Multiplexer #(.width(4), .enable("false")) multiplexer_6 (
    .in0(bit_extender_4_out), .in1(multiplexer_5_out[31:28]), .out(multiplexer_6_out), .sel(A_L));
  assign bit_extender_4_out = {{2{bit_extender_2_out[1]}}, bit_extender_2_out};  // Bit_Extender bit_extender_4
  Multiplexer #(.select(2), .width(32), .enable("false")) multiplexer_7 (
    .in0(multiplexer_5_out), .in1({bit_extender_3_out, multiplexer_5_out[31:4]}), .in2(multiplexer_5_out),
    .in3({multiplexer_5_out[27:0], multiplexer_6_out}), .out(multiplexer_7_out), .sel({L_R, shamt[2]}));
  assign bit_extender_5_out = {{4{bit_extender_3_out[3]}}, bit_extender_3_out};  // Bit_Extender bit_extender_5
  assign bit_extender_6_out = {{4{bit_extender_4_out[3]}}, bit_extender_4_out};  // Bit_Extender bit_extender_6
  Multiplexer #(.width(8), .enable("false")) multiplexer_8 (
    .in0(bit_extender_6_out), .in1(multiplexer_7_out[31:24]), .out(multiplexer_8_out), .sel(A_L));
  assign bit_extender_7_out = {{8{bit_extender_5_out[7]}}, bit_extender_5_out};  // Bit_Extender bit_extender_7
  Multiplexer #(.select(2), .width(32), .enable("false")) multiplexer_9 (
    .in0(multiplexer_7_out), .in1({bit_extender_5_out, multiplexer_7_out[31:8]}), .in2(multiplexer_7_out),
    .in3({multiplexer_7_out[23:0], multiplexer_8_out}), .out({multiplexer_9_out, multiplexer_9_out_2}),
    .sel({L_R, shamt[3]}));
  assign bit_extender_8_out = {{8{bit_extender_6_out[7]}}, bit_extender_6_out};  // Bit_Extender bit_extender_8
  Multiplexer #(.width(16), .enable("false")) multiplexer_10 (
    .in0(bit_extender_8_out), .in1(multiplexer_9_out), .out(multiplexer_10_out), .sel(A_L));
  Multiplexer #(.select(2), .width(32), .enable("false")) multiplexer_11 (
    .in0({multiplexer_9_out, multiplexer_9_out_2}), .in1({bit_extender_7_out, multiplexer_9_out}),
    .in2({multiplexer_9_out, multiplexer_9_out_2}), .in3({multiplexer_9_out_2, multiplexer_10_out}),
    .out(DataOut), .sel({L_R, shamt[4]}));

  // Other names for the same wires on the sheet: Din[31:0] = DataIn; Left_Right = L_R; Arth_Logic = A_L;
  //   Dout[31:0] = DataOut

  // Notes on the sheet:
  //   L/R,A/L: 00逻辑右移，01算术右移，10逻辑左移，11：循环左移
  //   输入引脚
  //   请勿修改引脚名称、电路名称及电路封装外观
  //   提示：使用多路选择器、逻辑门实现32位桶形移位器，禁止直接使用移位器组件。
  //   输出引脚
endmodule

module Adder16 (
  input  C0,
  input  [15:0] X,
  input  [15:0] Y,
  output C16,
  output Pg,
  output Gg,
  output [15:0] S
);

  wire C1, C2, C3, C4, G0, G1, G2, G3, P0, P1, P2, P3;

  CLA4 cla4_1 (.X(X[15:12]), .F(S[15:12]), .Cout(C16), .Y(Y[15:12]), .Pg(P3), .Cin(C3), .Gg(G3));
  CLA4 cla4_2 (.X(X[11:8]), .F(S[11:8]), .Y(Y[11:8]), .Pg(P2), .Cin(C2), .Gg(G2));  // open: Cout
  CLU4 clu4_1 (
    .P0(P0), .P1(P1), .P2(P2), .P3(P3), .C1(C1), .C3(C3), .G0(G0), .G1(G1), .G2(G2), .G3(G3), .C2(C2),
    .C4(C4), .C0(C0), .Pg(Pg), .Gg(Gg));
  CLA4 cla4_3 (.X(X[7:4]), .F(S[7:4]), .Y(Y[7:4]), .Pg(P1), .Cin(C1), .Gg(G1));  // open: Cout
  CLA4 cla4_4 (.X(X[3:0]), .F(S[3:0]), .Y(Y[3:0]), .Pg(P0), .Cin(C0), .Gg(G0));  // open: Cout
  // Probe on X
  // Probe on Y
  // Probe on S

  // Notes on the sheet:
  //   Y: pull=down
  //   X: pull=down
  //   C0: pull=down
  //   输入引脚区
  //   请勿修改引脚名称、电路名称及电路封装外观
  //   提示：使用4位先行进位加法器和CLU子电路实现16位并行加法器
  //   功能说明:16位Adder  S=X+Y，C16为最高位进位位，C0为进位输入， Pg、Gg为成组进位生成传递函数
  //   输出引脚区
  //   +
  //   =
  //   无符号加法
endmodule

module CLA4 (
  input  [3:0] X,
  input  [3:0] Y,
  input  Cin,
  output [3:0] F,
  output Cout,
  output Pg,
  output Gg
);

  wire C1, C2, C3, G0, G1, G2, G3, P0, P1, P2, P3;

  Hex_Digit_Display hex_digit_display_1 (.value(X));  // open: dp
  FA fa_1 (.A(X[3]), .F(F[3]), .B(Y[3]), .P(P3), .Cin(C3), .G(G3));
  Hex_Digit_Display hex_digit_display_2 (.value(Y));  // open: dp
  FA fa_2 (.A(X[2]), .F(F[2]), .B(Y[2]), .P(P2), .Cin(C2), .G(G2));
  Hex_Digit_Display hex_digit_display_3 (.value(F));  // open: dp
  CLU4 clu4_1 (
    .P0(P0), .P1(P1), .P2(P2), .P3(P3), .C1(C1), .C3(C3), .G0(G0), .G1(G1), .G2(G2), .G3(G3), .C2(C2),
    .C4(Cout), .C0(Cin), .Pg(Pg), .Gg(Gg));
  FA fa_3 (.A(X[0]), .F(F[0]), .B(Y[0]), .P(P0), .Cin(Cin), .G(G0));
  FA fa_4 (.A(X[1]), .F(F[1]), .B(Y[1]), .P(P1), .Cin(C1), .G(G1));

  // Other names for the same wires on the sheet: C4 = Cout; Z[3:0] = F

  // Notes on the sheet:
  //   +
  //   =
  //   输出
  //   输入
  //   请勿修改引脚名称、电路名称及电路封装外观
  //   提示：使用全加器和CLU子电路实现四位先行进位加法器CLA4
endmodule

module CLU4 (
  input  P0,
  input  P1,
  input  P2,
  input  P3,
  input  G0,
  input  G1,
  input  G2,
  input  G3,
  input  C0,
  output C1,
  output C3,
  output C2,
  output C4,
  output Pg,
  output Gg
);

  wire and_1_out, and_2_out, and_3_out, and_4_out, and_6_out, and_7_out, and_8_out, or_5_out, or_6_out;

  and and_1 (and_1_out, C0, P0);
  and and_2 (and_2_out, C1, P1);
  and and_3 (and_3_out, C2, P2);
  and and_4 (and_4_out, C3, P3);
  or or_1 (C1, and_1_out, G0);
  or or_2 (C2, and_2_out, G1);
  or or_3 (C3, and_3_out, G2);
  or or_4 (C4, and_4_out, G3);
  and and_5 (Pg, P0, P1, P2, P3);
  and and_6 (and_6_out, P1, G0);
  or or_5 (or_5_out, and_6_out, G1);
  and and_7 (and_7_out, or_5_out, P2);
  or or_6 (or_6_out, and_7_out, G2);
  and and_8 (and_8_out, or_6_out, P3);
  or or_7 (Gg, and_8_out, G3);

  // Notes on the sheet:
  //   输入引脚
  //   请勿修改引脚名称、电路名称及电路封装外观
  //   提示：使用逻辑门电路实现4位四位先行进位部件CLU，Pg、Gg为成组进位生成传递函数
  //   输出引脚
endmodule

module FA (
  input  A,
  input  B,
  input  Cin,
  output F,
  output P,
  output G
);

  xor xor_1 (F, Cin, B, A);
  or or_1 (P, B, A);
  and and_1 (G, B, A);

  // Notes on the sheet:
  //   输入引脚
  //   请勿修改引脚名称、电路名称及电路封装外观
  //   输出引脚
endmodule

module decode (
  input  [17:0] Addr,
  input  [2:0] MemOp,
  output AlignErr,
  output out_4,
  output out_5,
  output out_6,
  output out_7
);

  wire and_3_out, E_0, multiplexer_1_out, not_1_out, not_2_out;
  wire [3:0] _01, multiplexer_2_out;
  wire [3:1] _10;
  wire [3:3] _00;

  Decoder #(.select(2), .enable("false")) decoder_1 (.out0(_00[3]), .sel(Addr[1:0]));  // open: out1, out2, out3
  Decoder #(.select(2), .enable("false")) decoder_2 (
    .out0(_01[0]), .out1(_01[1]), .out2(_01[2]), .out3(_01[3]), .sel(Addr[1:0]));
  not not_1 (not_1_out, Addr[1]);
  not not_2 (not_2_out, Addr[0]);
  not not_3 (E_0, _00[3]);
  and and_1 (_10[1], not_1_out, not_2_out);
  and and_2 (_10[3], Addr[1], not_2_out);
  Multiplexer #(.select(2), .enable("false")) multiplexer_1 (
    .in0(E_0), .in1(1'b0), .in2(Addr[0]), .in3(1'b1), .out(multiplexer_1_out), .sel(MemOp[1:0]));
  Multiplexer #(.select(2), .width(4), .enable("false")) multiplexer_2 (
    .in0({4{_00[3]}}), .in1(_01), .in2({{2{_10[3]}}, {2{_10[1]}}}), .in3(4'b0000), .out(multiplexer_2_out),
    .sel(MemOp[1:0]));
  Multiplexer #(.enable("false")) multiplexer_3 (.in0(multiplexer_1_out), .in1(1'b1), .out(AlignErr), .sel(and_3_out));
  Multiplexer #(.width(4), .enable("false")) multiplexer_4 (
    .in0(multiplexer_2_out), .in1(4'b0000), .out({out_7, out_6, out_5, out_4}), .sel(and_3_out));
  and and_3 (and_3_out, ~MemOp[0], ~MemOp[1], MemOp[2]);  // AND_Gate

  // Other names for the same wires on the sheet: _00[2:0] = {3{_00[3]}}; _10 (some bits) = {_10[3], _10[1]};
  //   E_2 = Addr[0]; SEL[3:0] = {out_7, out_6, out_5, out_4}; SEL_0 = out_4; SEL_1 = out_5; SEL_2 = out_6;
  //   SEL_3 = out_7
endmodule

module io (
  input  [17:0] Addr,
  input  [31:0] Din,
  input  [2:0] MemOp,
  input  [7:0] in_4,
  input  [7:0] in_5,
  input  [7:0] in_6,
  input  [7:0] in_7,
  output [7:0] out_8,
  output [7:0] out_9,
  output [7:0] out_10,
  output [7:0] out_11,
  output [31:0] DataOut
);

  wire [7:0] Byte;
  wire [15:0] H_word;
  wire [31:0] Op1, Op2, Op5, Op6;

  Multiplexer #(.select(2), .width(8), .enable("false")) multiplexer_1 (
    .in0(in_4), .in1(in_5), .in2(in_6), .in3(in_7), .out(Byte), .sel(Addr[1:0]));
  assign Op1 = {{24{1'b0}}, Byte};  // Bit_Extender bit_extender_1
  assign Op5 = {{24{Byte[7]}}, Byte};  // Bit_Extender bit_extender_2
  assign Op2 = {{16{1'b0}}, H_word};  // Bit_Extender bit_extender_3
  Shifter #(.width(32)) shifter_1 (.in(Din), .\dist ({Addr[1:0], 3'b000}), .out({out_11, out_10, out_9, out_8}));
  Multiplexer #(.width(16), .enable("false")) multiplexer_2 (
    .in0({in_5, in_4}), .in1({in_7, in_6}), .out(H_word), .sel(Addr[1]));
  Multiplexer #(.select(3), .width(32), .enable("false")) multiplexer_3 (
    .in0({in_7, in_6, in_5, in_4}), .in1(Op1), .in2(Op2), .in5(Op5), .in6(Op6), .out(DataOut), .sel(MemOp));  // open: in3, in4, in7
  assign Op6 = {{16{H_word[15]}}, H_word};  // Bit_Extender bit_extender_4

  // Other names for the same wires on the sheet: Dout[31:0] = DataOut; in[31:0] = {out_11, out_10, out_9, out_8};
  //   in0[7:0] = out_8; in1[7:0] = out_9; in2[7:0] = out_10; in3[7:0] = out_11; Op0[31:0] = {in_7, in_6, in_5, in_4};
  //   out[31:0] = {in_7, in_6, in_5, in_4}; out0[7:0] = in_4; Word[31:0] = {in_7, in_6, in_5, in_4}; out1[7:0] = in_5;
  //   out2[7:0] = in_6; out3[7:0] = in_7
endmodule
