// Logisim project lab6.1.circ as structural Verilog: 1 circuit, main circuit 控制器
module \控制器  (
  input  [6:0] opcode,
  input  [2:0] funct3,
  input  [6:0] funct7,
  output [2:0] ExtOp,
  output RegWr,
  output [2:0] BandJ,
  output ALUASrc,
  output [1:0] ALUBSrc,
  output [3:0] ALUctr,
  output MemtoReg,
  output [2:0] MemOp,
  output MemWr
);

  wire actr1, actr2, and_2_out, auipc, Br, ext1, ext2, I_Ar, jal, jalr, lui, nor_3_out, nor_4_out, nor_5_out,
       or_6_out, or_10_out, R;
  wire [2:0] nor_2_out;
  wire [3:3] multiplexer_2_out;

  or or_1 (RegWr, lui, auipc, I_Ar, MemtoReg, R, jal, jalr);
  assign ExtOp = ext1 ? 3'b001 : 3'bz;  // Controlled_Buffer controlled_buffer_1
  or or_2 (ext1, lui, auipc);
  assign ALUctr = actr1 ? 4'b0000 : 4'bz;  // Controlled_Buffer controlled_buffer_2
  or or_3 (actr1, auipc, jal, jalr, MemtoReg, MemWr);
  Comparator #(.width(7), .mode("unsigned")) comparator_1 (.a(opcode), .b(7'b0110111), .eq(lui));  // open: gt, lt
  Comparator #(.width(7), .mode("unsigned")) comparator_2 (.a(opcode), .b(7'b1100011), .eq(Br));  // open: gt, lt
  Comparator #(.width(7), .mode("unsigned")) comparator_3 (.a(opcode), .b(7'b0010111), .eq(auipc));  // open: gt, lt
  Comparator #(.width(7), .mode("unsigned")) comparator_4 (.a(opcode), .b(7'b0000011), .eq(MemtoReg));  // open: gt, lt
  or or_4 (ALUASrc, auipc, jal, jalr);
  assign ExtOp = ext2 ? 3'b000 : 3'bz;  // Controlled_Buffer controlled_buffer_3
  or or_5 (ext2, I_Ar, MemtoReg, jalr);
  assign ALUctr = lui ? 4'b1111 : 4'bz;  // Controlled_Buffer controlled_buffer_4
  Comparator #(.width(7), .mode("unsigned")) comparator_5 (.a(opcode), .b(7'b0010011), .eq(I_Ar));  // open: gt, lt
  Comparator #(.width(7), .mode("unsigned")) comparator_6 (.a(opcode), .b(7'b0100011), .eq(MemWr));  // open: gt, lt
  Multiplexer #(.width(3), .enable("false")) multiplexer_1 (.in0(3'b000), .in1(nor_2_out), .out(MemOp), .sel(or_6_out));
  nor nor_1 (nor_2_out[2], funct3[2], funct3[1]);
  or or_6 (or_6_out, MemtoReg, MemWr);
  nor nor_2 (nor_2_out[0], funct3[0], funct3[1]);
  and and_1 (nor_2_out[1], funct3[0], ~funct3[1]);  // AND_Gate
  or or_7 (ALUBSrc[0], jal, jalr);
  assign BandJ = Br ? {Br, funct3[2], funct3[0]} : 3'bz;  // Controlled_Buffer controlled_buffer_5
  assign ExtOp = jal ? 3'b100 : 3'bz;  // Controlled_Buffer controlled_buffer_6
  assign ALUctr = Br ? {3'b001, funct3[1]} : 4'bz;  // Controlled_Buffer controlled_buffer_7
  Comparator #(.width(7), .mode("unsigned")) comparator_7 (.a(opcode), .b(7'b0110011), .eq(R));  // open: gt, lt
  assign BandJ = jalr ? 3'b010 : 3'bz;  // Controlled_Buffer controlled_buffer_8
  assign ExtOp = Br ? 3'b011 : 3'bz;  // Controlled_Buffer controlled_buffer_9
  Comparator #(.width(7), .mode("unsigned")) comparator_8 (.a(opcode), .b(7'b1101111), .eq(jal));  // open: gt, lt
  or or_8 (ALUBSrc[1], lui, auipc, I_Ar, MemtoReg, MemWr);
  assign BandJ = jal ? 3'b001 : 3'bz;  // Controlled_Buffer controlled_buffer_10
  assign ExtOp = MemWr ? 3'b010 : 3'bz;  // Controlled_Buffer controlled_buffer_11
  assign ALUctr = actr2 ? {multiplexer_2_out[3], funct3} : 4'bz;  // Controlled_Buffer controlled_buffer_12
  Multiplexer #(.enable("false")) multiplexer_2 (
    .in0(1'b0), .in1(funct7[5]), .out(multiplexer_2_out[3]), .sel(or_10_out));
  or or_9 (actr2, I_Ar, R);
  or or_10 (or_10_out, and_2_out, R);
  and and_2 (and_2_out, I_Ar, ~funct3[1], funct3[0]);  // AND_Gate
  Comparator #(.width(7), .mode("unsigned")) comparator_9 (.a(opcode), .b(7'b1100111), .eq(jalr));  // open: gt, lt
  nor nor_3 (nor_3_out, Br, jalr, jal);
  assign BandJ = nor_3_out ? 3'b000 : 3'bz;  // Controlled_Buffer controlled_buffer_13
  assign ExtOp = nor_4_out ? 3'b000 : 3'bz;  // Controlled_Buffer controlled_buffer_14
  nor nor_4 (nor_4_out, ext1, ext2, jal, Br, MemWr);
  assign ALUctr = nor_5_out ? 4'b0000 : 4'bz;  // Controlled_Buffer controlled_buffer_15
  nor nor_5 (nor_5_out, actr1, lui, Br, actr2);

  // Other names for the same wires on the sheet: I_l = MemtoReg; St = MemWr

  // Notes on the sheet:
  //   输入引脚
  //   请勿修改引脚名称、电路名称及电路封装外观
  //   提示：根据指令种类，把7位指令code用一位指令类型标志位来表示，再通过功能码来区分具体指令，生成控制信号。
  //   输出引脚
endmodule
