// Logisim project lab6.1.chk.circ as structural Verilog: 1 circuit, main circuit main
module main (
  output [5:0] Cnt,
  output [6:0] opcode,
  output [2:0] funct3,
  output [6:0] funct7,
  output [2:0] ExtOp,
  output RegWr,
  output [2:0] Branch,
  output MemWr,
  output ALUASrc,
  output [1:0] ALUBSrc,
  output [3:0] ALUctr,
  output [2:0] MemOp,
  output MemtoReg,
  output _passed,
  output halt
);

  wire CLK, comparator_2_eq, comparator_3_eq, comparator_4_eq, comparator_5_eq, comparator_6_eq,
       comparator_7_eq, comparator_8_eq, comparator_9_eq, comparator_10_eq, not_1_out, Running,
       \评测数据_2_data , \评测数据_3_data , \评测数据_6_data , \评测数据_8_data ;
  wire [1:0] \评测数据_4_data ;
  wire [2:0] \评测数据_7_data , \评测数据_9_data , \评测数据_data ;
  wire [3:0] \评测数据_5_data ;

  Clock clock_1 (.out(CLK));
  Counter #(.width(6), .max('h3f), .behavior("old")) counter_1 (
    .count(Running), .Q(Cnt), .clk(CLK));  // open: load, D, carry, clr, preset
  not not_1 (not_1_out, halt);
  not not_2 (Running, halt);
  Comparator #(.width(6), .mode("unsigned")) comparator_1 (.a(Cnt), .b(6'b100101), .eq(halt));  // open: gt, lt
  // AND_Gate and_1 has open pins: in0=not_1_out, in1=CLK, out=open
  ROM #(.addrWidth(6), .dataWidth(7), .Select("low")) u_Opcode (.addr(Cnt), .data(opcode));
  ROM #(.addrWidth(6), .dataWidth(3), .Select("low")) u_funct3 (.addr(Cnt), .data(funct3));
  ROM #(.addrWidth(6), .dataWidth(7), .Select("low")) u_Funct7 (.addr(Cnt), .data(funct7));
  ROM #(.addrWidth(6), .dataWidth(3), .Select("high")) \u_评测数据  (.addr(Cnt), .data(\评测数据_data ));
  ROM #(.addrWidth(6), .dataWidth(1), .Select("high")) \u_评测数据_2  (.addr(Cnt), .data(\评测数据_2_data ));
  RAM #(.addrWidth(6), .dataWidth(3), .bus("separate"), .simpleMode("false"), .Select("low")) ram_1 (
    .addr(Cnt), .din(ExtOp), .str(Running), .clk(CLK));  // open: data, sel, ld, clr
  Comparator #(.width(3), .mode("unsigned")) comparator_2 (
    .a(ExtOp), .b(\评测数据_data ), .eq(comparator_2_eq));  // open: gt, lt
  Comparator #(.width(1), .mode("unsigned")) comparator_3 (
    .a(RegWr), .b(\评测数据_2_data ), .eq(comparator_3_eq));  // open: gt, lt
  \控制器  \u_控制器_1  (
    .funct3(funct3), .opcode(opcode), .BandJ(Branch), .MemOp(MemOp), .ALUASrc(ALUASrc), .ALUBSrc(ALUBSrc),
    .ALUctr(ALUctr), .MemtoReg(MemtoReg), .RegWr(RegWr), .MemWr(MemWr), .ExtOp(ExtOp), .funct7(funct7));
  RAM #(.addrWidth(6), .dataWidth(1), .bus("separate"), .simpleMode("false"), .Select("low")) ram_2 (
    .addr(Cnt), .din(RegWr), .str(Running), .clk(CLK));  // open: data, sel, ld, clr
  ROM #(.addrWidth(6), .dataWidth(1), .Select("high")) \u_评测数据_3  (.addr(Cnt), .data(\评测数据_3_data ));
  ROM #(.addrWidth(6), .dataWidth(2), .Select("high")) \u_评测数据_4  (.addr(Cnt), .data(\评测数据_4_data ));
  RAM #(.addrWidth(6), .dataWidth(1), .bus("separate"), .simpleMode("false"), .Select("low")) ram_3 (
    .addr(Cnt), .din(ALUASrc), .str(Running), .clk(CLK));  // open: data, sel, ld, clr
  Comparator #(.width(1), .mode("unsigned")) comparator_4 (
    .a(ALUASrc), .b(\评测数据_3_data ), .eq(comparator_4_eq));  // open: gt, lt
  Comparator #(.width(2), .mode("unsigned")) comparator_5 (
    .a(ALUBSrc), .b(\评测数据_4_data ), .eq(comparator_5_eq));  // open: gt, lt
  RAM #(.addrWidth(6), .dataWidth(2), .bus("separate"), .simpleMode("false"), .Select("low")) ram_4 (
    .addr(Cnt), .din(ALUBSrc), .str(Running), .clk(CLK));  // open: data, sel, ld, clr
  ROM #(.addrWidth(6), .dataWidth(4), .Select("high")) \u_评测数据_5  (.addr(Cnt), .data(\评测数据_5_data ));
  ROM #(.addrWidth(6), .dataWidth(1), .Select("high")) \u_评测数据_6  (.addr(Cnt), .data(\评测数据_6_data ));
  and and_2 (_passed, comparator_2_eq, comparator_3_eq, comparator_4_eq, comparator_5_eq, comparator_6_eq, comparator_7_eq, comparator_8_eq, comparator_9_eq, comparator_10_eq);
  Comparator #(.width(4), .mode("unsigned")) comparator_6 (
    .a(ALUctr), .b(\评测数据_5_data ), .eq(comparator_6_eq));  // open: gt, lt
  Comparator #(.width(1), .mode("unsigned")) comparator_7 (
    .a(MemWr), .b(\评测数据_6_data ), .eq(comparator_7_eq));  // open: gt, lt
  RAM #(.addrWidth(6), .dataWidth(4), .bus("separate"), .simpleMode("false"), .Select("low")) ram_5 (
    .addr(Cnt), .din(ALUctr), .str(Running), .clk(CLK));  // open: data, sel, ld, clr
  ROM #(.addrWidth(6), .dataWidth(3), .Select("high")) \u_评测数据_7  (.addr(Cnt), .data(\评测数据_7_data ));
  ROM #(.addrWidth(6), .dataWidth(1), .Select("high")) \u_评测数据_8  (.addr(Cnt), .data(\评测数据_8_data ));
  RAM #(.addrWidth(6), .dataWidth(1), .bus("separate"), .simpleMode("false"), .Select("low")) ram_6 (
    .addr(Cnt), .din(MemWr), .str(Running), .clk(CLK));  // open: data, sel, ld, clr
  Comparator #(.width(3), .mode("unsigned")) comparator_8 (
    .a(Branch), .b(\评测数据_7_data ), .eq(comparator_8_eq));  // open: gt, lt
  Comparator #(.width(1), .mode("unsigned")) comparator_9 (
    .a(MemtoReg), .b(\评测数据_8_data ), .eq(comparator_9_eq));  // open: gt, lt
  RAM #(.addrWidth(6), .dataWidth(3), .bus("separate"), .simpleMode("false"), .Select("low")) ram_7 (
    .addr(Cnt), .din(Branch), .str(Running), .clk(CLK));  // open: data, sel, ld, clr
  ROM #(.addrWidth(6), .dataWidth(3), .Select("high")) \u_评测数据_9  (.addr(Cnt), .data(\评测数据_9_data ));
  RAM #(.addrWidth(6), .dataWidth(1), .bus("separate"), .simpleMode("false"), .Select("low")) ram_8 (
    .addr(Cnt), .din(MemtoReg), .str(Running), .clk(CLK));  // open: data, sel, ld, clr
  Comparator #(.width(3), .mode("unsigned")) comparator_10 (
    .a(MemOp), .b(\评测数据_9_data ), .eq(comparator_10_eq));  // open: gt, lt
  RAM #(.addrWidth(6), .dataWidth(3), .bus("separate"), .simpleMode("false"), .Select("low")) ram_9 (
    .addr(Cnt), .din(MemOp), .str(Running), .clk(CLK));  // open: data, sel, ld, clr
  RAM #(.addrWidth(6), .dataWidth(1), .bus("separate"), .simpleMode("false"), .Select("low")) ram_10 (
    .addr(Cnt), .din(_passed), .str(Running), .clk(CLK));  // open: data, sel, ld, clr

  // Other names for the same wires on the sheet: Equal = _passed; tunnel[5:0] = Cnt

  // Notes on the sheet:
  //   生成测试数据地址
  //   测试脉冲数
  //   输出数据
  //   contents of Opcode (hex, n*v repeats v):
  //   37 17 9*13 10*33 6f 67 6*63 5*3 23 23 23
  //   contents of funct3 (hex, n*v repeats v):
  //   0 0 0 2 3 4 6 7 1 5 5 0 0 1 2 3 4 5 5 6 7 0 0 0 1 4 5 6 7 0 1 2 4 5 0 1 2
  //   contents of Funct7 (hex, n*v repeats v):
  //   10*0 20 0 20 5*0 20
  //   contents of 评测数据 (hex, n*v repeats v):
  //   1 1 19*0 4 0 6*3 5*0 2 2 2
  //   contents of 评测数据_2 (hex, n*v repeats v):
  //   23*1 6*0 5*1
  //   生成测试电路输出结果
  //   contents of 评测数据_3 (hex, n*v repeats v):
  //   0 1 19*0 1 1
  //   contents of 评测数据_4 (hex, n*v repeats v):
  //   11*2 10*0 1 1 6*0 8*2
  //   输出引脚
  //   contents of 评测数据_5 (hex, n*v repeats v):
  //   f 0 0 2 3 4 6 7 1 5 d 0 8 1 2 3 4 5 d 6 7 0 0 4*2 3 3
  //   contents of 评测数据_6 (hex, n*v repeats v):
  //   34*0 1 1 1
  //   评测通过
  //   contents of 评测数据_7 (hex, n*v repeats v):
  //   21*0 1 2 4 5 6 7 6 7
  //   contents of 评测数据_8 (hex, n*v repeats v):
  //   29*0 5*1
  //   contents of 评测数据_9 (hex, n*v repeats v):
  //   29*0 5 6 0 1 2 5 6
endmodule
