// Logisim project lab6.2.chk.circ as structural Verilog: 1 circuit, main circuit main
module main (
  output [31:0] PC,
  output [31:0] IR,
  output [31:0] BusW,
  output [31:0] Din,
  output [15:0] Cycles,
  output _passed,
  output halt
);

  wire CLK, comparator_1_eq, comparator_2_eq, comparator_3_eq, comparator_4_eq, comparator_5_eq,
       comparator_6_eq, main_1_halt, not_1_out, Reset_data, Running;
  wire [6:0] tunnel;
  wire [15:0] main_1_cycles, \评测数据Cycles_data ;
  wire [31:0] Init_Addr_data, main_1_busw, main_1_din, main_1_ir, main_1_pc, \评测数据BusW_data , \评测数据Din_data ,
       \评测数据IR_data , \评测数据PC_data ;

  Clock clock_1 (.out(CLK));
  Counter #(.width(7), .max('h7f), .behavior("old")) counter_1 (
    .count(not_1_out), .Q(tunnel), .clk(CLK));  // open: load, D, carry, clr, preset
  not not_1 (not_1_out, halt);
  not not_2 (Running, comparator_1_eq);
  Comparator #(.width(7), .mode("unsigned")) comparator_1 (
    .a(tunnel), .b(7'b1011011), .eq(comparator_1_eq));  // open: gt, lt
  ROM #(.addrWidth(7), .dataWidth(32), .Select("low")) Init_Addr (.addr(tunnel), .data(Init_Addr_data));
  ROM #(.addrWidth(7), .dataWidth(1), .Select("low")) Reset (.addr(tunnel), .data(Reset_data));
  ROM #(.addrWidth(7), .dataWidth(7), .simpleMode("false"), .Select("low")) Funct7 (.addr(tunnel));  // open: data
  ROM #(.addrWidth(7), .dataWidth(32), .Select("high")) \u_评测数据PC  (.addr(tunnel), .data(\评测数据PC_data ));
  ROM #(.addrWidth(7), .dataWidth(32), .Select("high")) \u_评测数据IR  (.addr(tunnel), .data(\评测数据IR_data ));
  RAM #(.addrWidth(7), .dataWidth(32), .bus("separate"), .simpleMode("false"), .Select("low")) ram_1 (
    .addr(tunnel), .din(PC), .str(Running), .clk(CLK));  // open: data, sel, ld, clr
  Comparator #(.width(32), .mode("unsigned")) comparator_2 (
    .a(PC), .b(\评测数据PC_data ), .eq(comparator_2_eq));  // open: gt, lt
  Comparator #(.width(32), .mode("unsigned")) comparator_3 (
    .a(IR), .b(\评测数据IR_data ), .eq(comparator_3_eq));  // open: gt, lt
  lab6_2_main main_1 (
    .ReSet(Reset_data), .Init_Addr(Init_Addr_data), .PC(main_1_pc), .IR(main_1_ir), .BusW(main_1_busw),
    .Din(main_1_din), .Cycles(main_1_cycles), .Halt(main_1_halt), .clk(CLK));
  Register #(.width(1), .Select("low")) register_1 (.D(main_1_halt), .Q(halt), .clk(CLK));  // open: en, clr
  RAM #(.addrWidth(7), .dataWidth(32), .bus("separate"), .simpleMode("false"), .Select("low")) ram_2 (
    .addr(tunnel), .din(IR), .str(Running), .clk(CLK));  // open: data, sel, ld, clr
  ROM #(.addrWidth(7), .dataWidth(32), .Select("high")) \u_评测数据BusW  (.addr(tunnel), .data(\评测数据BusW_data ));
  ROM #(.addrWidth(7), .dataWidth(32), .Select("high")) \u_评测数据Din  (.addr(tunnel), .data(\评测数据Din_data ));
  Register #(.width(32), .trigger("falling"), .Select("low")) register_2 (
    .D(main_1_pc), .Q(PC), .clk(CLK));  // open: en, clr
  Register #(.width(32), .trigger("falling"), .Select("low")) register_3 (
    .D(main_1_ir), .Q(IR), .clk(CLK));  // open: en, clr
  Register #(.width(32), .trigger("falling"), .Select("low")) register_4 (
    .D(main_1_busw), .Q(BusW), .clk(CLK));  // open: en, clr
  Register #(.width(32), .trigger("falling"), .Select("low")) register_5 (
    .D(main_1_din), .Q(Din), .clk(CLK));  // open: en, clr
  Register #(.width(16), .trigger("falling"), .Select("low")) register_6 (
    .D(main_1_cycles), .Q(Cycles), .clk(CLK));  // open: en, clr
  RAM #(.addrWidth(7), .dataWidth(32), .bus("separate"), .simpleMode("false"), .Select("low")) ram_3 (
    .addr(tunnel), .din(BusW), .str(Running), .clk(CLK));  // open: data, sel, ld, clr
  Comparator #(.width(32), .mode("unsigned")) comparator_4 (
    .a(BusW), .b(\评测数据BusW_data ), .eq(comparator_4_eq));  // open: gt, lt
  Comparator #(.width(32), .mode("unsigned")) comparator_5 (
    .a(Din), .b(\评测数据Din_data ), .eq(comparator_5_eq));  // open: gt, lt
  RAM #(.addrWidth(7), .dataWidth(32), .bus("separate"), .simpleMode("false"), .Select("low")) ram_4 (
    .addr(tunnel), .din(Din), .str(Running), .clk(CLK));  // open: data, sel, ld, clr
  ROM #(.addrWidth(7), .dataWidth(16), .Select("high")) \u_评测数据Cycles  (.addr(tunnel), .data(\评测数据Cycles_data ));
  and and_1 (_passed, comparator_2_eq, comparator_3_eq, comparator_4_eq, comparator_5_eq, comparator_6_eq);
  Comparator #(.width(16), .mode("unsigned")) comparator_6 (
    .a(Cycles), .b(\评测数据Cycles_data ), .eq(comparator_6_eq));  // open: gt, lt
  RAM #(.addrWidth(7), .dataWidth(16), .bus("separate"), .simpleMode("false"), .Select("low")) ram_5 (
    .addr(tunnel), .din(Cycles), .str(Running), .clk(CLK));  // open: data, sel, ld, clr
  RAM #(.addrWidth(7), .dataWidth(1), .bus("separate"), .simpleMode("false"), .Select("low")) ram_6 (
    .addr(tunnel), .din(_passed), .str(Running), .clk(CLK));  // open: data, sel, ld, clr

  // Other names for the same wires on the sheet: Equal = _passed

  // Notes on the sheet:
  //   生成测试数据地址
  //   测试脉冲数
  //   输出数据
  //   contents of Reset (hex, n*v repeats v):
  //   1
  //   contents of Funct7 (hex, n*v repeats v):
  //   10*0 20 0 20 5*0 20
  //   contents of 评测数据PC (hex, n*v repeats v):
  //   0 0 4 8 c 10 14 18 1c 20 24 28 2c 30 34 38 3c 40 44 48 4c 50 54 58 5c 60 64 68 6c 70 74 78 7c 80 84
  //   88 8c 90 94 98 9c a0 a4 a8 ac b0 b4 b8 bc c0 c4 c8 cc d0 d4 d8 dc e0 e4 e8 ec f0 f4 f8 fc 100 104
  //   108 10c 110 114 118 11c 120 124 128 12c 130 134 138 144 148 14c 150 154 158 6*15c
  //   contents of 评测数据IR (hex, n*v repeats v):
  //   0 80000037 7ff00013 10c0b3 100193 14101863 800000b7 ffff8137 208733 7fff83b7 200193 12771c63 ff010b7
  //   ff008093 f0f0f137 f010113 20f7b3 f003b7 f038393 300193 10779a63 100093 3f00113 209833 800003b7
  //   400193 e781e63 800000b7 e00113 4020d8b3 fffe03b7 500193 e789263 800000b7 7ff0a913 100393 600193
  //   c791863 800000b7 7ff0b993 393 700193 a799e63 97 cc08093 ee00113 208023 ff00113 2080a3 c000113 208123
  //   113 2081a3 108a03 fff00393 800193 87a1263 da83 103b7 fee38393 900193 67a9863 1509223 209b03 c000393
  //   a00193 47b1e63 1609323 ab83 c103b7 fee38393 b00193 47b9263 40ac03 c103b7 fee38393 c00193 27c1863 c97
  //   10c8ce7 397 ff838393 d00193 7c9863 c10537 fee50513 6*73
  //   生成测试电路输出结果
  //   contents of 评测数据BusW (hex, n*v repeats v):
  //   0 80000000 7ff 0 1 0 80000000 ffff8000 7fff8000 7fff8000 2 0 ff01000 ff00ff0 f0f0f000 f0f0f0f0
  //   f000f0 f00000 f000f0 3 0 1 3f 80000000 80000000 4 0 80000000 e fffe0000 fffe0000 5 0 80000000 1 1 6
  //   0 80000000 0 0 7 0 a8 174 ee 174 ff 175 c0 176 0 177 ffffffff ffffffff 8 0 ffee 10000 ffee 9 0 178
  //   c0 c0 a 0 17a c0ffee c10000 c0ffee b 0 c0ffee c10000 c0ffee c 0 134 13c 144 13c d 0 c10000 c0ffee
  //   contents of 评测数据Din (hex, n*v repeats v):
  //   8*0 ffff8000 0 ffff8000 7fff8000 4*0 f0f0f0f0 f000f0 0 2 f000f0 ff00ff0 0 3f 0 0 80000000 0 7fff8000
  //   e 0 0 fffe0000 0 0 80000000 0 1 7*0 7fff8000 ee 0 ff 0 c0 0 0 174 0 0 ffffffff 0 0 7fff8000 0 ffee
  //   ffee 0 0 0 c0 c0 0 0 7fff8000 0 c0ffee 0 0 7fff8000 0 c0ffee 0 80000000 0 c0ffee 0 13c 0 7fff8000
  //   输出引脚
  //   contents of 评测数据Cycles (hex, n*v repeats v):
  //   0 0 1 2 3 4 5 6 7 8 9 a b c d e f 10 11 12 13 14 15 16 17 18 19 1a 1b 1c 1d 1e 1f 20 21 22 23 24 25
  //   26 27 28 29 2a 2b 2c 2d 2e 2f 30 31 32 33 34 35 36 37 38 39 3a 3b 3c 3d 3e 3f 40 41 42 43 44 45 46
  //   47 48 49 4a 4b 4c 4d 4e 4f 50 51 52 53 54 6*55
  //   评测通过
endmodule
