// Logisim project lab6.3.chk.circ as structural Verilog: 1 circuit, main circuit main
module main (
  output [31:0] PC,
  output [31:0] IR,
  output [31:0] BusW,
  output [31:0] Din,
  output [15:0] Cycles,
  output _passed,
  output halt
);

  wire CLK, comparator_1_eq, comparator_2_eq, comparator_3_eq, comparator_4_eq, comparator_5_eq,
       comparator_6_eq, main_1_halt, not_1_out, Reset_data, Running;
  wire [6:0] tunnel;
  wire [15:0] main_1_cycles, \评测数据Cycles_data ;
  wire [31:0] Init_Addr_data, main_1_busw, main_1_din, main_1_ir, main_1_pc, \评测数据BusW_data , \评测数据Din_data ,
       \评测数据IR_data , \评测数据PC_data ;

  Clock clock_1 (.out(CLK));
  Counter #(.width(7), .max('h7f), .behavior("old")) counter_1 (
    .count(not_1_out), .Q(tunnel), .clk(CLK));  // open: load, D, carry, clr, preset
  not not_1 (not_1_out, halt);
  not not_2 (Running, comparator_1_eq);
  Comparator #(.width(7), .mode("unsigned")) comparator_1 (
    .a(tunnel), .b(7'b1000110), .eq(comparator_1_eq));  // open: gt, lt
  ROM #(.addrWidth(7), .dataWidth(32), .Select("low")) Init_Addr (.addr(tunnel), .data(Init_Addr_data));
  ROM #(.addrWidth(7), .dataWidth(1), .Select("low")) Reset (.addr(tunnel), .data(Reset_data));
  ROM #(.addrWidth(7), .dataWidth(7), .simpleMode("false"), .Select("low")) Funct7 (.addr(tunnel));  // open: data
  ROM #(.addrWidth(7), .dataWidth(32), .Select("high")) \u_评测数据PC  (.addr(tunnel), .data(\评测数据PC_data ));
  ROM #(.addrWidth(7), .dataWidth(32), .Select("high")) \u_评测数据IR  (.addr(tunnel), .data(\评测数据IR_data ));
  RAM #(.addrWidth(7), .dataWidth(32), .bus("separate"), .simpleMode("false"), .Select("low")) ram_1 (
    .addr(tunnel), .din(PC), .str(Running), .clk(CLK));  // open: data, sel, ld, clr
  Comparator #(.width(32), .mode("unsigned")) comparator_2 (
    .a(PC), .b(\评测数据PC_data ), .eq(comparator_2_eq));  // open: gt, lt
  Comparator #(.width(32), .mode("unsigned")) comparator_3 (
    .a(IR), .b(\评测数据IR_data ), .eq(comparator_3_eq));  // open: gt, lt
  lab6_3_main main_1 (
    .ReSet(Reset_data), .Init_Addr(Init_Addr_data), .PC(main_1_pc), .IR(main_1_ir), .BusW(main_1_busw),
    .Din(main_1_din), .Cycles(main_1_cycles), .Halt(main_1_halt), .clk(CLK));
  Register #(.width(1), .Select("low")) register_1 (.D(main_1_halt), .Q(halt), .clk(CLK));  // open: en, clr
  RAM #(.addrWidth(7), .dataWidth(32), .bus("separate"), .simpleMode("false"), .Select("low")) ram_2 (
    .addr(tunnel), .din(IR), .str(Running), .clk(CLK));  // open: data, sel, ld, clr
  ROM #(.addrWidth(7), .dataWidth(32), .Select("high")) \u_评测数据BusW  (.addr(tunnel), .data(\评测数据BusW_data ));
  ROM #(.addrWidth(7), .dataWidth(32), .Select("high")) \u_评测数据Din  (.addr(tunnel), .data(\评测数据Din_data ));
  Register #(.width(32), .Select("low")) register_2 (.D(main_1_pc), .Q(PC), .clk(CLK));  // open: en, clr
  Register #(.width(32), .Select("low")) register_3 (.D(main_1_ir), .Q(IR), .clk(CLK));  // open: en, clr
  Register #(.width(32), .Select("low")) register_4 (.D(main_1_busw), .Q(BusW), .clk(CLK));  // open: en, clr
  Register #(.width(32), .Select("low")) register_5 (.D(main_1_din), .Q(Din), .clk(CLK));  // open: en, clr
  Register #(.width(16), .Select("low")) register_6 (.D(main_1_cycles), .Q(Cycles), .clk(CLK));  // open: en, clr
  RAM #(.addrWidth(7), .dataWidth(32), .bus("separate"), .simpleMode("false"), .Select("low")) ram_3 (
    .addr(tunnel), .din(BusW), .str(Running), .clk(CLK));  // open: data, sel, ld, clr
  Comparator #(.width(32), .mode("unsigned")) comparator_4 (
    .a(BusW), .b(\评测数据BusW_data ), .eq(comparator_4_eq));  // open: gt, lt
  Comparator #(.width(32), .mode("unsigned")) comparator_5 (
    .a(Din), .b(\评测数据Din_data ), .eq(comparator_5_eq));  // open: gt, lt
  RAM #(.addrWidth(7), .dataWidth(32), .bus("separate"), .simpleMode("false"), .Select("low")) ram_4 (
    .addr(tunnel), .din(Din), .str(Running), .clk(CLK));  // open: data, sel, ld, clr
  ROM #(.addrWidth(7), .dataWidth(16), .Select("high")) \u_评测数据Cycles  (.addr(tunnel), .data(\评测数据Cycles_data ));
  and and_1 (_passed, comparator_2_eq, comparator_3_eq, comparator_4_eq, comparator_5_eq, comparator_6_eq);
  Comparator #(.width(16), .mode("unsigned")) comparator_6 (
    .a(Cycles), .b(\评测数据Cycles_data ), .eq(comparator_6_eq));  // open: gt, lt
  RAM #(.addrWidth(7), .dataWidth(16), .bus("separate"), .simpleMode("false"), .Select("low")) ram_5 (
    .addr(tunnel), .din(Cycles), .str(Running), .clk(CLK));  // open: data, sel, ld, clr
  RAM #(.addrWidth(7), .dataWidth(1), .bus("separate"), .simpleMode("false"), .Select("low")) ram_6 (
    .addr(tunnel), .din(_passed), .str(Running), .clk(CLK));  // open: data, sel, ld, clr

  // Other names for the same wires on the sheet: Equal = _passed

  // Notes on the sheet:
  //   生成测试数据地址
  //   测试脉冲数
  //   输出数据
  //   contents of Funct7 (hex, n*v repeats v):
  //   10*0 20 0 20 5*0 20
  //   contents of 评测数据PC (hex, n*v repeats v):
  //   0 0 4 8 c 10 14 18 1c 10 14 18 1c 10 14 18 1c 10 14 18 1c 10 14 18 1c 10 14 18 1c 10 14 18 1c 10 14
  //   18 1c 10 14 18 1c 10 14 18 1c 10 14 18 1c 10 14 18 1c 10 14 18 1c 10 14 18 1c 10 14 18 1c 10 14 20
  //   24 28 2c
  //   contents of 评测数据IR (hex, n*v repeats v):
  //   0 4583 2058663 106613 d6c6b3 c686b3 b60663 160613 ff5ff06f c686b3 b60663 160613 ff5ff06f c686b3
  //   b60663 160613 ff5ff06f c686b3 b60663 160613 ff5ff06f c686b3 b60663 160613 ff5ff06f c686b3 b60663
  //   160613 ff5ff06f c686b3 b60663 160613 ff5ff06f c686b3 b60663 160613 ff5ff06f c686b3 b60663 160613
  //   ff5ff06f c686b3 b60663 160613 ff5ff06f c686b3 b60663 160613 ff5ff06f c686b3 b60663 160613 ff5ff06f
  //   c686b3 b60663 160613 ff5ff06f c686b3 b60663 160613 ff5ff06f c686b3 b60663 160613 ff5ff06f c686b3
  //   b60663 d02223 c10537 fee50513 73
  //   生成测试电路输出结果
  //   contents of 评测数据BusW (hex, n*v repeats v):
  //   0 10 0 1 0 1 1 2 20 3 1 3 20 6 1 4 20 a 1 5 20 f 1 6 20 15 1 7 20 1c 1 8 20 24 1 9 20 2d 1 a 20 37 1
  //   b 20 42 1 c 20 4e 1 d 20 5b 1 e 20 69 1 f 20 78 1 10 20 88 0 4 c10000 c0ffee
  //   contents of 评测数据Din (hex, n*v repeats v):
  //   5*0 1 10 0 0 2 10 0 0 3 10 0 0 4 10 0 0 5 10 0 0 6 10 0 0 7 10 0 0 8 10 0 0 9 10 0 0 a 10 0 0 b 10 0
  //   0 c 10 0 0 d 10 0 0 e 10 0 0 f 10 0 0 10 10 88 10
  //   输出引脚
  //   contents of 评测数据Cycles (hex, n*v repeats v):
  //   0 0 1 2 3 4 5 6 7 8 9 a b c d e f 10 11 12 13 14 15 16 17 18 19 1a 1b 1c 1d 1e 1f 20 21 22 23 24 25
  //   26 27 28 29 2a 2b 2c 2d 2e 2f 30 31 32 33 34 35 36 37 38 39 3a 3b 3c 3d 3e 3f 40 41 42 43 44 45
  //   评测通过
endmodule
