// Logisim project lab6.4.chk.circ as structural Verilog: 1 circuit, main circuit main
module main (
  output [31:0] PC,
  output [31:0] IR,
  output [31:0] BusW,
  output [31:0] Din,
  output [15:0] Cycles,
  output _passed,
  output halt
);

  wire CLK, comparator_1_eq, comparator_2_eq, comparator_3_eq, comparator_4_eq, comparator_5_eq,
       comparator_6_eq, main_1_halt, not_1_out, Reset_data, Running;
  wire [8:0] tunnel;
  wire [15:0] main_1_cycles, \评测数据Cycles_data ;
  wire [31:0] Init_Addr_data, main_1_busw, main_1_din, main_1_ir, main_1_pc, \评测数据BusW_data , \评测数据Din_data ,
       \评测数据IR_data , \评测数据PC_data ;

  Clock clock_1 (.out(CLK));
  Counter #(.width(9), .max('h1ff), .behavior("old")) counter_1 (
    .count(not_1_out), .Q(tunnel), .clk(CLK));  // open: load, D, carry, clr, preset
  not not_1 (not_1_out, halt);
  not not_2 (Running, comparator_1_eq);
  Comparator #(.width(9), .mode("unsigned")) comparator_1 (
    .a(tunnel), .b(9'h151), .eq(comparator_1_eq));  // open: gt, lt
  ROM #(.addrWidth(9), .dataWidth(32), .Select("low")) Init_Addr (.addr(tunnel), .data(Init_Addr_data));
  ROM #(.addrWidth(9), .dataWidth(1), .Select("low")) Reset (.addr(tunnel), .data(Reset_data));
  ROM #(.addrWidth(9), .dataWidth(32), .Select("high")) \u_评测数据PC  (.addr(tunnel), .data(\评测数据PC_data ));
  ROM #(.addrWidth(9), .dataWidth(32), .Select("high")) \u_评测数据IR  (.addr(tunnel), .data(\评测数据IR_data ));
  RAM #(.addrWidth(9), .dataWidth(32), .bus("separate"), .simpleMode("false"), .Select("low")) ram_1 (
    .addr(tunnel), .din(PC), .str(Running), .clk(CLK));  // open: data, sel, ld, clr
  Comparator #(.width(32), .mode("unsigned")) comparator_2 (
    .a(PC), .b(\评测数据PC_data ), .eq(comparator_2_eq));  // open: gt, lt
  Comparator #(.width(32), .mode("unsigned")) comparator_3 (
    .a(IR), .b(\评测数据IR_data ), .eq(comparator_3_eq));  // open: gt, lt
  lab6_4_main main_1 (
    .ReSet(Reset_data), .Init_Addr(Init_Addr_data), .PC(main_1_pc), .IR(main_1_ir), .BusW(main_1_busw),
    .Din(main_1_din), .Cycles(main_1_cycles), .Halt(main_1_halt), .clk(CLK));
  Register #(.width(1), .Select("low")) register_1 (.D(main_1_halt), .Q(halt), .clk(CLK));  // open: en, clr
  RAM #(.addrWidth(9), .dataWidth(32), .bus("separate"), .simpleMode("false"), .Select("low")) ram_2 (
    .addr(tunnel), .din(IR), .str(Running), .clk(CLK));  // open: data, sel, ld, clr
  ROM #(.addrWidth(9), .dataWidth(32), .Select("high")) \u_评测数据BusW  (.addr(tunnel), .data(\评测数据BusW_data ));
  ROM #(.addrWidth(9), .dataWidth(32), .Select("high")) \u_评测数据Din  (.addr(tunnel), .data(\评测数据Din_data ));
  Register #(.width(32), .Select("low")) register_2 (.D(main_1_pc), .Q(PC), .clk(CLK));  // open: en, clr
  Register #(.width(32), .Select("low")) register_3 (.D(main_1_ir), .Q(IR), .clk(CLK));  // open: en, clr
  Register #(.width(32), .Select("low")) register_4 (.D(main_1_busw), .Q(BusW), .clk(CLK));  // open: en, clr
  Register #(.width(32), .Select("low")) register_5 (.D(main_1_din), .Q(Din), .clk(CLK));  // open: en, clr
  Register #(.width(16), .Select("low")) register_6 (.D(main_1_cycles), .Q(Cycles), .clk(CLK));  // open: en, clr
  RAM #(.addrWidth(9), .dataWidth(32), .bus("separate"), .simpleMode("false"), .Select("low")) ram_3 (
    .addr(tunnel), .din(BusW), .str(Running), .clk(CLK));  // open: data, sel, ld, clr
  Comparator #(.width(32), .mode("unsigned")) comparator_4 (
    .a(BusW), .b(\评测数据BusW_data ), .eq(comparator_4_eq));  // open: gt, lt
  Comparator #(.width(32), .mode("unsigned")) comparator_5 (
    .a(Din), .b(\评测数据Din_data ), .eq(comparator_5_eq));  // open: gt, lt
  RAM #(.addrWidth(9), .dataWidth(32), .bus("separate"), .simpleMode("false"), .Select("low")) ram_4 (
    .addr(tunnel), .din(Din), .str(Running), .clk(CLK));  // open: data, sel, ld, clr
  ROM #(.addrWidth(9), .dataWidth(16), .Select("high")) \u_评测数据Cycles  (.addr(tunnel), .data(\评测数据Cycles_data ));
  and and_1 (_passed, comparator_2_eq, comparator_3_eq, comparator_4_eq, comparator_5_eq, comparator_6_eq);
  Comparator #(.width(16), .mode("unsigned")) comparator_6 (
    .a(Cycles), .b(\评测数据Cycles_data ), .eq(comparator_6_eq));  // open: gt, lt
  RAM #(.addrWidth(9), .dataWidth(16), .bus("separate"), .simpleMode("false"), .Select("low")) ram_5 (
    .addr(tunnel), .din(Cycles), .str(Running), .clk(CLK));  // open: data, sel, ld, clr
  RAM #(.addrWidth(9), .dataWidth(1), .bus("separate"), .simpleMode("false"), .Select("low")) ram_6 (
    .addr(tunnel), .din(_passed), .str(Running), .clk(CLK));  // open: data, sel, ld, clr

  // Other names for the same wires on the sheet: Equal = _passed

  // Notes on the sheet:
  //   生成测试数据地址
  //   测试脉冲数
  //   输出数据
  //   contents of 评测数据PC (hex, n*v repeats v):
  //   0 0 4 8 c 10 14 18 1c 20 24 28 2c 10 14 18 1c 20 24 28 2c 10 14 18 1c 20 24 28 2c 10 14 18 1c 28 2c
  //   10 14 18 1c 20 24 28 2c 10 14 18 1c 28 2c 10 14 18 1c 20 24 28 2c 10 14 18 1c 20 24 28 2c 10 14 18
  //   1c 20 24 28 2c 30 34 c 10 14 18 1c 20 24 28 2c 10 14 18 1c 20 24 28 2c 10 14 18 1c 28 2c 10 14 18 1c
  //   20 24 28 2c 10 14 18 1c 28 2c 10 14 18 1c 20 24 28 2c 10 14 18 1c 20 24 28 2c 10 14 18 1c 28 2c 30
  //   34 c 10 14 18 1c 28 2c 10 14 18 1c 28 2c 10 14 18 1c 28 2c 10 14 18 1c 28 2c 10 14 18 1c 20 24 28 2c
  //   10 14 18 1c 20 24 28 2c 10 14 18 1c 28 2c 30 34 c 10 14 18 1c 28 2c 10 14 18 1c 28 2c 10 14 18 1c 28
  //   2c 10 14 18 1c 20 24 28 2c 10 14 18 1c 20 24 28 2c 10 14 18 1c 28 2c 30 34 c 10 14 18 1c 28 2c 10 14
  //   18 1c 28 2c 10 14 18 1c 20 24 28 2c 10 14 18 1c 28 2c 10 14 18 1c 28 2c 30 34 c 10 14 18 1c 28 2c 10
  //   14 18 1c 20 24 28 2c 10 14 18 1c 28 2c 10 14 18 1c 28 2c 30 34 c 10 14 18 1c 28 2c 10 14 18 1c 28 2c
  //   10 14 18 1c 28 2c 30 34 c 10 14 18 1c 28 2c 10 14 18 1c 28 2c 30 34 c 10 14 18 1c 28 2c 30 34 38
  //   contents of 评测数据IR (hex, n*v repeats v):
  //   0 4283 100593 28633 100693 269713 74803 474883 108f663 1170023 1070223 168693 fec6e2e3 269713 74803
  //   474883 108f663 1170023 1070223 168693 fec6e2e3 269713 74803 474883 108f663 1170023 1070223 168693
  //   fec6e2e3 269713 74803 474883 108f663 168693 fec6e2e3 269713 74803 474883 108f663 1170023 1070223
  //   168693 fec6e2e3 269713 74803 474883 108f663 168693 fec6e2e3 269713 74803 474883 108f663 1170023
  //   1070223 168693 fec6e2e3 269713 74803 474883 108f663 1170023 1070223 168693 fec6e2e3 269713 74803
  //   474883 108f663 1170023 1070223 168693 fec6e2e3 40b60633 fcb61ce3 100693 269713 74803 474883 108f663
  //   1170023 1070223 168693 fec6e2e3 269713 74803 474883 108f663 1170023 1070223 168693 fec6e2e3 269713
  //   74803 474883 108f663 168693 fec6e2e3 269713 74803 474883 108f663 1170023 1070223 168693 fec6e2e3
  //   269713 74803 474883 108f663 168693 fec6e2e3 269713 74803 474883 108f663 1170023 1070223 168693
  //   fec6e2e3 269713 74803 474883 108f663 1170023 1070223 168693 fec6e2e3 269713 74803 474883 108f663
  //   168693 fec6e2e3 40b60633 fcb61ce3 100693 269713 74803 474883 108f663 168693 fec6e2e3 269713 74803
  //   474883 108f663 168693 fec6e2e3 269713 74803 474883 108f663 168693 fec6e2e3 269713 74803 474883
  //   108f663 168693 fec6e2e3 269713 74803 474883 108f663 1170023 1070223 168693 fec6e2e3 269713 74803
  //   474883 108f663 1170023 1070223 168693 fec6e2e3 269713 74803 474883 108f663 168693 fec6e2e3 40b60633
  //   fcb61ce3 100693 269713 74803 474883 108f663 168693 fec6e2e3 269713 74803 474883 108f663 168693
  //   fec6e2e3 269713 74803 474883 108f663 168693 fec6e2e3 269713 74803 474883 108f663 1170023 1070223
  //   168693 fec6e2e3 269713 74803 474883 108f663 1170023 1070223 168693 fec6e2e3 269713 74803 474883
  //   108f663 168693 fec6e2e3 40b60633 fcb61ce3 100693 269713 74803 474883 108f663 168693 fec6e2e3 269713
  //   74803 474883 108f663 168693 fec6e2e3 269713 74803 474883 108f663 1170023 1070223 168693 fec6e2e3
  //   269713 74803 474883 108f663 168693 fec6e2e3 269713 74803 474883 108f663 168693 fec6e2e3 40b60633
  //   fcb61ce3 100693 269713 74803 474883 108f663 168693 fec6e2e3 269713 74803 474883 108f663 1170023
  //   1070223 168693 fec6e2e3 269713 74803 474883 108f663 168693 fec6e2e3 269713 74803 474883 108f663
  //   168693 fec6e2e3 40b60633 fcb61ce3 100693 269713 74803 474883 108f663 168693 fec6e2e3 269713 74803
  //   474883 108f663 168693 fec6e2e3 269713 74803 474883 108f663 168693 fec6e2e3 40b60633 fcb61ce3 100693
  //   269713 74803 474883 108f663 168693 fec6e2e3 269713 74803 474883 108f663 168693 fec6e2e3 40b60633
  //   fcb61ce3 100693 269713 74803 474883 108f663 168693 fec6e2e3 40b60633 fcb61ce3 73
  //   生成测试电路输出结果
  //   contents of 评测数据BusW (hex, n*v repeats v):
  //   0 a 1 a 1 4 78 34 1 4 8 2 1 8 78 2 1 8 c 3 1 c 78 12 1 c 10 4 1 10 78 a3 0 5 1 14 a3 56 1 14 18 6 1
  //   18 a3 db 0 7 1 1c db 5 1 1c 20 8 1 20 db 49 1 20 24 9 1 24 db c7 1 24 28 a 0 9 0 1 4 34 2 1 4 8 2 1
  //   8 34 12 1 8 c 3 1 c 34 78 0 4 1 10 78 56 1 10 14 5 1 14 78 a3 0 6 1 18 a3 5 1 18 1c 7 1 1c a3 49 1
  //   1c 20 8 1 20 a3 c7 0 9 0 8 0 1 4 2 12 0 2 1 8 12 34 0 3 1 c 34 56 0 4 1 10 56 78 0 5 1 14 78 5 1 14
  //   18 6 1 18 78 49 1 18 1c 7 1 1c 78 a3 0 8 0 7 0 1 4 2 12 0 2 1 8 12 34 0 3 1 c 34 56 0 4 1 10 56 5 1
  //   10 14 5 1 14 56 49 1 14 18 6 1 18 56 78 0 7 0 6 0 1 4 2 12 0 2 1 8 12 34 0 3 1 c 34 5 1 c 10 4 1 10
  //   34 49 0 5 1 14 49 56 0 6 0 5 0 1 4 2 12 0 2 1 8 12 5 1 8 c 3 1 c 12 34 0 4 1 10 34 49 0 5 0 4 0 1 4
  //   2 5 0 2 1 8 5 12 0 3 1 c 12 34 0 4 0 3 0 1 4 2 5 0 2 1 8 5 12 0 3 0 2 0 1 4 2 5 0 2 0 1
  //   contents of 评测数据Din (hex, n*v repeats v):
  //   8*0 78 34 78 0 a 0 0 0 78 2 78 0 a 0 0 0 78 12 78 0 a 0 0 0 78 0 a 0 0 0 a3 56 a3 0 a 0 0 0 a3 0 a 0
  //   0 0 db 5 db 0 a 0 0 0 db 49 db 0 a 0 0 0 db c7 db 0 a 1 1 4*0 34 2 34 0 9 0 0 0 34 12 34 0 9 0 0 0
  //   34 0 9 0 0 0 78 56 78 0 9 0 0 0 78 0 9 0 0 0 a3 5 a3 0 9 0 0 0 a3 49 a3 0 9 0 0 0 a3 0 9 1 1 4*0 2 0
  //   8 0 0 0 12 0 8 0 0 0 34 0 8 0 0 0 56 0 8 0 0 0 78 5 78 0 8 0 0 0 78 49 78 0 8 0 0 0 78 0 8 1 1 4*0 2
  //   0 7 0 0 0 12 0 7 0 0 0 34 0 7 0 0 0 56 5 56 0 7 0 0 0 56 49 56 0 7 0 0 0 56 0 7 1 1 4*0 2 0 6 0 0 0
  //   12 0 6 0 0 0 34 5 34 0 6 0 0 0 34 0 6 0 0 0 49 0 6 1 1 4*0 2 0 5 0 0 0 12 5 12 0 5 0 0 0 12 0 5 0 0
  //   0 34 0 5 1 1 4*0 2 0 4 0 0 0 5 0 4 0 0 0 12 0 4 1 1 4*0 2 0 3 0 0 0 5 0 3 1 1 4*0 2 0 2 1 1
  //   输出引脚
  //   contents of 评测数据Cycles (hex, n*v repeats v):
  //   0 0 1 2 3 4 5 6 7 8 9 a b c d e f 10 11 12 13 14 15 16 17 18 19 1a 1b 1c 1d 1e 1f 20 21 22 23 24 25
  //   26 27 28 29 2a 2b 2c 2d 2e 2f 30 31 32 33 34 35 36 37 38 39 3a 3b 3c 3d 3e 3f 40 41 42 43 44 45 46
  //   47 48 49 4a 4b 4c 4d 4e 4f 50 51 52 53 54 55 56 57 58 59 5a 5b 5c 5d 5e 5f 60 61 62 63 64 65 66 67
  //   68 69 6a 6b 6c 6d 6e 6f 70 71 72 73 74 75 76 77 78 79 7a 7b 7c 7d 7e 7f 80 81 82 83 84 85 86 87 88
  //   89 8a 8b 8c 8d 8e 8f 90 91 92 93 94 95 96 97 98 99 9a 9b 9c 9d 9e 9f a0 a1 a2 a3 a4 a5 a6 a7 a8 a9
  //   aa ab ac ad ae af b0 b1 b2 b3 b4 b5 b6 b7 b8 b9 ba bb bc bd be bf c0 c1 c2 c3 c4 c5 c6 c7 c8 c9 ca
  //   cb cc cd ce cf d0 d1 d2 d3 d4 d5 d6 d7 d8 d9 da db dc dd de df e0 e1 e2 e3 e4 e5 e6 e7 e8 e9 ea eb
  //   ec ed ee ef f0 f1 f2 f3 f4 f5 f6 f7 f8 f9 fa fb fc fd fe ff 100 101 102 103 104 105 106 107 108 109
  //   10a 10b 10c 10d 10e 10f 110 111 112 113 114 115 116 117 118 119 11a 11b 11c 11d 11e 11f 120 121 122
  //   123 124 125 126 127 128 129 12a 12b 12c 12d 12e 12f 130 131 132 133 134 135 136 137 138 139 13a 13b
  //   13c 13d 13e 13f 140 141 142 143 144 145 146 147 148 149 14a 14b 14c 14d 14e 14f 150
  //   评测通过
endmodule
