// Logisim project lab8.3.circ as structural Verilog: 22 circuits, main circuit 跳转检测
module main (
  input  [31:0] Init_Addr,
  input  ReSet,
  input  [31:0] BP_PC,
  input  BPEn,
  input  clk,
  output [31:0] WB_PC,
  output [31:0] WB_BusW,
  output [15:0] Cycles,
  output Stop
);

  wire clk_out, clk_t, Halt, not_2_out;
  wire [15:0] \RS1转发次数 , \RS2转发次数 , \冲刷次数 , \分支指令数 , \跳转指令数 , \阻塞次数 ;
  wire [31:0] EX_PC, ID_PC, IF_PC, M_PC, WB_IR;

  Clock u_clk (.out(clk_out));
  not not_1 (clk_t, clk_out);
  // Probe on IF_PC
  // Probe on ID_PC
  // Probe on EX_PC
  // Probe on M_PC
  // Probe on WB_PC
  // Probe on Cycles
  // Probe on \阻塞次数 
  // Probe on \冲刷次数 
  // Probe on \跳转指令数 
  // Probe on \分支指令数 
  // Probe on \RS1转发次数 
  // Probe on \RS2转发次数 
  Register #(.width(1), .trigger("falling"), .Select("low")) register_1 (
    .D(Halt), .en(not_2_out), .Q(Stop), .clk(clk_t), .clr(ReSet));
  not not_2 (not_2_out, Stop);
  Hex_Digit_Display hex_digit_display_1 (.value(WB_IR[31:28]));  // open: dp
  Hex_Digit_Display hex_digit_display_2 (.value(WB_IR[27:24]));  // open: dp
  Hex_Digit_Display hex_digit_display_3 (.value(WB_IR[23:20]));  // open: dp
  Hex_Digit_Display hex_digit_display_4 (.value(WB_IR[19:16]));  // open: dp
  Hex_Digit_Display hex_digit_display_5 (.value(WB_IR[11:8]));  // open: dp
  Hex_Digit_Display hex_digit_display_6 (.value(WB_IR[15:12]));  // open: dp
  Hex_Digit_Display hex_digit_display_7 (.value(WB_IR[3:0]));  // open: dp
  Hex_Digit_Display hex_digit_display_8 (.value(WB_IR[7:4]));  // open: dp

  // Other names for the same wires on the sheet: BP_En = BPEn; 总周期数[15:0] = Cycles

  // Notes on the sheet:
  //   断点调试
  //   输入引脚
  //   输出引脚
  //   请勿修改引脚名称、电路名称及电路封装外观
  //   为方便调试，需要输出流水线各段保存的PC值、时钟周期数、冒险处理次数、分支与跳转指令执行数等信息
  //   流水调试日志
  //   程序运行分析
  //   程序执行结束
  //   数码管输出
endmodule

module \跳转检测  (
  input  [2:0] M_BandJ,
  input  M_Zero,
  input  M_Result0,
  output PCsrc
);


  // Notes on the sheet:
  //   M_BandJ: pull=down
  //   M_Zero: pull=down
  //   输入信号
  //   请勿修改引脚名称、电路名称及电路封装外观
  //   不要修改控制信号的编码定义、引脚名称和在布局中的位置。
  //   输出信号
endmodule

module \控制器  (
  input  [6:0] opcode,
  input  [2:0] funct3,
  input  [6:0] funct7,
  input  Stall,
  output [2:0] ExtOp,
  output RegWr,
  output [2:0] BandJ,
  output ALUASrc,
  output [1:0] ALUBSrc,
  output [3:0] ALUctr,
  output MemtoReg,
  output [2:0] MemOp,
  output MemWr,
  output Halt
);


  // Notes on the sheet:
  //   输入引脚
  //   请勿修改引脚名称、电路名称及电路封装外观
  //   提示：根据指令种类，把7位指令code用一位指令类型标志位来表示，再通过功能码来区分具体指令，生成控制信号。
  //   输出引脚
endmodule

module IFU (
  input  Reset,
  input  BPEn,
  input  PCSrc,
  input  Stall,
  input  [31:0] Initial_Address,
  input  [31:0] BP_PC,
  input  [31:0] PCTarget,
  input  CLK,
  input  halt,
  output [31:0] PC
);


  // Other names for the same wires on the sheet: BP_En = BPEn; Init_Addr[31:0] = Initial_Address

  // Notes on the sheet:
  //   Stall: pull=down
  //   PCSrc: pull=down
  //   PCTarget: pull=down
  //   断点调试
  //   输入信号
  //   请勿修改引脚名称、电路名称及电路封装外观
  //   指令存储器256KB，数据位为32位，地址位为16位。PC寄存器数据宽度32位，片选信号高电平有效
  //   输出信号
endmodule

module IDU (
  input  [2:0] ExtOp,
  input  RegWr,
  input  [4:0] WB_Rd,
  input  [31:0] IR,
  input  [31:0] BusW,
  input  CLK,
  output [6:0] OpCode,
  output [2:0] Funct3,
  output [6:0] Funct7,
  output [31:0] Imm,
  output [31:0] BusA,
  output [31:0] BusB,
  output [4:0] Rd,
  output [4:0] Rs1,
  output [4:0] Rs2
);


  // Other names for the same wires on the sheet: op[6:0] = OpCode

  // Notes on the sheet:
  //   WB_Rd: pull=down
  //   RegWr: pull=down
  //   BusW: pull=down
  //   ExtOp: pull=down
  //   指令解析
  //   输入信号
  //   为了后续实验中的引用，不要修改ExtOP编码定义。
  //   请勿修改引脚名称、电路名称及电路封装外观
  //   访问寄存器堆
  //   修改寄存器堆电路设计，0号寄存器始终为0。
  //   输出数据
  //   输出信号
endmodule

module RegFile (
  input  [4:0] R1_num,
  input  [4:0] R2_num,
  input  [4:0] Write_Reg_num,
  input  [31:0] Din,
  input  Write_Enable,
  input  Clock,
  output [31:0] Reg1Out,
  output [31:0] Reg2Out
);


  // Other names for the same wires on the sheet: CLK = Clock; RA[4:0] = R1_num; RB[4:0] = R2_num; RDA[31:0] = Reg1Out;
  //   RDB[31:0] = Reg2Out; RW[4:0] = Write_Reg_num; WE = Write_Enable

  // Notes on the sheet:
  //   输入引脚
  //   请勿修改引脚名称、电路名称及电路封装外观
  //   提示：使用译码器、多路选择器和32位寄存器及逻辑门实现寄存器堆，禁止直接使用存储器组件。
  //   输出引脚
endmodule

module \立即数扩展器  (
  input  [31:0] Instr,
  input  [2:0] Extop,
  output [31:0] imm
);


  // Notes on the sheet:
  //   Extop: pull=down
  //   Instr: pull=down
  //   输入引脚
  //   输出引脚
endmodule

module DataRAM (
  input  CLK,
  input  CLR,
  input  WE,
  input  [2:0] MemOp,
  input  [17:0] Addr,
  input  [31:0] Din,
  output AlignErr,
  output [31:0] DataOut
);


  // Other names for the same wires on the sheet: Dout[31:0] = DataOut

  // Notes on the sheet:
  //   输入引脚
  //   请勿修改引脚名称、电路名称及电路封装外观
  //   为了后续实验中的引用，不要修改MemOp的编码定义、引脚名称和在布局中的位置。
  //   32位数据存储器，按字节分4片存储，可按照字节、半字和字进行存储；读取字节或半字时，支持0扩展和符号位扩展。
  //   输出引脚
endmodule

module ALU (
  input  [3:0] ALUctr,
  input  [31:0] A,
  input  [31:0] B,
  output Zero,
  output [31:0] S
);

  // Probe on A
  // Probe on B
  // Probe on S

  // Other names for the same wires on the sheet: Result[31:0] = S

  // Notes on the sheet:
  //   B: pull=down
  //   ALUctr: pull=down
  //   A: pull=down
  //   输入引脚
  //   请勿修改引脚名称、电路名称及电路封装外观
  //   提示：使用32位并行加法器子电路、桶形移位器、ALU控制子电路实现32位ALU
  //   功能说明:32位ALU，输入32位操作数A、B，4位控制信号ALUctr，输出32位结果Reseult和1位Zero标志位
  //   输出引脚
  //   操作数和结果
endmodule

module ALUctrl (
  input  [3:0] ALUctr,
  output SUBctr,
  output SFTctr,
  output SIGctr,
  output ALctr,
  output [2:0] OPctr
);


  // Other names for the same wires on the sheet: LRctr = SFTctr

  // Notes on the sheet:
  //   输入引脚
  //   ALU操作控制信号生成部件
  //   输出引脚
endmodule

module Adder32 (
  input  Cin,
  input  [31:0] X,
  input  [31:0] Y,
  output CF,
  output Cout,
  output OF,
  output SF,
  output [31:0] S,
  output ZF
);

  // Probe on X
  // Probe on Y
  // Probe on S

  // Notes on the sheet:
  //   Y: pull=down
  //   Cin: pull=down
  //   X: pull=down
  //   输入引脚区
  //   输出引脚区
  //   请勿修改引脚名称、电路名称及电路封装外观
  //   提示：使用16位并行加法器子电路实现32位快速加法器
  //   功能说明:32位Adder  S=X+Y，Cout为最高位进位位，Cin为进位输入， S为和，溢出OF、进位CF、零ZF、符号SF。
  //   +
  //   =
  //   无符号加法
endmodule

// 移位器
module Shifter32 (
  input  [4:0] shamt,
  input  L_R,
  input  A_L,
  input  [31:0] DataIn,
  output [31:0] DataOut
);


  // Other names for the same wires on the sheet: Arth_Logic = A_L; Din[31:0] = DataIn; Dout[31:0] = DataOut;
  //   Left_Right = L_R

  // Notes on the sheet:
  //   L/R,A/L: 00逻辑右移，01算术右移，10逻辑左移，11：循环左移
  //   输入引脚
  //   请勿修改引脚名称、电路名称及电路封装外观
  //   提示：使用多路选择器、逻辑门实现32位桶形移位器，禁止直接使用移位器组件。
  //   输出引脚
endmodule

module Adder16 (
  input  C0,
  input  [15:0] X,
  input  [15:0] Y,
  output C16,
  output Pg,
  output Gg,
  output [15:0] S
);

  // Probe on X
  // Probe on Y
  // Probe on S

  // Notes on the sheet:
  //   Y: pull=down
  //   X: pull=down
  //   C0: pull=down
  //   输入引脚区
  //   请勿修改引脚名称、电路名称及电路封装外观
  //   提示：使用4位先行进位加法器和CLU子电路实现16位并行加法器
  //   功能说明:16位Adder  S=X+Y，C16为最高位进位位，C0为进位输入， Pg、Gg为成组进位生成传递函数
  //   输出引脚区
  //   +
  //   =
  //   无符号加法
endmodule

module CLA4 (
  input  [3:0] X,
  input  [3:0] Y,
  input  Cin,
  output [3:0] F,
  output Cout,
  output Pg,
  output Gg
);

  Hex_Digit_Display hex_digit_display_1 (.value(X));  // open: dp
  Hex_Digit_Display hex_digit_display_2 (.value(Y));  // open: dp
  Hex_Digit_Display hex_digit_display_3 (.value(F));  // open: dp

  // Other names for the same wires on the sheet: Z[3:0] = F

  // Notes on the sheet:
  //   +
  //   =
  //   输出
  //   输入
  //   请勿修改引脚名称、电路名称及电路封装外观
  //   提示：使用全加器和CLU子电路实现四位先行进位加法器CLA4
endmodule

module CLU4 (
  input  P0,
  input  P1,
  input  P2,
  input  P3,
  input  G0,
  input  G1,
  input  G2,
  input  G3,
  input  C0,
  output C1,
  output C3,
  output C2,
  output C4,
  output Pg,
  output Gg
);


  // Notes on the sheet:
  //   输入引脚
  //   请勿修改引脚名称、电路名称及电路封装外观
  //   提示：使用逻辑门电路实现4位四位先行进位部件CLU，Pg、Gg为成组进位生成传递函数
  //   输出引脚
endmodule

module FA (
  input  A,
  input  B,
  input  Cin,
  output F,
  output P,
  output G
);


  // Notes on the sheet:
  //   输入引脚
  //   请勿修改引脚名称、电路名称及电路封装外观
  //   输出引脚
endmodule

module \阻塞检测  (
  input  [6:0] IF_opcode,
  input  [4:0] EX_rd,
  input  [4:0] IF_rs1,
  input  EX_MemtoReg,
  input  [4:0] IF_rs2,
  output Stall
);


  // Notes on the sheet:
  //   EX_MemtoReg: pull=down
  //   EX_rd: pull=down
  //   输入信号
  //   输出信号
endmodule

module \转发检测  (
  input  [4:0] EX_rs1,
  input  [4:0] M_rd,
  input  [4:0] EX_rs2,
  input  [4:0] WB_rd,
  input  M_RegWr,
  input  WB_RegWr,
  input  [6:0] EX_opcode,
  output [1:0] BusAFW,
  output [1:0] BusBFW
);


  // Notes on the sheet:
  //   WB_rd: pull=down
  //   EX_rs1: pull=down
  //   M_rd: pull=down
  //   EX_rs2: pull=down
  //   输入信号
  //   输出信号
endmodule

module \流水段寄存器  (
  input  CLR,
  input  [31:0] PC,
  input  CLK,
  input  WE,
  input  Halt,
  input  [31:0] IR,
  input  [3:0] ALUctr,
  input  ALUASrc,
  input  [1:0] ALUBSrc,
  input  [31:0] BusA,
  input  [2:0] BandJ,
  input  [2:0] MemOp,
  input  MemWr,
  input  [31:0] BusB,
  input  RegWr,
  input  MemtoReg,
  input  [4:0] RD,
  input  [31:0] Imm,
  input  [4:0] RS1,
  input  [4:0] RS2,
  input  Zero,
  input  [31:0] Result,
  input  [6:0] Opcode,
  input  [31:0] PCTarget,
  input  [31:0] Dout,
  output [31:0] PCo,
  output Halto,
  output [31:0] IRo,
  output [3:0] ALUctro,
  output ALUASrco,
  output [1:0] ALUBSrco,
  output [31:0] BusAo,
  output [2:0] BandJo,
  output [2:0] MemOpo,
  output MemWro,
  output [31:0] BusBo,
  output RegWro,
  output MemtoRego,
  output [4:0] RDo,
  output [31:0] Immo,
  output [4:0] RS1o,
  output [4:0] RS2o,
  output Zeroo,
  output [31:0] Resulto,
  output [6:0] Opcodeo,
  output [31:0] PCTargeto,
  output [31:0] Douto
);


  // Notes on the sheet:
  //   输入引脚区
  //   输出引脚区
endmodule

module DM (
  input  [15:0] Addr,
  input  [31:0] Din,
  input  CLK,
  input  CLR,
  input  [2:0] MemOp,
  input  WE,
  input  SEL,
  output [31:0] DataOut
);


  // Other names for the same wires on the sheet: Dout[31:0] = DataOut

  // Notes on the sheet:
  //   输入引脚区
  //   32位数据存储器，按字节分4片存储，可按照字节、半字和字进行存储；读取字节或半字时，支持0扩展和符号位扩展。
  //   为了后续实验中的引用，不要修改MemOp的编码定义，以及引脚名称和在布局图中位置。
  //   输出引脚区
endmodule

module \基本流水线  (
  input  ReSet,
  input  BPEn,
  input  [31:0] Init_Addr,
  input  [31:0] BP_PC,
  input  clk,
  output WB_RegWr,
  output M_MemWr,
  output [1:0] BusAFW,
  output [1:0] BusBFW,
  output [31:0] IF_PC,
  output [31:0] ID_PC,
  output [31:0] EX_PC,
  output [31:0] M_PC,
  output [31:0] WB_PC,
  output [31:0] WB_BusW,
  output [31:0] M_Din,
  output [31:0] WB_IR,
  output Stop
);

  wire BP_Puase, clk_out, clk_t, comparator_1_eq, Halt, not_2_out;
  wire [15:0] \RS1转发次数 , \RS2转发次数 , \冲刷次数 , \分支和跳转指令数 , \总周期数 , \阻塞次数 ;

  Clock u_clk (.out(clk_out));
  not not_1 (clk_t, clk_out);
  // Probe on IF_PC
  // Probe on ID_PC
  // Probe on EX_PC
  // Probe on M_PC
  // Probe on WB_PC
  // Probe on \总周期数 
  // Probe on \阻塞次数 
  // Probe on \冲刷次数 
  // Probe on \RS1转发次数 
  // Probe on \RS2转发次数 
  // Probe on \分支和跳转指令数 
  Hex_Digit_Display hex_digit_display_1 (.value(WB_IR[31:28]));  // open: dp
  Hex_Digit_Display hex_digit_display_2 (.value(WB_IR[27:24]));  // open: dp
  Hex_Digit_Display hex_digit_display_3 (.value(WB_IR[23:20]));  // open: dp
  Hex_Digit_Display hex_digit_display_4 (.value(WB_IR[19:16]));  // open: dp
  Comparator #(.width(32)) comparator_1 (.a(IF_PC), .b(BP_PC), .eq(comparator_1_eq));  // open: gt, lt
  Hex_Digit_Display hex_digit_display_5 (.value(WB_IR[11:8]));  // open: dp
  Hex_Digit_Display hex_digit_display_6 (.value(WB_IR[15:12]));  // open: dp
  and and_1 (BP_Puase, BPEn, comparator_1_eq);
  Hex_Digit_Display hex_digit_display_7 (.value(WB_IR[3:0]));  // open: dp
  Hex_Digit_Display hex_digit_display_8 (.value(WB_IR[7:4]));  // open: dp
  Register #(.width(1), .trigger("falling"), .Select("low")) register_1 (
    .D(Halt), .en(not_2_out), .Q(Stop), .clk(clk_t), .clr(ReSet));
  not not_2 (not_2_out, Stop);

  // Other names for the same wires on the sheet: BP_En = BPEn

  // Notes on the sheet:
  //   断点调试
  //   输入引脚
  //   请勿修改引脚名称、电路名称及电路封装外观
  //   流水调试日志
  //   为方便自动评测，需要输出流水线各段保存的PC值、ID段寄存器写入信息、M段内存写入信息以及WB段指令信息
  //   输出引脚
  //   程序运行分析
  //   断点控制
  //   数码管输出
  //   程序执行结束
endmodule

module EU (
  input  [3:0] ALUctr,
  input  ALUASrc,
  input  [1:0] ALUBSrc,
  input  [31:0] PC,
  input  [31:0] BusA,
  input  [31:0] BusB,
  input  [31:0] Imm,
  input  [2:0] BandJ,
  output [31:0] PCTarget,
  output [31:0] Result,
  output Zero
);


  // Notes on the sheet:
  //   ALUASrc: pull=down
  //   ALUctr: pull=down
  //   Result: pull=down
  //   BandJ: pull=down
  //   ALUBSrc: pull=down
  //   PCTarget: pull=down
  //   输入信号
  //   请勿修改引脚名称、电路名称及电路封装外观
  //   为了后续实验中的引用，不要修改控制信号编码定义。
  //   输出信号
endmodule
