// Logisim project lab8.4.circ as structural Verilog: 24 circuits, main circuit test
module test (
  input  in_1,
  output [15:0] \RS2转发次数 ,
  output [15:0] \RS1转发次数 ,
  output [15:0] \分支指令数 ,
  output [15:0] \跳转指令数 ,
  output [15:0] \冲刷次数 ,
  output [15:0] \阻塞次数 ,
  output [15:0] \总周期数 ,
  output halt,
  output correct
);

  wire clock_1_out;
  wire [31:0] main_1_out_16;

  // Probe on \RS2转发次数 
  // Probe on \RS1转发次数 
  // Probe on \分支指令数 
  // Probe on \跳转指令数 
  // Probe on \冲刷次数 
  // Probe on \阻塞次数 
  Clock clock_1 (.out(clock_1_out));
  main main_1 (
    .Init_Addr({32{1'b0}}), .ReSet(in_1), .BP_PC({32{1'b0}}), .BPEn(1'b0), .Cycles(\总周期数 ), .halt(halt),
    .clk(clock_1_out), .out_16(main_1_out_16), .out_10(\阻塞次数 ), .out_11(\冲刷次数 ), .out_12(\跳转指令数 ),
    .out_13(\分支指令数 ), .out_14(\RS1转发次数 ), .out_15(\RS2转发次数 ));  // open: WB_PC, WB_BusW
  Comparator #(.width(32), .mode("unsigned")) comparator_1 (
    .a(main_1_out_16), .b(32'hc0ffee), .eq(correct));  // open: gt, lt
  // Probe on \总周期数 
  // Probe on main_1_out_16
endmodule

module main (
  input  [31:0] Init_Addr,
  input  ReSet,
  input  [31:0] BP_PC,
  input  BPEn,
  input  clk,
  output [31:0] WB_PC,
  output [31:0] WB_BusW,
  output [15:0] Cycles,
  output halt,
  output [15:0] out_10,
  output [15:0] out_11,
  output [15:0] out_12,
  output [15:0] out_13,
  output [15:0] out_14,
  output [15:0] out_15,
  output [31:0] out_16
);

  wire and_1_out, and_2_out, clk_t, comparator_1_eq, comparator_2_eq, comparator_3_eq, comparator_4_eq,
       eu_1_zero, not_1_out, not_2_out, or_1_out, or_2_out, or_3_out, or_4_out, or_5_out, or_6_out, or_7_out,
       PCSrc, Stall, Stop, \控制器_1_aluasrc , \控制器_1_memtoreg , \控制器_1_memwr , \控制器_1_regwr ,
       \流水段寄存器_2_aluasrco , \流水段寄存器_2_halto , \流水段寄存器_2_memtorego , \流水段寄存器_2_memwro , \流水段寄存器_2_regwro ,
       \流水段寄存器_3_halto , \流水段寄存器_3_memtorego , \流水段寄存器_3_memwro , \流水段寄存器_3_regwro , \流水段寄存器_4_memtorego ,
       \流水段寄存器_4_regwro ;
  wire [1:0] BusAFW, BusBFW, \控制器_1_alubsrc , \流水段寄存器_2_alubsrco ;
  wire [2:0] idu_1_funct3, WB_BandJ, \控制器_1_bandj , \控制器_1_extop , \控制器_1_memop , \流水段寄存器_2_bandjo ,
       \流水段寄存器_2_memopo , \流水段寄存器_3_bandjo , \流水段寄存器_3_memopo ;
  wire [3:0] \控制器_1_aluctr , \流水段寄存器_2_aluctro ;
  wire [4:0] idu_1_rd, idu_1_rs1, idu_1_rs2, \流水段寄存器_2_rdo , \流水段寄存器_2_rs1o , \流水段寄存器_2_rs2o ,
       \流水段寄存器_3_rdo , \流水段寄存器_4_rdo ;
  wire [6:0] idu_1_funct7, idu_1_opcode;
  wire [31:0] dataram_1_dataout, eu_1_pctarget, eu_1_result, EX_PC, ID_PC, idu_1_busa, idu_1_busb, idu_1_imm,
       IF_PC, M_PC, multiplexer_1_out, multiplexer_2_out, WB_IR, \指令存储器_data , \流水段寄存器_1_iro ,
       \流水段寄存器_2_busao , \流水段寄存器_2_busbo , \流水段寄存器_2_immo , \流水段寄存器_2_iro , \流水段寄存器_3_busbo , \流水段寄存器_3_iro ,
       \流水段寄存器_3_resulto , \流水段寄存器_4_douto , \流水段寄存器_4_resulto ;

  Clock u_clk (.out(clk_t));
  or or_1 (or_1_out, halt, Stop);
  IFU ifu_1 (
    .CLK(clk_t), .Reset(ReSet), .PCSrc(or_3_out), .Initial_Address(Init_Addr), .PCTarget(eu_1_pctarget),
    .PC(IF_PC), .halt(or_1_out), .BPEn(BPEn), .BP_PC(BP_PC), .Stall(Stall));
  // Probe on BP_PC
  ROM #(.addrWidth(16), .dataWidth(32), .Select("high"), .simpleMode("false")) \u_指令存储器  (
    .addr(IF_PC[17:2]), .data(\指令存储器_data ), .sel(1'b1));
  and and_1 (and_1_out, ~Stall, ~comparator_1_eq);  // AND_Gate
  or or_2 (or_2_out, or_3_out, and_1_out);
  \流水段寄存器  \u_流水段寄存器_1  (
    .CLR(or_3_out), .CLK(clk_t), .WE(or_2_out), .PC(IF_PC), .PCo(ID_PC), .IR(\指令存储器_data ),
    .IRo(\流水段寄存器_1_iro ));  // open: ALUctr, ALUctro, ALUASrc, ALUASrco, ALUBSrc, ALUBSrco, Halt, Halto, BandJ, BandJo, MemOp, MemOpo, MemWr, MemWro, RegWr, RegWro, MemtoReg, MemtoRego, RD, RDo, BusA, BusAo, RS1, RS1o, RS2, RS2o, Zero, Zeroo, BusB, BusBo, Imm, Result, PCTarget, Dout, Immo, Resulto, PCTargeto, Douto
  IDU idu_1 (
    .OpCode(idu_1_opcode), .RegWr(\流水段寄存器_4_regwro ), .Imm(idu_1_imm), .Funct3(idu_1_funct3),
    .Funct7(idu_1_funct7), .CLK(clk_t), .IR(\流水段寄存器_1_iro ), .BusW(WB_BusW), .BusA(idu_1_busa),
    .BusB(idu_1_busb), .ExtOp(\控制器_1_extop ), .Rd(idu_1_rd), .Rs1(idu_1_rs1), .Rs2(idu_1_rs2),
    .WB_Rd(\流水段寄存器_4_rdo ), .x10(out_16));
  \控制器  \u_控制器_1  (
    .opcode(idu_1_opcode), .ExtOp(\控制器_1_extop ), .RegWr(\控制器_1_regwr ), .BandJ(\控制器_1_bandj ),
    .funct3(idu_1_funct3), .ALUASrc(\控制器_1_aluasrc ), .ALUBSrc(\控制器_1_alubsrc ), .ALUctr(\控制器_1_aluctr ),
    .funct7(idu_1_funct7), .MemtoReg(\控制器_1_memtoreg ), .MemOp(\控制器_1_memop ), .MemWr(\控制器_1_memwr ),
    .Stall(Stall));  // open: Halt
  Comparator #(.width(32), .mode("unsigned")) comparator_1 (
    .a(32'hdead10cc), .b(\流水段寄存器_1_iro ), .eq(comparator_1_eq));  // open: gt, lt
  \阻塞检测  \u_阻塞检测_1  (
    .EX_MemtoReg(\流水段寄存器_2_memtorego ), .EX_rd(\流水段寄存器_2_rdo ), .Stall(Stall), .IF_opcode(idu_1_opcode),
    .IF_rs1(idu_1_rs1), .IF_rs2(idu_1_rs2));
  // Probe on IF_PC
  // Probe on ID_PC
  // Probe on EX_PC
  // Probe on M_PC
  // Probe on WB_PC
  \流水段寄存器  \u_流水段寄存器_2  (
    .ALUctr(\控制器_1_aluctr ), .ALUctro(\流水段寄存器_2_aluctro ), .CLR(or_3_out), .ALUASrc(\控制器_1_aluasrc ),
    .ALUASrco(\流水段寄存器_2_aluasrco ), .CLK(clk_t), .ALUBSrc(\控制器_1_alubsrc ), .ALUBSrco(\流水段寄存器_2_alubsrco ),
    .WE(1'b1), .Halt(comparator_1_eq), .Halto(\流水段寄存器_2_halto ), .BandJ(\控制器_1_bandj ),
    .BandJo(\流水段寄存器_2_bandjo ), .PC(ID_PC), .MemOp(\控制器_1_memop ), .PCo(EX_PC), .MemOpo(\流水段寄存器_2_memopo ),
    .MemWr(\控制器_1_memwr ), .MemWro(\流水段寄存器_2_memwro ), .RegWr(\控制器_1_regwr ), .RegWro(\流水段寄存器_2_regwro ),
    .IR(\流水段寄存器_1_iro ), .MemtoReg(\控制器_1_memtoreg ), .IRo(\流水段寄存器_2_iro ), .MemtoRego(\流水段寄存器_2_memtorego ),
    .RD(idu_1_rd), .RDo(\流水段寄存器_2_rdo ), .BusA(idu_1_busa), .BusAo(\流水段寄存器_2_busao ), .RS1(idu_1_rs1),
    .RS1o(\流水段寄存器_2_rs1o ), .RS2(idu_1_rs2), .RS2o(\流水段寄存器_2_rs2o ), .BusB(idu_1_busb),
    .BusBo(\流水段寄存器_2_busbo ), .Imm(idu_1_imm), .Immo(\流水段寄存器_2_immo ));  // open: Zero, Zeroo, Result, PCTarget, Dout, Resulto, PCTargeto, Douto
  or or_3 (or_3_out, ReSet, PCSrc);
  // Probe on Cycles
  // Probe on out_10
  // Probe on out_11
  // Probe on out_12
  // Probe on out_13
  Multiplexer #(.select(2), .width(32), .enable("false")) multiplexer_1 (
    .in0(\流水段寄存器_2_busao ), .in1(\流水段寄存器_3_resulto ), .in2(WB_BusW), .out(multiplexer_1_out), .sel(BusAFW));  // open: in3
  Multiplexer #(.select(2), .width(32), .enable("false")) multiplexer_2 (
    .in0(\流水段寄存器_2_busbo ), .in1(\流水段寄存器_3_resulto ), .in2(WB_BusW), .out(multiplexer_2_out), .sel(BusBFW));  // open: in3
  // Probe on out_14
  // Probe on out_15
  \转发检测  \u_转发检测_1  (
    .EX_rs1(\流水段寄存器_2_rs1o ), .M_RegWr(\流水段寄存器_3_regwro ), .EX_rs2(\流水段寄存器_2_rs2o ), .M_rd(\流水段寄存器_3_rdo ),
    .WB_RegWr(\流水段寄存器_4_regwro ), .WB_rd(\流水段寄存器_4_rdo ), .BusAFW(BusAFW), .BusBFW(BusBFW));
  \跳转检测  \u_跳转检测_1  (.EX_BandJ(\流水段寄存器_2_bandjo ), .PCsrc(PCSrc), .EX_Zero(eu_1_zero), .EX_Result0(eu_1_result[0]));
  EU eu_1 (
    .ALUctr(\流水段寄存器_2_aluctro ), .ALUASrc(\流水段寄存器_2_aluasrco ), .ALUBSrc(\流水段寄存器_2_alubsrco ),
    .BandJ(\流水段寄存器_2_bandjo ), .PC(EX_PC), .BusA(multiplexer_1_out), .BusB(multiplexer_2_out),
    .Imm(\流水段寄存器_2_immo ), .PCTarget(eu_1_pctarget), .Result(eu_1_result), .Zero(eu_1_zero));
  Register #(.width(1), .trigger("falling"), .Select("low")) register_1 (
    .D(halt), .en(not_1_out), .Q(Stop), .clk(clk_t), .clr(ReSet));
  not not_1 (not_1_out, Stop);
  \流水段寄存器  \u_流水段寄存器_3  (
    .CLR(ReSet), .CLK(clk_t), .WE(1'b1), .Halt(\流水段寄存器_2_halto ), .Halto(\流水段寄存器_3_halto ),
    .BandJ(\流水段寄存器_2_bandjo ), .BandJo(\流水段寄存器_3_bandjo ), .PC(EX_PC), .MemOp(\流水段寄存器_2_memopo ), .PCo(M_PC),
    .MemOpo(\流水段寄存器_3_memopo ), .MemWr(\流水段寄存器_2_memwro ), .MemWro(\流水段寄存器_3_memwro ),
    .RegWr(\流水段寄存器_2_regwro ), .RegWro(\流水段寄存器_3_regwro ), .IR(\流水段寄存器_2_iro ),
    .MemtoReg(\流水段寄存器_2_memtorego ), .IRo(\流水段寄存器_3_iro ), .MemtoRego(\流水段寄存器_3_memtorego ),
    .RD(\流水段寄存器_2_rdo ), .RDo(\流水段寄存器_3_rdo ), .Zero(eu_1_zero), .BusB(multiplexer_2_out),
    .BusBo(\流水段寄存器_3_busbo ), .Result(eu_1_result), .Resulto(\流水段寄存器_3_resulto ));  // open: ALUctr, ALUctro, ALUASrc, ALUASrco, ALUBSrc, ALUBSrco, BusA, BusAo, RS1, RS1o, RS2, RS2o, Zeroo, Imm, PCTarget, Dout, Immo, PCTargeto, Douto
  Hex_Digit_Display hex_digit_display_1 (.value(WB_IR[27:24]));  // open: dp
  Hex_Digit_Display hex_digit_display_2 (.value(WB_IR[31:28]));  // open: dp
  Hex_Digit_Display hex_digit_display_3 (.value(WB_IR[23:20]));  // open: dp
  Hex_Digit_Display hex_digit_display_4 (.value(WB_IR[19:16]));  // open: dp
  Hex_Digit_Display hex_digit_display_5 (.value(WB_IR[11:8]));  // open: dp
  Hex_Digit_Display hex_digit_display_6 (.value(WB_IR[15:12]));  // open: dp
  DataRAM dataram_1 (
    .Addr(\流水段寄存器_3_resulto [17:0]), .Din(\流水段寄存器_3_busbo ), .CLK(clk_t), .CLR(ReSet),
    .WE(\流水段寄存器_3_memwro ), .MemOp(\流水段寄存器_3_memopo ), .DataOut(dataram_1_dataout));  // open: AlignErr
  Hex_Digit_Display hex_digit_display_7 (.value(WB_IR[3:0]));  // open: dp
  Hex_Digit_Display hex_digit_display_8 (.value(WB_IR[7:4]));  // open: dp
  \流水段寄存器  \u_流水段寄存器_4  (
    .CLR(ReSet), .CLK(clk_t), .WE(1'b1), .Halt(\流水段寄存器_3_halto ), .Halto(halt), .BandJ(\流水段寄存器_3_bandjo ),
    .BandJo(WB_BandJ), .PC(M_PC), .PCo(WB_PC), .RegWr(\流水段寄存器_3_regwro ), .RegWro(\流水段寄存器_4_regwro ),
    .IR(\流水段寄存器_3_iro ), .MemtoReg(\流水段寄存器_3_memtorego ), .IRo(WB_IR), .MemtoRego(\流水段寄存器_4_memtorego ),
    .RD(\流水段寄存器_3_rdo ), .RDo(\流水段寄存器_4_rdo ), .Result(\流水段寄存器_3_resulto ), .Dout(dataram_1_dataout),
    .Resulto(\流水段寄存器_4_resulto ), .Douto(\流水段寄存器_4_douto ));  // open: ALUctr, ALUctro, ALUASrc, ALUASrco, ALUBSrc, ALUBSrco, MemOp, MemOpo, MemWr, MemWro, BusA, BusAo, RS1, RS1o, RS2, RS2o, Zero, Zeroo, BusB, BusBo, Imm, PCTarget, Immo, PCTargeto
  Multiplexer #(.width(32), .enable("false")) multiplexer_3 (
    .in0(\流水段寄存器_4_resulto ), .in1(\流水段寄存器_4_douto ), .out(WB_BusW), .sel(\流水段寄存器_4_memtorego ));
  not not_2 (not_2_out, halt);
  // Probe on Cycles
  Counter #(.width(16), .max('hffff), .behavior("old")) \u_计数器  (
    .count(not_2_out), .Q(Cycles), .clk(clk_t), .clr(ReSet));  // open: load, D, carry, preset
  // Probe on out_10
  Counter #(.width(16), .max('hffff), .behavior("old")) \u_计数器_2  (
    .count(Stall), .Q(out_10), .clk(clk_t), .clr(ReSet));  // open: load, D, carry, preset
  // Probe on out_14
  Counter #(.width(16), .max('hffff), .behavior("old")) \u_计数器_3  (
    .count(or_4_out), .Q(out_14), .clk(clk_t), .clr(ReSet));  // open: load, D, carry, preset
  or or_4 (or_4_out, BusAFW[0], BusAFW[1]);
  // Probe on out_15
  Counter #(.width(16), .max('hffff), .behavior("old")) \u_计数器_4  (
    .count(or_5_out), .Q(out_15), .clk(clk_t), .clr(ReSet));  // open: load, D, carry, preset
  or or_5 (or_5_out, BusBFW[0], BusBFW[1]);
  Comparator #(.width(7), .mode("unsigned")) comparator_2 (
    .a(WB_IR[6:0]), .b(7'b1101111), .eq(comparator_2_eq));  // open: gt, lt
  Comparator #(.width(7), .mode("unsigned")) comparator_3 (
    .a(WB_IR[6:0]), .b(7'b1100111), .eq(comparator_3_eq));  // open: gt, lt
  Counter #(.width(16), .max('hffff), .behavior("old")) \u_计数器_5  (
    .count(or_6_out), .Q(out_12), .clk(clk_t), .clr(ReSet));  // open: load, D, carry, preset
  or or_6 (or_6_out, comparator_2_eq, comparator_3_eq);
  // Probe on out_12
  Counter #(.width(16), .max('hffff), .behavior("old")) \u_计数器_6  (
    .count(PCSrc), .Q(out_11), .clk(clk_t), .clr(ReSet));  // open: load, D, carry, preset
  Comparator #(.width(7), .mode("unsigned")) comparator_4 (
    .a(WB_IR[6:0]), .b(7'b1100011), .eq(comparator_4_eq));  // open: gt, lt
  or or_7 (or_7_out, WB_BandJ[0], WB_BandJ[1], WB_BandJ[2]);
  // Probe on out_11
  // Probe on out_13
  Counter #(.width(16), .max('hffff), .behavior("old")) \u_计数器_7  (
    .count(and_2_out), .Q(out_13), .clk(clk_t), .clr(ReSet));  // open: load, D, carry, preset
  and and_2 (and_2_out, comparator_4_eq, or_7_out);

  // Other names for the same wires on the sheet: BP_En = BPEn; RS1转发次数[15:0] = out_14; RS2转发次数[15:0] = out_15;
  //   x10[31:0] = out_16; 冲刷次数[15:0] = out_11; 分支指令数[15:0] = out_13; 总周期数[15:0] = Cycles; 跳转指令数[15:0] = out_12;
  //   阻塞次数[15:0] = out_10

  // Notes on the sheet:
  //   断点调试
  //   输入引脚
  //   contents of 指令存储器 (hex, n*v repeats v):
  //   93 113 193 213 293 313 393 413 493 513 593 613 693 713 793 813 893 913 993 a13 a93 b13 b93 c13 c93
  //   d13 d93 e13 e93 f13 f93 2097 f8408093 aa0137 aa10113 20a023 a703 aa03b7 aa38393 200193 46771063 2097
  //   f5c08093 aa00b137 a0010113 20a223 40a703 aa00b3b7 a0038393 300193 42771c63 2097 f3408093 aa01137
  //   aa010113 20a423 80a703 aa013b7 aa038393 400193 40771863 2097 f0c08093 a00aa137 a10113 20a623 c0a703
  //   a00aa3b7 a38393 500193 3e771463 2097 f0008093 aa0137 aa10113 fe20aa23 ff40a703 aa03b7 aa38393 600193
  //   3c771063 2097 ed808093 aa00b137 a0010113 fe20ac23 ff80a703 aa00b3b7 a0038393 700193 38771c63 2097
  //   eb008093 aa01137 aa010113 fe20ae23 ffc0a703 aa013b7 aa038393 800193 36771863 2097 e8808093 a00aa137
  //   a10113 20a023 a703 a00aa3b7 a38393 900193 34771463 2097 e6408093 12345137 67810113 fe008213 2222023
  //   a283 123453b7 67838393 a00193 30729e63 2097 e3808093 58213137 9810113 ffd08093 20a3a3 2217 e2420213
  //   22283 582133b7 9838393 b00193 2e729463 c00193 213 aabbd0b7 cdd08093 2117 dd410113 112023 12703
  //   aabbd3b7 cdd38393 2a771e63 120213 200293 fc521ae3 d00193 213 daabc0b7 ccd08093 2117 d9c10113 13
  //   112223 412703 daabc3b7 ccd38393 28771063 120213 200293 fc5218e3 e00193 213 ddaac0b7 bcc08093 2117
  //   d6010113 13 13 112423 812703 ddaac3b7 bcc38393 24771063 120213 200293 fc5216e3 f00193 213 cddab0b7
  //   bbc08093 13 2117 d1c10113 112623 c12703 cddab3b7 bbc38393 20771263 120213 200293 fc5218e3 1000193
  //   213 ccddb0b7 abb08093 13 2117 ce010113 13 112823 1012703 ccddb3b7 abb38393 1c771263 120213 200293
  //   fc5216e3 1100193 213 bccde0b7 aab08093 13 13 2117 c9c10113 112a23 1412703 bccde3b7 aab38393 18771263
  //   120213 200293 fc5216e3 1200193 213 2117 c6c10113 1120b7 23308093 112023 12703 1123b7 23338393
  //   14771663 120213 200293 fc521ae3 1300193 213 2117 c3410113 300110b7 22308093 13 112223 412703
  //   300113b7 22338393 10771863 120213 200293 fc5218e3 1400193 213 2117 bf810113 330010b7 12208093 13 13
  //   112423 812703 330013b7 12238393 c771863 120213 200293 fc5216e3 1500193 213 2117 bb810113 13 233000b7
  //   11208093 112623 c12703 233003b7 11238393 8771a63 120213 200293 fc5218e3 1600193 213 2117 b7c10113 13
  //   223300b7 1108093 13 112823 1012703 223303b7 1138393 4771a63 120213 200293 fc5216e3 1700193 213 2117
  //   b3c10113 13 13 122330b7 108093 112a23 1412703 122333b7 138393 771a63 120213 200293 fc5216e3 301863
  //   deade537 ead50513 dead10cc c10537 fee50513 dead10cc c0001073
  //   输出引脚
  //   请勿修改引脚名称、电路名称及电路封装外观
  //   为方便调试，需要输出流水线各段保存的PC值、时钟周期数、冒险处理次数、分支与跳转指令执行数等信息
  //   流水调试日志
  //   程序运行分析
  //   程序执行结束
  //   数码管输出
endmodule

module \跳转检测  (
  input  [2:0] EX_BandJ,
  input  EX_Zero,
  input  EX_Result0,
  output PCsrc
);

  wire not_1_out, or_1_out;

  not not_1 (not_1_out, EX_Zero);
  or or_1 (or_1_out, ~EX_Result0, EX_Zero);  // OR_Gate
  Multiplexer #(.select(3), .enable("false")) multiplexer_1 (
    .in0(1'b0), .in1(1'b1), .in2(1'b1), .in4(EX_Zero), .in5(not_1_out), .in6(EX_Result0), .in7(or_1_out),
    .out(PCsrc), .sel(EX_BandJ));  // open: in3

  // Notes on the sheet:
  //   EX_BandJ: pull=down
  //   EX_Zero: pull=down
  //   输入信号
  //   请勿修改引脚名称、电路名称及电路封装外观
  //   不要修改控制信号的编码定义、引脚名称和在布局中的位置。
  //   输出信号
endmodule

module IFU (
  input  Reset,
  input  BPEn,
  input  PCSrc,
  input  Stall,
  input  [31:0] Initial_Address,
  input  [31:0] BP_PC,
  input  [31:0] PCTarget,
  input  CLK,
  input  halt,
  output [31:0] PC
);

  wire and_1_out, and_2_out, comparator_1_eq, or_1_out, or_2_out;
  wire [31:0] adder_1_out, multiplexer_1_out, multiplexer_2_out;

  Adder #(.width(32)) adder_1 (.a(PC), .b(32'h4), .out(adder_1_out));  // open: cin, cout
  Comparator #(.width(32), .mode("unsigned")) comparator_1 (.a(PC), .b(BP_PC), .eq(comparator_1_eq));  // open: gt, lt
  Multiplexer #(.width(32), .enable("false")) multiplexer_1 (
    .in0(adder_1_out), .in1(PCTarget), .out(multiplexer_1_out), .sel(PCSrc));
  Multiplexer #(.width(32), .enable("false")) multiplexer_2 (
    .in0(multiplexer_1_out), .in1(Initial_Address), .out(multiplexer_2_out), .sel(Reset));
  or or_1 (or_1_out, and_1_out, PCSrc, Reset);
  and and_1 (and_1_out, ~and_2_out, ~or_2_out);  // AND_Gate
  and and_2 (and_2_out, comparator_1_eq, BPEn);
  or or_2 (or_2_out, halt, Stall);
  Register #(.width(32), .trigger("falling"), .Select("high")) register_1 (
    .D(multiplexer_2_out), .en(or_1_out), .Q(PC), .clk(CLK), .cs(1'b1));  // open: clr, preset

  // Other names for the same wires on the sheet: BP_En = BPEn; Init_Addr[31:0] = Initial_Address

  // Notes on the sheet:
  //   PCSrc: pull=down
  //   Stall: pull=down
  //   PCTarget: pull=down
  //   断点调试
  //   输入信号
  //   请勿修改引脚名称、电路名称及电路封装外观
  //   指令存储器256KB，数据位为32位，地址位为16位。PC寄存器数据宽度32位，片选信号高电平有效
  //   输出信号
endmodule

module IDU (
  input  [2:0] ExtOp,
  input  RegWr,
  input  [4:0] WB_Rd,
  input  [31:0] IR,
  input  [31:0] BusW,
  input  CLK,
  output [6:0] OpCode,
  output [2:0] Funct3,
  output [6:0] Funct7,
  output [31:0] Imm,
  output [31:0] BusA,
  output [31:0] BusB,
  output [31:0] x10,
  output [4:0] Rd,
  output [4:0] Rs1,
  output [4:0] Rs2
);

  \立即数扩展器  \u_立即数扩展器_1  (.Instr(IR), .Extop(ExtOp), .imm(Imm));
  RegFile regfile_1 (
    .R1_num(IR[24:20]), .R2_num(IR[19:15]), .Write_Reg_num(WB_Rd), .Write_Enable(RegWr), .Clock(CLK),
    .Din(BusW), .Reg1Out(BusB), .Reg2Out(BusA), .x10(x10));

  assign Funct3 = IR[14:12];
  assign Funct7 = IR[31:25];
  assign OpCode = IR[6:0];
  assign Rd = IR[11:7];
  assign Rs1 = IR[19:15];
  assign Rs2 = IR[24:20];

  // Other names for the same wires on the sheet: op[6:0] = IR[6:0]

  // Notes on the sheet:
  //   ExtOp: pull=down
  //   RegWr: pull=down
  //   WB_Rd: pull=down
  //   BusW: pull=down
  //   输入信号
  //   为了后续实验中的引用，不要修改ExtOP编码定义。
  //   请勿修改引脚名称、电路名称及电路封装外观
  //   修改寄存器堆电路设计，0号寄存器始终为0。
  //   输出信号
endmodule

module \控制器_无stall  (
  input  [6:0] opcode,
  input  [2:0] funct3,
  input  [6:0] funct7,
  output [2:0] ExtOp,
  output RegWr,
  output [2:0] BandJ,
  output ALUASrc,
  output [1:0] ALUBSrc,
  output [3:0] ALUctr,
  output MemtoReg,
  output [2:0] MemOp,
  output MemWr,
  output Halt
);

  wire actr1, actr2, and_2_out, auipc, Br, ext1, ext2, I_Ar, jal, jalr, lui, nor_3_out, nor_4_out, nor_5_out,
       or_6_out, or_10_out, R;
  wire [2:0] nor_2_out;
  wire [3:3] multiplexer_2_out;

  or or_1 (RegWr, lui, auipc, I_Ar, MemtoReg, R, jal, jalr);
  assign ExtOp = ext1 ? 3'b001 : 3'bz;  // Controlled_Buffer controlled_buffer_1
  or or_2 (ext1, lui, auipc);
  assign ALUctr = actr1 ? 4'b0000 : 4'bz;  // Controlled_Buffer controlled_buffer_2
  or or_3 (actr1, auipc, jal, jalr, MemtoReg, MemWr);
  Comparator #(.width(7), .mode("unsigned")) comparator_1 (.a(opcode), .b(7'b0110111), .eq(lui));  // open: gt, lt
  Comparator #(.width(7), .mode("unsigned")) comparator_2 (.a(opcode), .b(7'b1100011), .eq(Br));  // open: gt, lt
  Comparator #(.width(7), .mode("unsigned")) comparator_3 (.a(opcode), .b(7'b0010111), .eq(auipc));  // open: gt, lt
  Comparator #(.width(7), .mode("unsigned")) comparator_4 (.a(opcode), .b(7'b0000011), .eq(MemtoReg));  // open: gt, lt
  or or_4 (ALUASrc, auipc, jal, jalr);
  assign ExtOp = ext2 ? 3'b000 : 3'bz;  // Controlled_Buffer controlled_buffer_3
  or or_5 (ext2, I_Ar, MemtoReg, jalr);
  assign ALUctr = lui ? 4'b1111 : 4'bz;  // Controlled_Buffer controlled_buffer_4
  Comparator #(.width(7), .mode("unsigned")) comparator_5 (.a(opcode), .b(7'b0010011), .eq(I_Ar));  // open: gt, lt
  Comparator #(.width(7), .mode("unsigned")) comparator_6 (.a(opcode), .b(7'b0100011), .eq(MemWr));  // open: gt, lt
  nor nor_1 (nor_2_out[2], funct3[2], funct3[1]);
  Multiplexer #(.width(3), .enable("false")) multiplexer_1 (.in0(3'b000), .in1(nor_2_out), .out(MemOp), .sel(or_6_out));
  or or_6 (or_6_out, MemtoReg, MemWr);
  nor nor_2 (nor_2_out[0], funct3[0], funct3[1]);
  and and_1 (nor_2_out[1], funct3[0], ~funct3[1]);  // AND_Gate
  or or_7 (ALUBSrc[0], jal, jalr);
  assign BandJ = Br ? {Br, funct3[2], funct3[0]} : 3'bz;  // Controlled_Buffer controlled_buffer_5
  assign ExtOp = jal ? 3'b100 : 3'bz;  // Controlled_Buffer controlled_buffer_6
  assign ALUctr = Br ? {3'b001, funct3[1]} : 4'bz;  // Controlled_Buffer controlled_buffer_7
  Comparator #(.width(7), .mode("unsigned")) comparator_7 (.a(opcode), .b(7'b0110011), .eq(R));  // open: gt, lt
  Comparator #(.width(7), .mode("unsigned")) comparator_8 (.a(opcode), .b(7'b1110011), .eq(Halt));  // open: gt, lt
  assign BandJ = jalr ? 3'b010 : 3'bz;  // Controlled_Buffer controlled_buffer_8
  assign ExtOp = Br ? 3'b011 : 3'bz;  // Controlled_Buffer controlled_buffer_9
  Comparator #(.width(7), .mode("unsigned")) comparator_9 (.a(opcode), .b(7'b1101111), .eq(jal));  // open: gt, lt
  or or_8 (ALUBSrc[1], lui, auipc, I_Ar, MemtoReg, MemWr);
  assign BandJ = jal ? 3'b001 : 3'bz;  // Controlled_Buffer controlled_buffer_10
  assign ExtOp = MemWr ? 3'b010 : 3'bz;  // Controlled_Buffer controlled_buffer_11
  assign ALUctr = actr2 ? {multiplexer_2_out[3], funct3} : 4'bz;  // Controlled_Buffer controlled_buffer_12
  Multiplexer #(.enable("false")) multiplexer_2 (
    .in0(1'b0), .in1(funct7[5]), .out(multiplexer_2_out[3]), .sel(or_10_out));
  or or_9 (actr2, I_Ar, R);
  or or_10 (or_10_out, and_2_out, R);
  and and_2 (and_2_out, I_Ar, ~funct3[1], funct3[0]);  // AND_Gate
  Comparator #(.width(7), .mode("unsigned")) comparator_10 (.a(opcode), .b(7'b1100111), .eq(jalr));  // open: gt, lt
  nor nor_3 (nor_3_out, Br, jalr, jal);
  assign BandJ = nor_3_out ? 3'b000 : 3'bz;  // Controlled_Buffer controlled_buffer_13
  assign ExtOp = nor_4_out ? 3'b000 : 3'bz;  // Controlled_Buffer controlled_buffer_14
  nor nor_4 (nor_4_out, ext1, ext2, jal, Br, MemWr);
  assign ALUctr = nor_5_out ? 4'b0000 : 4'bz;  // Controlled_Buffer controlled_buffer_15
  nor nor_5 (nor_5_out, actr1, lui, Br, actr2);

  // Other names for the same wires on the sheet: I_l = MemtoReg; St = MemWr

  // Notes on the sheet:
  //   输入引脚
  //   请勿修改引脚名称、电路名称及电路封装外观
  //   提示：根据指令种类，把7位指令code用一位指令类型标志位来表示，再通过功能码来区分具体指令，生成控制信号。
  //   输出引脚
endmodule

module \控制器  (
  input  [6:0] opcode,
  input  [2:0] funct3,
  input  [6:0] funct7,
  input  Stall,
  output [2:0] ExtOp,
  output RegWr,
  output [2:0] BandJ,
  output ALUASrc,
  output [1:0] ALUBSrc,
  output [3:0] ALUctr,
  output MemtoReg,
  output [2:0] MemOp,
  output MemWr,
  output Halt
);

  wire actr1, actr2, and_3_out, and_4_out, and_7_out, and_8_out, and_9_out, and_10_out, and_13_out,
       and_14_out, and_15_out, and_16_out, and_17_out, and_19_out, and_20_out, and_21_out, auipc, Br, ext1,
       ext2, I_Ar, I_l, jal, jalr, lui, nor_3_out, nor_4_out, nor_5_out, or_1_out, or_4_out, or_6_out,
       or_7_out, or_8_out, or_9_out, or_11_out, or_12_out, or_13_out, R, St;
  wire [2:0] nor_2_out;
  wire [3:3] multiplexer_2_out;

  and and_1 (RegWr, or_1_out, ~Stall);  // AND_Gate
  or or_1 (or_1_out, lui, auipc, I_Ar, I_l, R, jal, jalr);
  and and_2 (MemtoReg, I_l, ~Stall);  // AND_Gate
  assign ExtOp = and_3_out ? 3'b001 : 3'bz;  // Controlled_Buffer controlled_buffer_1
  and and_3 (and_3_out, ~Stall, ext1);  // AND_Gate
  or or_2 (ext1, lui, auipc);
  assign ALUctr = and_4_out ? 4'b0000 : 4'bz;  // Controlled_Buffer controlled_buffer_2
  and and_4 (and_4_out, ~Stall, actr1);  // AND_Gate
  or or_3 (actr1, auipc, jal, jalr, I_l, St);
  Comparator #(.width(7), .mode("unsigned")) comparator_1 (.a(opcode), .b(7'b0110111), .eq(lui));  // open: gt, lt
  Comparator #(.width(7), .mode("unsigned")) comparator_2 (.a(opcode), .b(7'b1100011), .eq(Br));  // open: gt, lt
  and and_5 (ALUASrc, or_4_out, ~Stall);  // AND_Gate
  Comparator #(.width(7), .mode("unsigned")) comparator_3 (.a(opcode), .b(7'b0010111), .eq(auipc));  // open: gt, lt
  Comparator #(.width(7), .mode("unsigned")) comparator_4 (.a(opcode), .b(7'b0000011), .eq(I_l));  // open: gt, lt
  or or_4 (or_4_out, auipc, jal, jalr);
  and and_6 (MemWr, St, ~Stall);  // AND_Gate
  assign ExtOp = and_7_out ? 3'b000 : 3'bz;  // Controlled_Buffer controlled_buffer_3
  and and_7 (and_7_out, ~Stall, ext2);  // AND_Gate
  or or_5 (ext2, I_Ar, I_l, jalr);
  assign ALUctr = and_8_out ? 4'b1111 : 4'bz;  // Controlled_Buffer controlled_buffer_4
  and and_8 (and_8_out, ~Stall, lui);  // AND_Gate
  Comparator #(.width(7), .mode("unsigned")) comparator_5 (.a(opcode), .b(7'b0010011), .eq(I_Ar));  // open: gt, lt
  Comparator #(.width(7), .mode("unsigned")) comparator_6 (.a(opcode), .b(7'b0100011), .eq(St));  // open: gt, lt
  assign ExtOp = and_9_out ? 3'b100 : 3'bz;  // Controlled_Buffer controlled_buffer_5
  and and_9 (and_9_out, ~Stall, jal);  // AND_Gate
  assign ALUctr = and_10_out ? {3'b001, funct3[1]} : 4'bz;  // Controlled_Buffer controlled_buffer_6
  and and_10 (and_10_out, ~Stall, Br);  // AND_Gate
  nor nor_1 (nor_2_out[2], funct3[2], funct3[1]);
  nor nor_2 (nor_2_out[0], funct3[0], funct3[1]);
  and and_11 (nor_2_out[1], funct3[0], ~funct3[1]);  // AND_Gate
  or or_6 (or_6_out, jal, jalr);
  and and_12 (ALUBSrc[0], or_6_out, ~Stall);  // AND_Gate
  and and_13 (and_13_out, Br, ~Stall);  // AND_Gate
  assign BandJ = and_13_out ? {Br, funct3[2], funct3[0]} : 3'bz;  // Controlled_Buffer controlled_buffer_7
  assign ExtOp = and_14_out ? 3'b011 : 3'bz;  // Controlled_Buffer controlled_buffer_8
  and and_14 (and_14_out, ~Stall, Br);  // AND_Gate
  Multiplexer #(.width(3), .enable("false")) multiplexer_1 (
    .in0(3'b000), .in1(nor_2_out), .out(MemOp), .sel(and_15_out));
  and and_15 (and_15_out, or_7_out, ~Stall);  // AND_Gate
  or or_7 (or_7_out, I_l, St);
  Comparator #(.width(7), .mode("unsigned")) comparator_7 (.a(opcode), .b(7'b0110011), .eq(R));  // open: gt, lt
  Comparator #(.width(7), .mode("unsigned")) comparator_8 (.a(opcode), .b(7'b1110011), .eq(Halt));  // open: gt, lt
  and and_16 (and_16_out, jalr, ~Stall);  // AND_Gate
  assign BandJ = and_16_out ? 3'b010 : 3'bz;  // Controlled_Buffer controlled_buffer_9
  and and_17 (and_17_out, I_Ar, ~funct3[1], funct3[0]);  // AND_Gate
  Comparator #(.width(7), .mode("unsigned")) comparator_9 (.a(opcode), .b(7'b1101111), .eq(jal));  // open: gt, lt
  or or_8 (or_8_out, lui, auipc, I_Ar, I_l, St);
  and and_18 (ALUBSrc[1], or_8_out, ~Stall);  // AND_Gate
  and and_19 (and_19_out, jal, ~Stall);  // AND_Gate
  assign BandJ = and_19_out ? 3'b001 : 3'bz;  // Controlled_Buffer controlled_buffer_10
  assign ExtOp = and_20_out ? 3'b010 : 3'bz;  // Controlled_Buffer controlled_buffer_11
  and and_20 (and_20_out, ~Stall, St);  // AND_Gate
  Multiplexer #(.enable("false")) multiplexer_2 (
    .in0(1'b0), .in1(funct7[5]), .out(multiplexer_2_out[3]), .sel(or_9_out));
  assign ALUctr = and_21_out ? {multiplexer_2_out[3], funct3} : 4'bz;  // Controlled_Buffer controlled_buffer_12
  and and_21 (and_21_out, ~Stall, actr2);  // AND_Gate
  or or_9 (or_9_out, and_17_out, R);
  or or_10 (actr2, I_Ar, R);
  Comparator #(.width(7), .mode("unsigned")) comparator_10 (.a(opcode), .b(7'b1100111), .eq(jalr));  // open: gt, lt
  assign ExtOp = or_11_out ? 3'b000 : 3'bz;  // Controlled_Buffer controlled_buffer_13
  or or_11 (or_11_out, Stall, nor_3_out);
  nor nor_3 (nor_3_out, ext1, ext2, St, jal, Br);
  nor nor_4 (nor_4_out, jalr, Br, jal);
  or or_12 (or_12_out, nor_4_out, Stall);
  assign BandJ = or_12_out ? 3'b000 : 3'bz;  // Controlled_Buffer controlled_buffer_14
  assign ALUctr = or_13_out ? 4'b0000 : 4'bz;  // Controlled_Buffer controlled_buffer_15
  or or_13 (or_13_out, Stall, nor_5_out);
  nor nor_5 (nor_5_out, actr1, lui, Br, actr2);

  // Notes on the sheet:
  //   输入引脚
  //   请勿修改引脚名称、电路名称及电路封装外观
  //   提示：根据指令种类，把7位指令code用一位指令类型标志位来表示，再通过功能码来区分具体指令，生成控制信号。
  //   输出引脚
endmodule

module RegFile (
  input  [4:0] R1_num,
  input  [4:0] R2_num,
  input  [4:0] Write_Reg_num,
  input  [31:0] Din,
  input  Write_Enable,
  input  Clock,
  output [31:0] x10,
  output [31:0] Reg1Out,
  output [31:0] Reg2Out
);

  wire and_1_out, and_2_out, and_3_out, and_4_out, and_5_out, and_6_out, and_7_out, and_8_out, and_9_out,
       and_10_out, and_11_out, and_12_out, and_13_out, and_14_out, and_15_out, and_16_out, and_17_out,
       and_18_out, and_19_out, and_20_out, and_21_out, and_22_out, and_23_out, and_24_out, and_25_out,
       and_26_out, and_27_out, and_28_out, and_29_out, and_30_out, and_31_out, decoder_1_out1,
       decoder_1_out2, decoder_1_out3, decoder_1_out4, decoder_1_out5, decoder_1_out6, decoder_1_out7,
       decoder_1_out8, decoder_1_out9, decoder_1_out10, decoder_1_out11, decoder_1_out12, decoder_1_out13,
       decoder_1_out14, decoder_1_out15, decoder_1_out16, decoder_1_out17, decoder_1_out18, decoder_1_out19,
       decoder_1_out20, decoder_1_out21, decoder_1_out22, decoder_1_out23, decoder_1_out24, decoder_1_out25,
       decoder_1_out26, decoder_1_out27, decoder_1_out28, decoder_1_out29, decoder_1_out30, decoder_1_out31;
  wire [31:0] _7_q, _25_q, register_1_q, register_2_q, register_3_q, register_4_q, register_5_q,
       register_6_q, register_7_q, register_8_q, register_9_q, register_10_q, register_11_q, register_12_q,
       register_13_q, register_14_q, register_15_q, register_16_q, register_17_q, register_18_q,
       register_19_q, register_20_q, register_21_q, register_22_q, register_23_q, register_24_q,
       register_25_q, register_26_q, register_27_q, x1_q, x3_q;

  Decoder #(.select(5), .enable("false")) decoder_1 (
    .out1(decoder_1_out1), .out2(decoder_1_out2), .out3(decoder_1_out3), .out4(decoder_1_out4),
    .out5(decoder_1_out5), .out6(decoder_1_out6), .out7(decoder_1_out7), .out8(decoder_1_out8),
    .out9(decoder_1_out9), .out10(decoder_1_out10), .out11(decoder_1_out11), .out12(decoder_1_out12),
    .out13(decoder_1_out13), .out14(decoder_1_out14), .out15(decoder_1_out15), .out16(decoder_1_out16),
    .out17(decoder_1_out17), .out18(decoder_1_out18), .out19(decoder_1_out19), .out20(decoder_1_out20),
    .out21(decoder_1_out21), .out22(decoder_1_out22), .out23(decoder_1_out23), .out24(decoder_1_out24),
    .out25(decoder_1_out25), .out26(decoder_1_out26), .out27(decoder_1_out27), .out28(decoder_1_out28),
    .out29(decoder_1_out29), .out30(decoder_1_out30), .out31(decoder_1_out31), .sel(Write_Reg_num));  // open: out0
  and and_1 (and_1_out, Write_Enable, decoder_1_out1);
  and and_2 (and_2_out, Write_Enable, decoder_1_out2);
  and and_3 (and_3_out, Write_Enable, decoder_1_out3);
  and and_4 (and_4_out, Write_Enable, decoder_1_out4);
  and and_5 (and_5_out, Write_Enable, decoder_1_out5);
  and and_6 (and_6_out, Write_Enable, decoder_1_out6);
  and and_7 (and_7_out, Write_Enable, decoder_1_out7);
  and and_8 (and_8_out, Write_Enable, decoder_1_out8);
  and and_9 (and_9_out, Write_Enable, decoder_1_out9);
  and and_10 (and_10_out, Write_Enable, decoder_1_out10);
  and and_11 (and_11_out, Write_Enable, decoder_1_out11);
  and and_12 (and_12_out, Write_Enable, decoder_1_out12);
  and and_13 (and_13_out, Write_Enable, decoder_1_out13);
  and and_14 (and_14_out, Write_Enable, decoder_1_out14);
  and and_15 (and_15_out, Write_Enable, decoder_1_out15);
  and and_16 (and_16_out, Write_Enable, decoder_1_out16);
  and and_17 (and_17_out, Write_Enable, decoder_1_out17);
  and and_18 (and_18_out, Write_Enable, decoder_1_out18);
  and and_19 (and_19_out, Write_Enable, decoder_1_out19);
  and and_20 (and_20_out, Write_Enable, decoder_1_out20);
  and and_21 (and_21_out, Write_Enable, decoder_1_out21);
  and and_22 (and_22_out, Write_Enable, decoder_1_out22);
  and and_23 (and_23_out, Write_Enable, decoder_1_out23);
  and and_24 (and_24_out, Write_Enable, decoder_1_out24);
  and and_25 (and_25_out, Write_Enable, decoder_1_out25);
  and and_26 (and_26_out, Write_Enable, decoder_1_out26);
  and and_27 (and_27_out, Write_Enable, decoder_1_out27);
  and and_28 (and_28_out, Write_Enable, decoder_1_out28);
  and and_29 (and_29_out, Write_Enable, decoder_1_out29);
  and and_30 (and_30_out, Write_Enable, decoder_1_out30);
  and and_31 (and_31_out, Write_Enable, decoder_1_out31);
  Register #(.width(32), .Select("low")) register_1 (.en(1'b0), .Q(register_1_q), .clk(Clock), .clr(1'b1));  // open: D
  Register #(.width(32), .Select("low")) x1 (.D(Din), .en(and_1_out), .Q(x1_q), .clk(Clock));  // open: clr
  Register #(.width(32), .Select("low")) register_2 (
    .D(Din), .en(and_2_out), .Q(register_2_q), .clk(Clock));  // open: clr
  Register #(.width(32), .Select("low")) x3 (.D(Din), .en(and_3_out), .Q(x3_q), .clk(Clock));  // open: clr
  Register #(.width(32), .Select("low")) register_3 (
    .D(Din), .en(and_4_out), .Q(register_3_q), .clk(Clock));  // open: clr
  Register #(.width(32), .Select("low")) register_4 (
    .D(Din), .en(and_5_out), .Q(register_4_q), .clk(Clock));  // open: clr
  Register #(.width(32), .Select("low")) register_5 (
    .D(Din), .en(and_6_out), .Q(register_5_q), .clk(Clock));  // open: clr
  Register #(.width(32), .Select("low")) _7 (.D(Din), .en(and_7_out), .Q(_7_q), .clk(Clock));  // open: clr
  Register #(.width(32), .Select("low")) register_6 (
    .D(Din), .en(and_8_out), .Q(register_6_q), .clk(Clock));  // open: clr
  Register #(.width(32), .Select("low")) register_7 (
    .D(Din), .en(and_9_out), .Q(register_7_q), .clk(Clock));  // open: clr
  Register #(.width(32), .Select("low")) u_x10 (.D(Din), .en(and_10_out), .Q(x10), .clk(Clock));  // open: clr
  Register #(.width(32), .Select("low")) register_8 (
    .D(Din), .en(and_11_out), .Q(register_8_q), .clk(Clock));  // open: clr
  Register #(.width(32), .Select("low")) register_9 (
    .D(Din), .en(and_12_out), .Q(register_9_q), .clk(Clock));  // open: clr
  Register #(.width(32), .Select("low")) register_10 (
    .D(Din), .en(and_13_out), .Q(register_10_q), .clk(Clock));  // open: clr
  Register #(.width(32), .Select("low")) register_11 (
    .D(Din), .en(and_14_out), .Q(register_11_q), .clk(Clock));  // open: clr
  Register #(.width(32), .Select("low")) register_12 (
    .D(Din), .en(and_15_out), .Q(register_12_q), .clk(Clock));  // open: clr
  Register #(.width(32), .Select("low")) register_13 (
    .D(Din), .en(and_16_out), .Q(register_13_q), .clk(Clock));  // open: clr
  Register #(.width(32), .Select("low")) register_14 (
    .D(Din), .en(and_17_out), .Q(register_14_q), .clk(Clock));  // open: clr
  Register #(.width(32), .Select("low")) register_15 (
    .D(Din), .en(and_18_out), .Q(register_15_q), .clk(Clock));  // open: clr
  Register #(.width(32), .Select("low")) register_16 (
    .D(Din), .en(and_19_out), .Q(register_16_q), .clk(Clock));  // open: clr
  Register #(.width(32), .Select("low")) register_17 (
    .D(Din), .en(and_20_out), .Q(register_17_q), .clk(Clock));  // open: clr
  Register #(.width(32), .Select("low")) register_18 (
    .D(Din), .en(and_21_out), .Q(register_18_q), .clk(Clock));  // open: clr
  Register #(.width(32), .Select("low")) register_19 (
    .D(Din), .en(and_22_out), .Q(register_19_q), .clk(Clock));  // open: clr
  Register #(.width(32), .Select("low")) register_20 (
    .D(Din), .en(and_23_out), .Q(register_20_q), .clk(Clock));  // open: clr
  Register #(.width(32), .Select("low")) register_21 (
    .D(Din), .en(and_24_out), .Q(register_21_q), .clk(Clock));  // open: clr
  Register #(.width(32), .Select("low")) _25 (.D(Din), .en(and_25_out), .Q(_25_q), .clk(Clock));  // open: clr
  Register #(.width(32), .Select("low")) register_22 (
    .D(Din), .en(and_26_out), .Q(register_22_q), .clk(Clock));  // open: clr
  Register #(.width(32), .Select("low")) register_23 (
    .D(Din), .en(and_27_out), .Q(register_23_q), .clk(Clock));  // open: clr
  Register #(.width(32), .Select("low")) register_24 (
    .D(Din), .en(and_28_out), .Q(register_24_q), .clk(Clock));  // open: clr
  Register #(.width(32), .Select("low")) register_25 (
    .D(Din), .en(and_29_out), .Q(register_25_q), .clk(Clock));  // open: clr
  Register #(.width(32), .Select("low")) register_26 (
    .D(Din), .en(and_30_out), .Q(register_26_q), .clk(Clock));  // open: clr
  Register #(.width(32), .Select("low")) register_27 (
    .D(Din), .en(and_31_out), .Q(register_27_q), .clk(Clock));  // open: clr
  Multiplexer #(.select(5), .width(32), .enable("false")) multiplexer_1 (
    .in0(register_1_q), .in1(x1_q), .in2(register_2_q), .in3(x3_q), .in4(register_3_q), .in5(register_4_q),
    .in6(register_5_q), .in7(_7_q), .in8(register_6_q), .in9(register_7_q), .in10(x10), .in11(register_8_q),
    .in12(register_9_q), .in13(register_10_q), .in14(register_11_q), .in15(register_12_q),
    .in16(register_13_q), .in17(register_14_q), .in18(register_15_q), .in19(register_16_q),
    .in20(register_17_q), .in21(register_18_q), .in22(register_19_q), .in23(register_20_q),
    .in24(register_21_q), .in25(_25_q), .in26(register_22_q), .in27(register_23_q), .in28(register_24_q),
    .in29(register_25_q), .in30(register_26_q), .in31(register_27_q), .out(Reg1Out), .sel(R1_num));
  Multiplexer #(.select(5), .width(32), .enable("false")) multiplexer_2 (
    .in0(register_1_q), .in1(x1_q), .in2(register_2_q), .in3(x3_q), .in4(register_3_q), .in5(register_4_q),
    .in6(register_5_q), .in7(_7_q), .in8(register_6_q), .in9(register_7_q), .in10(x10), .in11(register_8_q),
    .in12(register_9_q), .in13(register_10_q), .in14(register_11_q), .in15(register_12_q),
    .in16(register_13_q), .in17(register_14_q), .in18(register_15_q), .in19(register_16_q),
    .in20(register_17_q), .in21(register_18_q), .in22(register_19_q), .in23(register_20_q),
    .in24(register_21_q), .in25(_25_q), .in26(register_22_q), .in27(register_23_q), .in28(register_24_q),
    .in29(register_25_q), .in30(register_26_q), .in31(register_27_q), .out(Reg2Out), .sel(R2_num));

  // Other names for the same wires on the sheet: CLK = Clock; RA[4:0] = R1_num; RB[4:0] = R2_num; RDA[31:0] = Reg1Out;
  //   RDB[31:0] = Reg2Out; RW[4:0] = Write_Reg_num; WE = Write_Enable

  // Notes on the sheet:
  //   输入引脚
  //   请勿修改引脚名称、电路名称及电路封装外观
  //   提示：使用译码器、多路选择器和32位寄存器及逻辑门实现寄存器堆，禁止直接使用存储器组件。
  //   输出引脚
endmodule

module \立即数扩展器  (
  input  [31:0] Instr,
  input  [2:0] Extop,
  output [31:0] imm
);

  wire [11:0] bit_extender_4_out;
  wire [19:0] bit_extender_3_out;
  wire [26:0] bit_extender_2_out;
  wire [31:0] bit_extender_1_out;

  assign bit_extender_1_out = {{20{Instr[31]}}, Instr[31:20]};  // Bit_Extender bit_extender_1
  assign bit_extender_2_out = {{20{Instr[31]}}, Instr[31:25]};  // Bit_Extender bit_extender_2
  assign bit_extender_3_out = {{19{Instr[31]}}, Instr[31]};  // Bit_Extender bit_extender_3
  assign bit_extender_4_out = {{11{Instr[31]}}, Instr[31]};  // Bit_Extender bit_extender_4
  Multiplexer #(.select(3), .width(32), .enable("false")) multiplexer_1 (
    .in0(bit_extender_1_out), .in1({Instr[31:12], {12{1'b0}}}), .in2({bit_extender_2_out, Instr[11:7]}),
    .in3({bit_extender_3_out, Instr[7], Instr[30:25], Instr[11:8], 1'b0}),
    .in4({bit_extender_4_out, Instr[19:12], Instr[20], Instr[30:21], 1'b0}), .out(imm), .sel(Extop));  // open: in5, in6, in7

  // Notes on the sheet:
  //   Instr: pull=down
  //   Extop: pull=down
  //   输入引脚
  //   输出引脚
endmodule

module DataRAM (
  input  CLK,
  input  CLR,
  input  WE,
  input  [2:0] MemOp,
  input  [17:0] Addr,
  input  [31:0] Din,
  output AlignErr,
  output [31:0] DataOut
);

  wire decode_1_out_4, decode_1_out_5, decode_1_out_6, decode_1_out_7;
  wire [7:0] _0_data, _1_data, _2_data, _3_data, io_1_out_9, io_1_out_10, io_1_out_11, io_1_out_12;

  decode decode_1 (
    .Addr(Addr), .MemOp(MemOp), .AlignErr(AlignErr), .out_4(decode_1_out_4), .out_5(decode_1_out_5),
    .out_6(decode_1_out_6), .out_7(decode_1_out_7));
  io io_1 (
    .AlignErr(AlignErr), .MemOp(MemOp), .Addr(Addr), .DataOut(DataOut), .Din(Din), .out_9(io_1_out_9),
    .in_5(_0_data), .out_10(io_1_out_10), .in_6(_1_data), .out_11(io_1_out_11), .in_7(_2_data),
    .out_12(io_1_out_12), .in_8(_3_data));
  RAM #(.addrWidth(16), .bus("separate"), .Select("high"), .simpleMode("false")) _0 (
    .addr(Addr[17:2]), .din(io_1_out_9), .data(_0_data), .str(WE), .sel(decode_1_out_4), .clk(CLK), .clr(CLR));  // open: ld
  // Probe on _0_data
  RAM #(.addrWidth(16), .bus("separate"), .Select("high"), .simpleMode("false")) _1 (
    .addr(Addr[17:2]), .din(io_1_out_10), .data(_1_data), .str(WE), .sel(decode_1_out_5), .clk(CLK), .clr(CLR));  // open: ld
  // Probe on _1_data
  RAM #(.addrWidth(16), .bus("separate"), .Select("high"), .simpleMode("false")) _2 (
    .addr(Addr[17:2]), .din(io_1_out_11), .data(_2_data), .str(WE), .sel(decode_1_out_6), .clk(CLK), .clr(CLR));  // open: ld
  // Probe on _2_data
  RAM #(.addrWidth(16), .bus("separate"), .Select("high"), .simpleMode("false")) _3 (
    .addr(Addr[17:2]), .din(io_1_out_12), .data(_3_data), .str(WE), .sel(decode_1_out_7), .clk(CLK), .clr(CLR));  // open: ld
  // Probe on _3_data

  // Other names for the same wires on the sheet: Dout[31:0] = DataOut

  // Notes on the sheet:
  //   输入引脚
  //   请勿修改引脚名称、电路名称及电路封装外观
  //   为了后续实验中的引用，不要修改MemOp的编码定义、引脚名称和在布局中的位置。
  //   32位数据存储器，按字节分4片存储，可按照字节、半字和字进行存储；读取字节或半字时，支持0扩展和符号位扩展。
  //   输出引脚
endmodule

module ALU (
  input  [3:0] ALUctr,
  input  [31:0] A,
  input  [31:0] B,
  output Zero,
  output [31:0] S
);

  wire adder32_1_cf, adder32_1_of, adder32_1_sf, aluctrl_1_alctr, aluctrl_1_sftctr, aluctrl_1_sigctr,
       aluctrl_1_subctr, multiplexer_1_out, xor_3_out;
  wire [2:0] aluctrl_1_opctr;
  wire [31:0] adder32_1_s, and_1_out, bit_extender_1_out, bit_extender_2_out, or_1_out, shifter32_1_dataout,
       xor_1_out, xor_2_out;

  assign xor_1_out = B ^ bit_extender_1_out;  // XOR_Gate xor_1, 32 bits wide
  assign bit_extender_1_out = {{31{aluctrl_1_subctr}}, aluctrl_1_subctr};  // Bit_Extender bit_extender_1
  assign and_1_out = A & B;  // AND_Gate and_1, 32 bits wide
  assign or_1_out = A | B;  // OR_Gate or_1, 32 bits wide
  Adder32 adder32_1 (
    .CF(adder32_1_cf), .OF(adder32_1_of), .SF(adder32_1_sf), .ZF(Zero), .X(A), .Y(xor_1_out),
    .Cin(aluctrl_1_subctr), .S(adder32_1_s));  // open: Cout
  assign xor_2_out = A ^ B;  // XOR_Gate xor_2, 32 bits wide
  Shifter32 shifter32_1 (
    .DataIn(A), .shamt(B[4:0]), .L_R(aluctrl_1_sftctr), .A_L(aluctrl_1_alctr), .DataOut(shifter32_1_dataout));
  assign bit_extender_2_out = {{31{1'b0}}, multiplexer_1_out};  // Bit_Extender bit_extender_2
  Multiplexer #(.enable("false")) multiplexer_1 (
    .in0(adder32_1_cf), .in1(xor_3_out), .out(multiplexer_1_out), .sel(aluctrl_1_sigctr));
  xor xor_3 (xor_3_out, adder32_1_of, adder32_1_sf);
  Multiplexer #(.select(3), .width(32), .enable("false")) multiplexer_2 (
    .in0(adder32_1_s), .in1(and_1_out), .in2(or_1_out), .in3(xor_2_out), .in4(shifter32_1_dataout), .in5(B),
    .in6(bit_extender_2_out), .out(S), .sel(aluctrl_1_opctr));  // open: in7
  ALUctrl aluctrl_1 (
    .SUBctr(aluctrl_1_subctr), .SFTctr(aluctrl_1_sftctr), .SIGctr(aluctrl_1_sigctr), .ALctr(aluctrl_1_alctr),
    .OPctr(aluctrl_1_opctr), .ALUctr(ALUctr));
  // Probe on A
  // Probe on B
  // Probe on S

  // Other names for the same wires on the sheet: Result[31:0] = S

  // Notes on the sheet:
  //   A: pull=down
  //   B: pull=down
  //   ALUctr: pull=down
  //   输入引脚
  //   请勿修改引脚名称、电路名称及电路封装外观
  //   提示：使用32位并行加法器子电路、桶形移位器、ALU控制子电路实现32位ALU
  //   功能说明:32位ALU，输入32位操作数A、B，4位控制信号ALUctr，输出32位结果Reseult和1位Zero标志位
  //   输出引脚
  //   操作数和结果
endmodule

module ALUctrl (
  input  [3:0] ALUctr,
  output SUBctr,
  output SFTctr,
  output SIGctr,
  output ALctr,
  output [2:0] OPctr
);

  wire _3, _4, _5, _6, _7, _8, _15;

  Decoder #(.select(4), .enable("false")) decoder_1 (
    .out1(SFTctr), .out2(SIGctr), .out3(_3), .out4(_4), .out5(_5), .out6(_6), .out7(_7), .out8(_8),
    .out13(ALctr), .out15(_15), .sel(ALUctr));  // open: out0, out9, out10, out11, out12, out14
  or or_1 (SUBctr, SIGctr, _3, _8);
  or or_2 (OPctr[2], SFTctr, SIGctr, _3, _5, ALctr, _15);
  or or_3 (OPctr[1], SIGctr, _3, _4, _6);
  or or_4 (OPctr[0], _4, _7, _15);

  // Other names for the same wires on the sheet: _2 = SIGctr; _13 = ALctr; _1 = SFTctr; LRctr = SFTctr

  // Notes on the sheet:
  //   输入引脚
  //   输出引脚
endmodule

module Adder32 (
  input  Cin,
  input  [31:0] X,
  input  [31:0] Y,
  output CF,
  output Cout,
  output OF,
  output SF,
  output [31:0] S,
  output ZF
);

  wire adder16_2_c16, and_1_out, and_2_out;

  Adder16 adder16_1 (.X(X[31:16]), .Y(Y[31:16]), .C0(adder16_2_c16), .S(S[31:16]), .C16(Cout));  // open: Pg, Gg
  Adder16 adder16_2 (.X(X[15:0]), .Y(Y[15:0]), .C0(Cin), .S(S[15:0]), .C16(adder16_2_c16));  // open: Pg, Gg
  and and_1 (and_1_out, ~X[31], ~Y[31], S[31]);  // AND_Gate
  and and_2 (and_2_out, X[31], Y[31], ~S[31]);  // AND_Gate
  Comparator #(.width(32), .mode("unsigned")) comparator_1 (.a(S), .b({32{1'b0}}), .eq(ZF));  // open: gt, lt
  xor xor_1 (CF, Cout, Cin);
  or or_1 (OF, and_1_out, and_2_out);
  // Probe on X
  // Probe on Y
  // Probe on S

  assign SF = S[31];

  // Notes on the sheet:
  //   X: pull=down
  //   Y: pull=down
  //   Cin: pull=down
  //   输入引脚区
  //   输出引脚区
  //   请勿修改引脚名称、电路名称及电路封装外观
  //   提示：使用16位并行加法器子电路实现32位快速加法器
  //   功能说明:32位Adder  S=X+Y，Cout为最高位进位位，Cin为进位输入， S为和，溢出OF、进位CF、零ZF、符号SF。
  //   +
  //   =
  //   无符号加法
endmodule

// 移位器
module Shifter32 (
  input  [4:0] shamt,
  input  L_R,
  input  A_L,
  input  [31:0] DataIn,
  output [31:0] DataOut
);

  wire [0:0] multiplexer_1_out;
  wire [1:0] bit_extender_1_out, bit_extender_2_out, multiplexer_3_out, multiplexer_3_out_2,
       multiplexer_4_out;
  wire [3:0] bit_extender_3_out, bit_extender_4_out, multiplexer_6_out;
  wire [7:0] bit_extender_5_out, bit_extender_6_out, multiplexer_8_out;
  wire [15:0] bit_extender_7_out, bit_extender_8_out, multiplexer_9_out, multiplexer_9_out_2,
       multiplexer_10_out;
  wire [27:0] multiplexer_3_out_3;
  wire [31:0] multiplexer_5_out, multiplexer_7_out;
  wire [31:31] multiplexer_2_out;

  Multiplexer #(.enable("false")) multiplexer_1 (.in0(1'b0), .in1(DataIn[31]), .out(multiplexer_1_out[0]), .sel(A_L));
  Multiplexer #(.enable("false")) multiplexer_2 (.in0(1'b0), .in1(DataIn[31]), .out(multiplexer_2_out[31]), .sel(A_L));
  Multiplexer #(.select(2), .width(32), .enable("false")) multiplexer_3 (
    .in0(DataIn), .in1({multiplexer_2_out[31], DataIn[31:1]}), .in2(DataIn),
    .in3({DataIn[30:0], multiplexer_1_out[0]}),
    .out({multiplexer_3_out, multiplexer_3_out_3, multiplexer_3_out_2}), .sel({L_R, shamt[0]}));
  assign bit_extender_1_out = {{1{multiplexer_2_out[31]}}, multiplexer_2_out[31]};  // Bit_Extender bit_extender_1
  Multiplexer #(.width(2), .enable("false")) multiplexer_4 (
    .in0(bit_extender_2_out), .in1(multiplexer_3_out), .out(multiplexer_4_out), .sel(A_L));
  assign bit_extender_2_out = {{1{1'b0}}, 1'b0};  // Bit_Extender bit_extender_2
  assign bit_extender_3_out = {{2{bit_extender_1_out[1]}}, bit_extender_1_out};  // Bit_Extender bit_extender_3
  Multiplexer #(.select(2), .width(32), .enable("false")) multiplexer_5 (
    .in0({multiplexer_3_out, multiplexer_3_out_3, multiplexer_3_out_2}),
    .in1({bit_extender_1_out, multiplexer_3_out, multiplexer_3_out_3}),
    .in2({multiplexer_3_out, multiplexer_3_out_3, multiplexer_3_out_2}),
    .in3({multiplexer_3_out_3, multiplexer_3_out_2, multiplexer_4_out}), .out(multiplexer_5_out),
    .sel({L_R, shamt[1]}));
  Multiplexer #(.width(4), .enable("false")) multiplexer_6 (
    .in0(bit_extender_4_out), .in1(multiplexer_5_out[31:28]), .out(multiplexer_6_out), .sel(A_L));
  assign bit_extender_4_out = {{2{bit_extender_2_out[1]}}, bit_extender_2_out};  // Bit_Extender bit_extender_4
  Multiplexer #(.select(2), .width(32), .enable("false")) multiplexer_7 (
    .in0(multiplexer_5_out), .in1({bit_extender_3_out, multiplexer_5_out[31:4]}), .in2(multiplexer_5_out),
    .in3({multiplexer_5_out[27:0], multiplexer_6_out}), .out(multiplexer_7_out), .sel({L_R, shamt[2]}));
  assign bit_extender_5_out = {{4{bit_extender_3_out[3]}}, bit_extender_3_out};  // Bit_Extender bit_extender_5
  assign bit_extender_6_out = {{4{bit_extender_4_out[3]}}, bit_extender_4_out};  // Bit_Extender bit_extender_6
  Multiplexer #(.width(8), .enable("false")) multiplexer_8 (
    .in0(bit_extender_6_out), .in1(multiplexer_7_out[31:24]), .out(multiplexer_8_out), .sel(A_L));
  assign bit_extender_7_out = {{8{bit_extender_5_out[7]}}, bit_extender_5_out};  // Bit_Extender bit_extender_7
  Multiplexer #(.select(2), .width(32), .enable("false")) multiplexer_9 (
    .in0(multiplexer_7_out), .in1({bit_extender_5_out, multiplexer_7_out[31:8]}), .in2(multiplexer_7_out),
    .in3({multiplexer_7_out[23:0], multiplexer_8_out}), .out({multiplexer_9_out, multiplexer_9_out_2}),
    .sel({L_R, shamt[3]}));
  assign bit_extender_8_out = {{8{bit_extender_6_out[7]}}, bit_extender_6_out};  // Bit_Extender bit_extender_8
  Multiplexer #(.width(16), .enable("false")) multiplexer_10 (
    .in0(bit_extender_8_out), .in1(multiplexer_9_out), .out(multiplexer_10_out), .sel(A_L));
  Multiplexer #(.select(2), .width(32), .enable("false")) multiplexer_11 (
    .in0({multiplexer_9_out, multiplexer_9_out_2}), .in1({bit_extender_7_out, multiplexer_9_out}),
    .in2({multiplexer_9_out, multiplexer_9_out_2}), .in3({multiplexer_9_out_2, multiplexer_10_out}),
    .out(DataOut), .sel({L_R, shamt[4]}));

  // Other names for the same wires on the sheet: Din[31:0] = DataIn; Left_Right = L_R; Arth_Logic = A_L;
  //   Dout[31:0] = DataOut

  // Notes on the sheet:
  //   L/R,A/L: 00逻辑右移，01算术右移，10逻辑左移，11：循环左移
  //   输入引脚
  //   请勿修改引脚名称、电路名称及电路封装外观
  //   提示：使用多路选择器、逻辑门实现32位桶形移位器，禁止直接使用移位器组件。
  //   输出引脚
endmodule

module Adder16 (
  input  C0,
  input  [15:0] X,
  input  [15:0] Y,
  output C16,
  output Pg,
  output Gg,
  output [15:0] S
);

  wire C1, C2, C3, C4, G0, G1, G2, G3, P0, P1, P2, P3;

  CLA4 cla4_1 (.X(X[15:12]), .F(S[15:12]), .Cout(C16), .Y(Y[15:12]), .Pg(P3), .Cin(C3), .Gg(G3));
  CLA4 cla4_2 (.X(X[11:8]), .F(S[11:8]), .Y(Y[11:8]), .Pg(P2), .Cin(C2), .Gg(G2));  // open: Cout
  CLU4 clu4_1 (
    .P0(P0), .P1(P1), .P2(P2), .P3(P3), .C1(C1), .C3(C3), .G0(G0), .G1(G1), .G2(G2), .G3(G3), .C2(C2),
    .C4(C4), .C0(C0), .Pg(Pg), .Gg(Gg));
  CLA4 cla4_3 (.X(X[7:4]), .F(S[7:4]), .Y(Y[7:4]), .Pg(P1), .Cin(C1), .Gg(G1));  // open: Cout
  CLA4 cla4_4 (.X(X[3:0]), .F(S[3:0]), .Y(Y[3:0]), .Pg(P0), .Cin(C0), .Gg(G0));  // open: Cout
  // Probe on X
  // Probe on Y
  // Probe on S

  // Notes on the sheet:
  //   Y: pull=down
  //   X: pull=down
  //   C0: pull=down
  //   输入引脚区
  //   请勿修改引脚名称、电路名称及电路封装外观
  //   提示：使用4位先行进位加法器和CLU子电路实现16位并行加法器
  //   功能说明:16位Adder  S=X+Y，C16为最高位进位位，C0为进位输入， Pg、Gg为成组进位生成传递函数
  //   输出引脚区
  //   +
  //   =
  //   无符号加法
endmodule

module CLA4 (
  input  [3:0] X,
  input  [3:0] Y,
  input  Cin,
  output [3:0] F,
  output Cout,
  output Pg,
  output Gg
);

  wire C1, C2, C3, G0, G1, G2, G3, P0, P1, P2, P3;

  Hex_Digit_Display hex_digit_display_1 (.value(X));  // open: dp
  FA fa_1 (.A(X[3]), .F(F[3]), .B(Y[3]), .P(P3), .Cin(C3), .G(G3));
  Hex_Digit_Display hex_digit_display_2 (.value(Y));  // open: dp
  FA fa_2 (.A(X[2]), .F(F[2]), .B(Y[2]), .P(P2), .Cin(C2), .G(G2));
  Hex_Digit_Display hex_digit_display_3 (.value(F));  // open: dp
  CLU4 clu4_1 (
    .P0(P0), .P1(P1), .P2(P2), .P3(P3), .C1(C1), .C3(C3), .G0(G0), .G1(G1), .G2(G2), .G3(G3), .C2(C2),
    .C4(Cout), .C0(Cin), .Pg(Pg), .Gg(Gg));
  FA fa_3 (.A(X[1]), .F(F[1]), .B(Y[1]), .P(P1), .Cin(C1), .G(G1));
  FA fa_4 (.A(X[0]), .F(F[0]), .B(Y[0]), .P(P0), .Cin(Cin), .G(G0));

  // Other names for the same wires on the sheet: C4 = Cout; Z[3:0] = F

  // Notes on the sheet:
  //   +
  //   =
  //   输出
  //   输入
  //   请勿修改引脚名称、电路名称及电路封装外观
  //   提示：使用全加器和CLU子电路实现四位先行进位加法器CLA4
endmodule

module CLU4 (
  input  P0,
  input  P1,
  input  P2,
  input  P3,
  input  G0,
  input  G1,
  input  G2,
  input  G3,
  input  C0,
  output C1,
  output C3,
  output C2,
  output C4,
  output Pg,
  output Gg
);

  wire and_1_out, and_2_out, and_3_out, and_4_out, and_6_out, and_7_out, and_8_out, or_5_out, or_6_out;

  and and_1 (and_1_out, C0, P0);
  and and_2 (and_2_out, C1, P1);
  and and_3 (and_3_out, C2, P2);
  and and_4 (and_4_out, C3, P3);
  or or_1 (C1, and_1_out, G0);
  or or_2 (C2, and_2_out, G1);
  or or_3 (C3, and_3_out, G2);
  or or_4 (C4, and_4_out, G3);
  and and_5 (Pg, P0, P1, P2, P3);
  and and_6 (and_6_out, P1, G0);
  or or_5 (or_5_out, and_6_out, G1);
  and and_7 (and_7_out, or_5_out, P2);
  or or_6 (or_6_out, and_7_out, G2);
  and and_8 (and_8_out, or_6_out, P3);
  or or_7 (Gg, and_8_out, G3);

  // Notes on the sheet:
  //   输入引脚
  //   请勿修改引脚名称、电路名称及电路封装外观
  //   提示：使用逻辑门电路实现4位四位先行进位部件CLU，Pg、Gg为成组进位生成传递函数
  //   输出引脚
endmodule

module FA (
  input  A,
  input  B,
  input  Cin,
  output F,
  output P,
  output G
);

  xor xor_1 (F, Cin, B, A);
  or or_1 (P, B, A);
  and and_1 (G, B, A);

  // Notes on the sheet:
  //   输入引脚
  //   请勿修改引脚名称、电路名称及电路封装外观
  //   输出引脚
endmodule

module \阻塞检测  (
  input  [6:0] IF_opcode,
  input  [4:0] EX_rd,
  input  [4:0] IF_rs1,
  input  EX_MemtoReg,
  input  [4:0] IF_rs2,
  output Stall
);

  wire and_1_out, and_2_out, Br, comparator_2_eq, comparator_3_eq, comparator_4_eq, comparator_5_eq,
       comparator_6_eq, comparator_7_eq, I, or_1_out, or_2_out, R, St;

  Comparator #(.width(7), .mode("unsigned")) comparator_1 (.a(IF_opcode), .b(7'b1100011), .eq(Br));  // open: gt, lt
  or or_1 (or_1_out, St, R, Br, I);
  Comparator #(.width(5), .mode("unsigned")) comparator_2 (
    .a(IF_rs1), .b(EX_rd), .eq(comparator_2_eq));  // open: gt, lt
  Comparator #(.width(5), .mode("unsigned")) comparator_3 (
    .a(EX_rd), .b(IF_rs2), .eq(comparator_3_eq));  // open: gt, lt
  or or_2 (or_2_out, St, R, Br);
  Comparator #(.width(5), .mode("unsigned")) comparator_4 (
    .a(EX_rd), .b({5{1'b0}}), .eq(comparator_4_eq));  // open: gt, lt
  Comparator #(.width(7), .mode("unsigned")) comparator_5 (
    .a(IF_opcode), .b(7'b0000011), .eq(comparator_5_eq));  // open: gt, lt
  and and_1 (and_1_out, or_1_out, EX_MemtoReg, comparator_2_eq, ~comparator_4_eq);  // AND_Gate
  and and_2 (and_2_out, comparator_3_eq, EX_MemtoReg, or_2_out, ~comparator_4_eq);  // AND_Gate
  Comparator #(.width(7), .mode("unsigned")) comparator_6 (
    .a(IF_opcode), .b(7'b0010011), .eq(comparator_6_eq));  // open: gt, lt
  or or_3 (Stall, and_1_out, and_2_out);
  Comparator #(.width(7), .mode("unsigned")) comparator_7 (
    .a(IF_opcode), .b(7'b1100111), .eq(comparator_7_eq));  // open: gt, lt
  or or_4 (I, comparator_6_eq, comparator_7_eq, comparator_5_eq);
  Comparator #(.width(7), .mode("unsigned")) comparator_8 (.a(IF_opcode), .b(7'b0110011), .eq(R));  // open: gt, lt
  Comparator #(.width(7), .mode("unsigned")) comparator_9 (.a(IF_opcode), .b(7'b0100011), .eq(St));  // open: gt, lt

  // Notes on the sheet:
  //   EX_MemtoReg: pull=down
  //   EX_rd: pull=down
  //   输入信号
  //   输出信号
endmodule

module \转发检测  (
  input  [4:0] EX_rs1,
  input  [4:0] M_rd,
  input  [4:0] EX_rs2,
  input  [4:0] WB_rd,
  input  M_RegWr,
  input  WB_RegWr,
  output [1:0] BusAFW,
  output [1:0] BusBFW
);

  wire comparator_1_eq, comparator_2_eq, comparator_3_eq, comparator_4_eq, comparator_5_eq, comparator_6_eq;

  Comparator #(.width(5), .mode("unsigned")) comparator_1 (
    .a({5{1'b0}}), .b(M_rd), .eq(comparator_1_eq));  // open: gt, lt
  Comparator #(.width(5), .mode("unsigned")) comparator_2 (
    .a({5{1'b0}}), .b(WB_rd), .eq(comparator_2_eq));  // open: gt, lt
  Comparator #(.width(5), .mode("unsigned")) comparator_3 (
    .a(WB_rd), .b(EX_rs2), .eq(comparator_3_eq));  // open: gt, lt
  Comparator #(.width(5), .mode("unsigned")) comparator_4 (.a(EX_rs2), .b(M_rd), .eq(comparator_4_eq));  // open: gt, lt
  Comparator #(.width(5), .mode("unsigned")) comparator_5 (
    .a(WB_rd), .b(EX_rs1), .eq(comparator_5_eq));  // open: gt, lt
  Comparator #(.width(5), .mode("unsigned")) comparator_6 (.a(EX_rs1), .b(M_rd), .eq(comparator_6_eq));  // open: gt, lt
  and and_1 (BusAFW[0], comparator_6_eq, ~comparator_1_eq, M_RegWr);  // AND_Gate
  and and_2 (BusBFW[1], comparator_3_eq, ~comparator_2_eq, WB_RegWr, ~BusBFW[0]);  // AND_Gate
  and and_3 (BusBFW[0], comparator_4_eq, ~comparator_1_eq, M_RegWr);  // AND_Gate
  and and_4 (BusAFW[1], comparator_5_eq, ~comparator_2_eq, WB_RegWr, ~BusAFW[0]);  // AND_Gate

  // Notes on the sheet:
  //   M_rd: pull=down
  //   EX_rs1: pull=down
  //   WB_rd: pull=down
  //   EX_rs2: pull=down
  //   输入信号
  //   输出信号
endmodule

module \流水段寄存器  (
  input  CLR,
  input  [31:0] PC,
  input  CLK,
  input  WE,
  input  Halt,
  input  [31:0] IR,
  input  [3:0] ALUctr,
  input  ALUASrc,
  input  [1:0] ALUBSrc,
  input  [31:0] BusA,
  input  [2:0] BandJ,
  input  [2:0] MemOp,
  input  MemWr,
  input  [31:0] BusB,
  input  RegWr,
  input  MemtoReg,
  input  [4:0] RD,
  input  [31:0] Imm,
  input  [4:0] RS1,
  input  [4:0] RS2,
  input  Zero,
  input  [31:0] Result,
  input  [31:0] PCTarget,
  input  [31:0] Dout,
  output [31:0] PCo,
  output Halto,
  output [31:0] IRo,
  output [3:0] ALUctro,
  output ALUASrco,
  output [1:0] ALUBSrco,
  output [31:0] BusAo,
  output [2:0] BandJo,
  output [2:0] MemOpo,
  output MemWro,
  output [31:0] BusBo,
  output RegWro,
  output MemtoRego,
  output [4:0] RDo,
  output [31:0] Immo,
  output [4:0] RS1o,
  output [4:0] RS2o,
  output Zeroo,
  output [31:0] Resulto,
  output [31:0] PCTargeto,
  output [31:0] Douto
);

  wire multiplexer_3_out, multiplexer_4_out, multiplexer_9_out, multiplexer_10_out, multiplexer_14_out,
       multiplexer_19_out;
  wire [1:0] multiplexer_20_out;
  wire [2:0] multiplexer_5_out, multiplexer_11_out;
  wire [3:0] multiplexer_15_out;
  wire [4:0] multiplexer_6_out, multiplexer_16_out, multiplexer_21_out;
  wire [31:0] multiplexer_1_out, multiplexer_2_out, multiplexer_7_out, multiplexer_8_out, multiplexer_12_out,
       multiplexer_13_out, multiplexer_17_out, multiplexer_18_out;

  Multiplexer #(.width(32), .enable("false")) multiplexer_1 (
    .in0(PC), .in1({32{1'b0}}), .out(multiplexer_1_out), .sel(CLR));
  Register #(.width(32), .trigger("falling"), .Select("low")) register_1 (
    .D(multiplexer_1_out), .en(WE), .Q(PCo), .clk(CLK));  // open: clr
  Multiplexer #(.width(32), .enable("false")) multiplexer_2 (
    .in0(Imm), .in1({32{1'b0}}), .out(multiplexer_2_out), .sel(CLR));
  Register #(.width(32), .trigger("falling"), .Select("low")) register_2 (
    .D(multiplexer_2_out), .en(WE), .Q(Immo), .clk(CLK));  // open: clr
  Register #(.width(1), .trigger("falling"), .Select("low")) register_3 (
    .D(multiplexer_3_out), .en(WE), .Q(Halto), .clk(CLK));  // open: clr
  Multiplexer #(.enable("false")) multiplexer_3 (.in0(Halt), .in1(1'b0), .out(multiplexer_3_out), .sel(CLR));
  Multiplexer #(.enable("false")) multiplexer_4 (.in0(MemtoReg), .in1(1'b0), .out(multiplexer_4_out), .sel(CLR));
  Register #(.width(1), .trigger("falling"), .Select("low")) register_4 (
    .D(multiplexer_4_out), .en(WE), .Q(MemtoRego), .clk(CLK));  // open: clr
  Multiplexer #(.width(3), .enable("false")) multiplexer_5 (
    .in0(BandJ), .in1(3'b000), .out(multiplexer_5_out), .sel(CLR));
  Register #(.width(3), .trigger("falling"), .Select("low")) register_5 (
    .D(multiplexer_5_out), .en(WE), .Q(BandJo), .clk(CLK));  // open: clr
  Register #(.width(5), .trigger("falling"), .Select("low")) register_6 (
    .D(multiplexer_6_out), .en(WE), .Q(RS2o), .clk(CLK));  // open: clr
  Multiplexer #(.width(5), .enable("false")) multiplexer_6 (
    .in0(RS2), .in1({5{1'b0}}), .out(multiplexer_6_out), .sel(CLR));
  Multiplexer #(.width(32), .enable("false")) multiplexer_7 (
    .in0(IR), .in1({32{1'b0}}), .out(multiplexer_7_out), .sel(CLR));
  Multiplexer #(.width(32), .enable("false")) multiplexer_8 (
    .in0(Result), .in1({32{1'b0}}), .out(multiplexer_8_out), .sel(CLR));
  Multiplexer #(.enable("false")) multiplexer_9 (.in0(ALUASrc), .in1(1'b0), .out(multiplexer_9_out), .sel(CLR));
  Multiplexer #(.enable("false")) multiplexer_10 (.in0(Zero), .in1(1'b0), .out(multiplexer_10_out), .sel(CLR));
  Multiplexer #(.width(3), .enable("false")) multiplexer_11 (
    .in0(MemOp), .in1(3'b000), .out(multiplexer_11_out), .sel(CLR));
  Register #(.width(32), .trigger("falling"), .Select("low")) register_7 (
    .D(multiplexer_7_out), .en(WE), .Q(IRo), .clk(CLK));  // open: clr
  Register #(.width(32), .trigger("falling"), .Select("low")) register_8 (
    .D(multiplexer_8_out), .en(WE), .Q(Resulto), .clk(CLK));  // open: clr
  Register #(.width(1), .trigger("falling"), .Select("low")) register_9 (
    .D(multiplexer_9_out), .en(WE), .Q(ALUASrco), .clk(CLK));  // open: clr
  Register #(.width(1), .trigger("falling"), .Select("low")) register_10 (
    .D(multiplexer_10_out), .en(WE), .Q(Zeroo), .clk(CLK));  // open: clr
  Register #(.width(3), .trigger("falling"), .Select("low")) register_11 (
    .D(multiplexer_11_out), .en(WE), .Q(MemOpo), .clk(CLK));  // open: clr
  Register #(.width(32), .trigger("falling"), .Select("low")) register_12 (
    .D(multiplexer_12_out), .en(WE), .Q(BusAo), .clk(CLK));  // open: clr
  Multiplexer #(.width(32), .enable("false")) multiplexer_12 (
    .in0(BusA), .in1({32{1'b0}}), .out(multiplexer_12_out), .sel(CLR));
  Multiplexer #(.width(32), .enable("false")) multiplexer_13 (
    .in0(PCTarget), .in1({32{1'b0}}), .out(multiplexer_13_out), .sel(CLR));
  Register #(.width(32), .trigger("falling"), .Select("low")) register_13 (
    .D(multiplexer_13_out), .en(WE), .Q(PCTargeto), .clk(CLK));  // open: clr
  Multiplexer #(.enable("false")) multiplexer_14 (.in0(MemWr), .in1(1'b0), .out(multiplexer_14_out), .sel(CLR));
  Register #(.width(1), .trigger("falling"), .Select("low")) register_14 (
    .D(multiplexer_14_out), .en(WE), .Q(MemWro), .clk(CLK));  // open: clr
  Register #(.width(4), .trigger("falling"), .Select("low")) register_15 (
    .D(multiplexer_15_out), .en(WE), .Q(ALUctro), .clk(CLK));  // open: clr
  Multiplexer #(.width(4), .enable("false")) multiplexer_15 (
    .in0(ALUctr), .in1(4'b0000), .out(multiplexer_15_out), .sel(CLR));
  Multiplexer #(.width(5), .enable("false")) multiplexer_16 (
    .in0(RD), .in1({5{1'b0}}), .out(multiplexer_16_out), .sel(CLR));
  Register #(.width(5), .trigger("falling"), .Select("low")) register_16 (
    .D(multiplexer_16_out), .en(WE), .Q(RDo), .clk(CLK));  // open: clr
  Multiplexer #(.width(32), .enable("false")) multiplexer_17 (
    .in0(BusB), .in1({32{1'b0}}), .out(multiplexer_17_out), .sel(CLR));
  Register #(.width(32), .trigger("falling"), .Select("low")) register_17 (
    .D(multiplexer_17_out), .en(WE), .Q(BusBo), .clk(CLK));  // open: clr
  Multiplexer #(.width(32), .enable("false")) multiplexer_18 (
    .in0(Dout), .in1({32{1'b0}}), .out(multiplexer_18_out), .sel(CLR));
  Register #(.width(32), .trigger("falling"), .Select("low")) register_18 (
    .D(multiplexer_18_out), .en(WE), .Q(Douto), .clk(CLK));  // open: clr
  Register #(.width(1), .trigger("falling"), .Select("low")) register_19 (
    .D(multiplexer_19_out), .en(WE), .Q(RegWro), .clk(CLK));  // open: clr
  Multiplexer #(.enable("false")) multiplexer_19 (.in0(RegWr), .in1(1'b0), .out(multiplexer_19_out), .sel(CLR));
  Register #(.width(2), .trigger("falling"), .Select("low")) register_20 (
    .D(multiplexer_20_out), .en(WE), .Q(ALUBSrco), .clk(CLK));  // open: clr
  Multiplexer #(.width(2), .enable("false")) multiplexer_20 (
    .in0(ALUBSrc), .in1(2'b00), .out(multiplexer_20_out), .sel(CLR));
  Register #(.width(5), .trigger("falling"), .Select("low")) register_21 (
    .D(multiplexer_21_out), .en(WE), .Q(RS1o), .clk(CLK));  // open: clr
  Multiplexer #(.width(5), .enable("false")) multiplexer_21 (
    .in0(RS1), .in1({5{1'b0}}), .out(multiplexer_21_out), .sel(CLR));

  // Notes on the sheet:
  //   输入引脚区
  //   输出引脚区
endmodule

module EU (
  input  [3:0] ALUctr,
  input  ALUASrc,
  input  [1:0] ALUBSrc,
  input  [31:0] PC,
  input  [31:0] BusA,
  input  [31:0] BusB,
  input  [31:0] Imm,
  input  [2:0] BandJ,
  output [31:0] PCTarget,
  output [31:0] Result,
  output Zero
);

  wire and_1_out;
  wire [31:0] multiplexer_1_out, multiplexer_2_out, multiplexer_3_out;

  Multiplexer #(.width(32), .enable("false")) multiplexer_1 (
    .in0(BusA), .in1(PC), .out(multiplexer_1_out), .sel(ALUASrc));
  Multiplexer #(.select(2), .width(32), .enable("false")) multiplexer_2 (
    .in0(BusB), .in1(32'h4), .in2(Imm), .out(multiplexer_2_out), .sel(ALUBSrc));  // open: in3
  ALU alu_1 (.A(multiplexer_1_out), .B(multiplexer_2_out), .ALUctr(ALUctr), .S(Result), .Zero(Zero));
  and and_1 (and_1_out, ~BandJ[0], BandJ[1], ~BandJ[2]);  // AND_Gate
  Multiplexer #(.width(32), .enable("false")) multiplexer_3 (
    .in0(PC), .in1(BusA), .out(multiplexer_3_out), .sel(and_1_out));
  Adder32 adder32_1 (.X(multiplexer_3_out), .Y(Imm), .S(PCTarget));  // open: CF, OF, SF, ZF, Cin, Cout
  // Probe on PCTarget

  // Notes on the sheet:
  //   ALUctr: pull=down
  //   ALUASrc: pull=down
  //   ALUBSrc: pull=down
  //   Result: pull=down
  //   PCTarget: pull=down
  //   BandJ: pull=down
  //   输入信号
  //   请勿修改引脚名称、电路名称及电路封装外观
  //   为了后续实验中的引用，不要修改控制信号编码定义。
  //   输出信号
endmodule

module decode (
  input  [17:0] Addr,
  input  [2:0] MemOp,
  output AlignErr,
  output out_4,
  output out_5,
  output out_6,
  output out_7
);

  wire and_3_out, E_0, multiplexer_1_out, not_1_out, not_2_out;
  wire [3:0] _01, multiplexer_2_out;
  wire [3:1] _10;
  wire [3:3] _00;

  Decoder #(.select(2), .enable("false")) decoder_1 (.out0(_00[3]), .sel(Addr[1:0]));  // open: out1, out2, out3
  Decoder #(.select(2), .enable("false")) decoder_2 (
    .out0(_01[0]), .out1(_01[1]), .out2(_01[2]), .out3(_01[3]), .sel(Addr[1:0]));
  not not_1 (not_1_out, Addr[1]);
  not not_2 (not_2_out, Addr[0]);
  not not_3 (E_0, _00[3]);
  and and_1 (_10[1], not_1_out, not_2_out);
  and and_2 (_10[3], Addr[1], not_2_out);
  Multiplexer #(.select(2), .enable("false")) multiplexer_1 (
    .in0(E_0), .in1(1'b0), .in2(Addr[0]), .in3(1'b1), .out(multiplexer_1_out), .sel(MemOp[1:0]));
  Multiplexer #(.select(2), .width(4), .enable("false")) multiplexer_2 (
    .in0({4{_00[3]}}), .in1(_01), .in2({{2{_10[3]}}, {2{_10[1]}}}), .in3(4'b0000), .out(multiplexer_2_out),
    .sel(MemOp[1:0]));
  Multiplexer #(.enable("false")) multiplexer_3 (.in0(multiplexer_1_out), .in1(1'b1), .out(AlignErr), .sel(and_3_out));
  Multiplexer #(.width(4), .enable("false")) multiplexer_4 (
    .in0(multiplexer_2_out), .in1(4'b0000), .out({out_7, out_6, out_5, out_4}), .sel(and_3_out));
  and and_3 (and_3_out, ~MemOp[0], ~MemOp[1], MemOp[2]);  // AND_Gate

  // Other names for the same wires on the sheet: _00[2:0] = {3{_00[3]}}; _10 (some bits) = {_10[3], _10[1]};
  //   E_2 = Addr[0]; SEL[3:0] = {out_7, out_6, out_5, out_4}; SEL_0 = out_4; SEL_1 = out_5; SEL_2 = out_6;
  //   SEL_3 = out_7
endmodule

module io (
  input  [17:0] Addr,
  input  [31:0] Din,
  input  AlignErr,
  input  [2:0] MemOp,
  input  [7:0] in_5,
  input  [7:0] in_6,
  input  [7:0] in_7,
  input  [7:0] in_8,
  output [7:0] out_9,
  output [7:0] out_10,
  output [7:0] out_11,
  output [7:0] out_12,
  output [31:0] DataOut
);

  wire [31:0] aligned, multiplexer_1_out, Op1, Op2, Op5, Op6;

  assign Op1 = {{24{1'b0}}, aligned[7:0]};  // Bit_Extender bit_extender_1
  assign Op5 = {{24{aligned[7]}}, aligned[7:0]};  // Bit_Extender bit_extender_2
  assign Op2 = {{16{1'b0}}, aligned[15:0]};  // Bit_Extender bit_extender_3
  assign Op6 = {{16{aligned[15]}}, aligned[15:0]};  // Bit_Extender bit_extender_4
  Shifter #(.width(32)) shifter_1 (.in(Din), .\dist ({Addr[1:0], 3'b000}), .out({out_12, out_11, out_10, out_9}));
  Shifter #(.width(32), .shift("lr")) shifter_2 (
    .in({in_8, in_7, in_6, in_5}), .\dist ({Addr[1:0], 3'b000}), .out(aligned));
  Multiplexer #(.select(3), .width(32), .enable("false")) multiplexer_1 (
    .in0(aligned), .in1(Op1), .in2(Op2), .in5(Op5), .in6(Op6), .out(multiplexer_1_out), .sel(MemOp));  // open: in3, in4, in7
  Multiplexer #(.width(32), .enable("false")) multiplexer_2 (
    .in0(multiplexer_1_out), .in1({in_8, in_7, in_6, in_5}), .out(DataOut), .sel(AlignErr));

  // Other names for the same wires on the sheet: Op0[31:0] = aligned; Dout[31:0] = DataOut;
  //   in[31:0] = {out_12, out_11, out_10, out_9}; in0[7:0] = out_9; in1[7:0] = out_10; in2[7:0] = out_11;
  //   in3[7:0] = out_12; out[31:0] = {in_8, in_7, in_6, in_5}; out0[7:0] = in_5; out1[7:0] = in_6; out2[7:0] = in_7;
  //   out3[7:0] = in_8
endmodule
