// Logisim project lab8.1.chk.circ as structural Verilog: 1 circuit, main circuit main
module main (
  output [8:0] Cnt,
  output [31:0] WB_PC,
  output [31:0] WB_BusW,
  output [15:0] Cycles,
  output _passed,
  output halt
);

  wire CLK, comparator_2_eq, comparator_3_eq, main_1_halt, not_2_out, Reset_data, Running;
  wire [15:0] main_1_cycles;
  wire [31:0] Init_Addr_data, main_1_wb_busw, main_1_wb_pc, \评测数据WBBusW_data , \评测数据WBPC_data ;

  Clock u_clk (.out(CLK));
  // NOT_Gate not_1 has open pins: in=halt, out=open
  Comparator #(.width(9), .mode("unsigned")) comparator_1 (.a(9'hc3), .b(Cnt), .gt(Running));  // open: eq, lt
  Counter #(.width(9), .max('h1ff), .behavior("old")) counter_1 (
    .count(Running), .Q(Cnt), .clk(CLK));  // open: load, D, carry, clr, preset
  not not_2 (not_2_out, halt);
  ROM #(.addrWidth(9), .dataWidth(32), .Select("low")) Init_Addr (.addr(Cnt), .data(Init_Addr_data));
  ROM #(.addrWidth(9), .dataWidth(1), .Select("low")) Reset (.addr(Cnt), .data(Reset_data));
  ROM #(.addrWidth(9), .dataWidth(32), .Select("high")) \u_评测数据WBBusW  (.addr(Cnt), .data(\评测数据WBBusW_data ));
  ROM #(.addrWidth(9), .dataWidth(32), .Select("high")) \u_评测数据WBPC  (.addr(Cnt), .data(\评测数据WBPC_data ));
  // Probe on WB_PC
  Comparator #(.width(32), .mode("unsigned")) comparator_2 (
    .a(WB_BusW), .b(\评测数据WBBusW_data ), .eq(comparator_2_eq));  // open: gt, lt
  Comparator #(.width(32), .mode("unsigned")) comparator_3 (
    .a(WB_PC), .b(\评测数据WBPC_data ), .eq(comparator_3_eq));  // open: gt, lt
  RAM #(.addrWidth(9), .dataWidth(32), .bus("separate"), .simpleMode("false"), .Select("low")) ram_1 (
    .addr(Cnt), .din(WB_BusW), .str(not_2_out), .clk(CLK));  // open: data, sel, ld, clr
  // Probe on WB_BusW
  lab8_1_main main_1 (
    .Init_Addr(Init_Addr_data), .ReSet(Reset_data), .BP_PC(Init_Addr_data), .BPEn(Reset_data),
    .WB_PC(main_1_wb_pc), .Cycles(main_1_cycles), .halt(main_1_halt), .clk(CLK), .WB_BusW(main_1_wb_busw));
  and and_1 (_passed, comparator_2_eq, comparator_3_eq);
  Register #(.width(32), .Select("low")) register_1 (.D(main_1_wb_pc), .Q(WB_PC), .clk(CLK));  // open: en, clr
  Register #(.width(16), .Select("low")) register_2 (.D(main_1_cycles), .Q(Cycles), .clk(CLK));  // open: en, clr
  Register #(.width(1), .Select("low")) register_3 (.D(main_1_halt), .Q(halt), .clk(CLK));  // open: en, clr
  Register #(.width(32), .Select("low")) register_4 (.D(main_1_wb_busw), .Q(WB_BusW), .clk(CLK));  // open: en, clr
  RAM #(.addrWidth(9), .dataWidth(32), .bus("separate"), .simpleMode("false"), .Select("low")) ram_2 (
    .addr(Cnt), .din(WB_PC), .str(not_2_out), .clk(CLK));  // open: data, sel, ld, clr
  RAM #(.addrWidth(9), .dataWidth(1), .bus("separate"), .simpleMode("false"), .Select("low")) ram_3 (
    .addr(Cnt), .din(_passed), .str(not_2_out), .clk(CLK));  // open: data, sel, ld, clr

  // Other names for the same wires on the sheet: Equal = _passed; tunnel[8:0] = Cnt

  // Notes on the sheet:
  //   比执行总周期数多1
  //   生成测试数据地址
  //   输入引脚
  //   contents of 评测数据WBBusW (hex, n*v repeats v):
  //   5*0 80000000 7ff 0 1 0 80000000 ffff8000 7fff8000 7fff8000 2 0 ff01000 ff00ff0 f0f0f000 f0f0f0f0
  //   f000f0 f00000 f000f0 3 0 1 3f 80000000 80000000 4 0 80000000 e fffe0000 fffe0000 5 0 80000000 1 1 6
  //   0 80000000 0 0 7 0 20a8 2000 ee 2000 ff 2001 c0 2002 0 2003 ffffffff 8 ffffffff 2000 0 9 10000 ffee
  //   ffee 11fee 0 a c0 c0 2004 0 b c10000 c0ffee c0ffee c11fee 0 c c10000 c0ffee 2000 c0ffee 4000 2004
  //   c0ffee c11ff2 0 d 140 148 0 0 0 150 148 0 e a 0 5*1 2 0 188 0 0 0 2 1 2 3 0 188 0 0 0 3 2 3 4 0 188
  //   0 0 0 5 3 5 5 0 188 0 0 0 8 5 8 6 0 188 0 0 0 d 8 d 7 0 188 0 0 0 15 d 15 8 0 188 0 0 0 22 15 22 9 0
  //   188 0 0 0 37 22 37 a 0 188 0 0 0 59 37 59 b 1 0 0 0 2008 c10000 c0ffee
  //   contents of 评测数据WBPC (hex, n*v repeats v):
  //   6*0 4 8 c 10 14 18 1c 20 24 28 2c 30 34 38 3c 40 44 48 4c 50 54 58 5c 60 64 68 6c 70 74 78 7c 80 84
  //   88 8c 90 94 98 9c a0 a4 a8 ac b0 b4 b8 bc c0 c4 c8 cc d0 d4 d8 dc dc e0 e4 e8 ec f0 f0 f4 f8 fc 100
  //   104 108 10c 110 114 118 118 11c 120 124 128 12c 130 130 134 138 138 13c 140 144 0 0 0 150 154 158
  //   15c 160 164 168 16c 170 174 178 17c 180 184 0 0 0 170 174 178 17c 180 184 0 0 0 170 174 178 17c 180
  //   184 0 0 0 170 174 178 17c 180 184 0 0 0 170 174 178 17c 180 184 0 0 0 170 174 178 17c 180 184 0 0 0
  //   170 174 178 17c 180 184 0 0 0 170 174 178 17c 180 184 0 0 0 170 174 178 17c 180 184 0 0 0 170 174
  //   178 17c 180 0 0 0 188 18c 190 194 194
  //   生成测试电路输出结果
  //   输出引脚
endmodule
