// Logisim project lab8.2.chk.circ as structural Verilog: 1 circuit, main circuit main
module main (
  output [8:0] Cnt,
  output [31:0] WB_PC,
  output [31:0] WB_BusW,
  output [15:0] Cycles,
  output _passed,
  output halt
);

  wire CLK, comparator_2_eq, comparator_3_eq, main_1_halt, not_2_out, Reset_data, Running;
  wire [15:0] main_1_cycles;
  wire [31:0] Init_Addr_data, main_1_wb_busw, main_1_wb_pc, \评测数据WBBusW_data , \评测数据WBPC_data ;

  Clock u_clk (.out(CLK));
  // NOT_Gate not_1 has open pins: in=halt, out=open
  Comparator #(.width(9), .mode("unsigned")) comparator_1 (.a(9'h47), .b(Cnt), .gt(Running));  // open: eq, lt
  Counter #(.width(9), .max('h1ff), .behavior("old")) counter_1 (
    .count(Running), .Q(Cnt), .clk(CLK));  // open: load, D, carry, clr, preset
  not not_2 (not_2_out, halt);
  ROM #(.addrWidth(9), .dataWidth(32), .Select("low")) Init_Addr (.addr(Cnt), .data(Init_Addr_data));
  ROM #(.addrWidth(9), .dataWidth(1), .Select("low")) Reset (.addr(Cnt), .data(Reset_data));
  ROM #(.addrWidth(9), .dataWidth(32), .Select("high")) \u_评测数据WBBusW  (.addr(Cnt), .data(\评测数据WBBusW_data ));
  ROM #(.addrWidth(9), .dataWidth(32), .Select("high")) \u_评测数据WBPC  (.addr(Cnt), .data(\评测数据WBPC_data ));
  // Probe on WB_PC
  Comparator #(.width(32), .mode("unsigned")) comparator_2 (
    .a(WB_BusW), .b(\评测数据WBBusW_data ), .eq(comparator_2_eq));  // open: gt, lt
  Comparator #(.width(32), .mode("unsigned")) comparator_3 (
    .a(WB_PC), .b(\评测数据WBPC_data ), .eq(comparator_3_eq));  // open: gt, lt
  RAM #(.addrWidth(9), .dataWidth(32), .bus("separate"), .simpleMode("false"), .Select("low")) ram_1 (
    .addr(Cnt), .din(WB_BusW), .str(not_2_out), .clk(CLK));  // open: data, sel, ld, clr
  // Probe on WB_BusW
  lab8_2_main main_1 (
    .Init_Addr(Init_Addr_data), .ReSet(Reset_data), .BP_PC(Init_Addr_data), .BPEn(Reset_data),
    .WB_PC(main_1_wb_pc), .Cycles(main_1_cycles), .halt(main_1_halt), .clk(CLK), .WB_BusW(main_1_wb_busw));
  and and_1 (_passed, comparator_2_eq, comparator_3_eq);
  Register #(.width(32), .Select("low")) register_1 (.D(main_1_wb_pc), .Q(WB_PC), .clk(CLK));  // open: en, clr
  Register #(.width(16), .Select("low")) register_2 (.D(main_1_cycles), .Q(Cycles), .clk(CLK));  // open: en, clr
  Register #(.width(1), .Select("low")) register_3 (.D(main_1_halt), .Q(halt), .clk(CLK));  // open: en, clr
  Register #(.width(32), .Select("low")) register_4 (.D(main_1_wb_busw), .Q(WB_BusW), .clk(CLK));  // open: en, clr
  RAM #(.addrWidth(9), .dataWidth(32), .bus("separate"), .simpleMode("false"), .Select("low")) ram_2 (
    .addr(Cnt), .din(WB_PC), .str(not_2_out), .clk(CLK));  // open: data, sel, ld, clr
  RAM #(.addrWidth(9), .dataWidth(1), .bus("separate"), .simpleMode("false"), .Select("low")) ram_3 (
    .addr(Cnt), .din(_passed), .str(not_2_out), .clk(CLK));  // open: data, sel, ld, clr

  // Other names for the same wires on the sheet: Equal = _passed; tunnel[8:0] = Cnt

  // Notes on the sheet:
  //   比执行总周期数多1
  //   生成测试数据地址
  //   输入引脚
  //   contents of 评测数据WBBusW (hex, n*v repeats v):
  //   5*0 a 0 0 1 0 1 2 4*0 3 3 4*0 6 4 4*0 a 5 4*0 f 6 4*0 15 7 4*0 1c 8 4*0 24 9 4*0 2d a 4*0 37 b 1 4
  //   c10000 c0ffee
  //   contents of 评测数据WBPC (hex, n*v repeats v):
  //   6*0 4 4 8 c 10 14 18 0 0 0 10 14 18 0 0 0 10 14 18 0 0 0 10 14 18 0 0 0 10 14 18 0 0 0 10 14 18 0 0
  //   0 10 14 18 0 0 0 10 14 18 0 0 0 10 14 18 0 0 0 10 14 18 1c 20 24 28
  //   生成测试电路输出结果
  //   输出引脚
endmodule
