// Logisim project lab8.3.chk.circ as structural Verilog: 1 circuit, main circuit main
module main (
  output [9:0] Cnt,
  output [31:0] WB_PC,
  output [31:0] WB_BusW,
  output [15:0] Cycles,
  output _passed,
  output halt
);

  wire CLK, comparator_2_eq, comparator_3_eq, main_1_halt, not_1_out, not_2_out, Reset_data, Running;
  wire [15:0] main_1_cycles;
  wire [31:0] Init_Addr_data, main_1_wb_busw, main_1_wb_pc, \评测数据WBBusW_data , \评测数据WBPC_data ;

  Clock u_clk (.out(CLK));
  not not_1 (not_1_out, halt);
  Comparator #(.width(10), .mode("unsigned")) comparator_1 (.a(10'h248), .b(Cnt), .gt(Running));  // open: eq, lt
  Counter #(.width(10), .max('h3ff), .behavior("old")) counter_1 (
    .count(Running), .Q(Cnt), .clk(CLK));  // open: load, D, carry, clr, preset
  not not_2 (not_2_out, halt);
  ROM #(.addrWidth(10), .dataWidth(32), .Select("low")) Init_Addr (.addr(Cnt), .data(Init_Addr_data));
  ROM #(.addrWidth(10), .dataWidth(1), .Select("low")) Reset (.addr(Cnt), .data(Reset_data));
  ROM #(.addrWidth(10), .dataWidth(32), .Select("high")) \u_评测数据WBBusW  (.addr(Cnt), .data(\评测数据WBBusW_data ));
  ROM #(.addrWidth(10), .dataWidth(32), .Select("high")) \u_评测数据WBPC  (.addr(Cnt), .data(\评测数据WBPC_data ));
  // Probe on WB_PC
  Comparator #(.width(32), .mode("unsigned")) comparator_2 (
    .a(WB_BusW), .b(\评测数据WBBusW_data ), .eq(comparator_2_eq));  // open: gt, lt
  Comparator #(.width(32), .mode("unsigned")) comparator_3 (
    .a(WB_PC), .b(\评测数据WBPC_data ), .eq(comparator_3_eq));  // open: gt, lt
  RAM #(.addrWidth(10), .dataWidth(32), .bus("separate"), .simpleMode("false"), .Select("low")) ram_1 (
    .addr(Cnt), .din(WB_BusW), .str(not_2_out), .clk(CLK));  // open: data, sel, ld, clr
  // Probe on WB_BusW
  lab8_3_main main_1 (
    .Init_Addr(Init_Addr_data), .ReSet(Reset_data), .BP_PC(Init_Addr_data), .BPEn(Reset_data),
    .WB_PC(main_1_wb_pc), .Cycles(main_1_cycles), .halt(main_1_halt), .clk(CLK), .WB_BusW(main_1_wb_busw));
  and and_1 (_passed, comparator_2_eq, comparator_3_eq);
  Register #(.width(32), .Select("low")) register_1 (.D(main_1_wb_pc), .Q(WB_PC), .clk(CLK));  // open: en, clr
  Register #(.width(16), .Select("low")) register_2 (.D(main_1_cycles), .Q(Cycles), .clk(CLK));  // open: en, clr
  Register #(.width(1), .Select("low")) register_3 (.D(main_1_halt), .Q(halt), .clk(CLK));  // open: en, clr
  Register #(.width(32), .Select("low")) register_4 (.D(main_1_wb_busw), .Q(WB_BusW), .clk(CLK));  // open: en, clr
  RAM #(.addrWidth(10), .dataWidth(32), .bus("separate"), .simpleMode("false"), .Select("low")) ram_2 (
    .addr(Cnt), .din(WB_PC), .str(not_2_out), .clk(CLK));  // open: data, sel, ld, clr
  RAM #(.addrWidth(10), .dataWidth(1), .bus("separate"), .simpleMode("false"), .Select("low")) ram_3 (
    .addr(Cnt), .din(_passed), .str(not_2_out), .clk(CLK));  // open: data, sel, ld, clr

  // Other names for the same wires on the sheet: Equal = _passed; tunnel[9:0] = Cnt

  // Notes on the sheet:
  //   比执行总周期数多1
  //   生成测试数据地址
  //   输入引脚
  //   contents of 评测数据WBBusW (hex, n*v repeats v):
  //   5*0 a 1 4 1 a 0 9 0 4 78 34 80 1 4 8 1 1 0 0 4 8 78 2 84 1 8 c 2 1 0 0 8 c 78 12 88 1 c 10 3 1 0 0 c
  //   10 78 ffffffa3 8c 1 10 14 4 1 0 0 10 14 78 56 90 1 14 18 5 1 0 0 14 18 78 ffffffdb 94 1 18 1c 6 1 0
  //   0 18 1c 78 5 98 1 1c 20 7 1 0 0 1c 20 78 49 9c 1 20 24 8 1 0 0 20 24 78 ffffffc7 a0 1 24 28 9 0 9
  //   4*0 8 0 4 34 2 3c 1 4 8 1 1 0 0 4 8 34 12 40 1 8 c 2 1 0 0 8 c 34 ffffffa3 44 1 c 10 3 1 0 0 c 10 34
  //   56 48 0 0 0 4 1 0 0 10 14 56 ffffffdb 6e 1 14 18 5 1 0 0 14 18 56 5 72 1 18 1c 6 1 0 0 18 1c 56 49
  //   76 1 1c 20 7 1 0 0 1c 20 56 ffffffc7 7a 1 20 24 8 0 8 4*0 7 0 4 2 12 a 0 0 0 1 1 0 0 4 8 12 ffffffa3
  //   1e 1 8 c 2 1 0 0 8 c 12 34 22 0 0 0 3 1 0 0 c 10 34 ffffffdb 48 1 10 14 4 1 0 0 10 14 34 5 4c 1 14
  //   18 5 1 0 0 14 18 34 49 50 0 0 0 6 1 0 0 18 1c 49 ffffffc7 69 1 1c 20 7 0 7 4*0 6 0 4 2 ffffffa3 a 1
  //   4 8 1 1 0 0 4 8 2 12 e 0 0 0 2 1 0 0 8 c 12 ffffffdb 22 1 c 10 3 1 0 0 c 10 12 5 26 1 10 14 4 1 0 0
  //   10 14 12 34 2a 0 0 0 5 1 0 0 14 18 34 ffffffc7 50 1 18 1c 6 0 6 4*0 5 0 4 ffffffa3 2 ffffffab 0 0 0
  //   1 1 0 0 4 8 2 ffffffdb e 1 8 c 2 1 0 0 8 c 2 5 12 0 0 0 3 1 0 0 c 10 5 12 19 0 0 0 4 1 0 0 10 14 12
  //   ffffffc7 2a 1 14 18 5 0 5 4*0 4 0 4 ffffffa3 ffffffdb ffffffab 0 0 0 1 1 0 0 4 8 ffffffdb 2 ffffffe7
  //   0 0 0 2 1 0 0 8 c 2 5 12 0 0 0 3 1 0 0 c 10 5 ffffffc7 19 1 10 14 4 0 4 4*0 3 0 4 ffffffa3 ffffffdb
  //   ffffffab 0 0 0 1 1 0 0 4 8 ffffffdb 2 ffffffe7 0 0 0 2 1 0 0 8 c 2 ffffffc7 12 1 c 10 3 0 3 4*0 2 0
  //   4 ffffffa3 ffffffdb ffffffab 0 0 0 1 1 0 0 4 8 ffffffdb ffffffc7 ffffffe7 1 8 c 2 0 2 4*0 1 0 4
  //   ffffffa3 ffffffc7 ffffffab 0 0 0 1 0 1
  //   contents of 评测数据WBPC (hex, n*v repeats v):
  //   6*0 4 8 c 10 14 18 1c 20 24 28 2c 2c 30 34 38 3c 0 0 1c 20 24 28 2c 2c 30 34 38 3c 0 0 1c 20 24 28
  //   2c 2c 30 34 38 3c 0 0 1c 20 24 28 2c 2c 30 34 38 3c 0 0 1c 20 24 28 2c 2c 30 34 38 3c 0 0 1c 20 24
  //   28 2c 2c 30 34 38 3c 0 0 1c 20 24 28 2c 2c 30 34 38 3c 0 0 1c 20 24 28 2c 2c 30 34 38 3c 0 0 1c 20
  //   24 28 2c 2c 30 34 38 3c 40 44 0 0 14 18 1c 20 24 28 2c 2c 30 34 38 3c 0 0 1c 20 24 28 2c 2c 30 34 38
  //   3c 0 0 1c 20 24 28 2c 2c 30 34 38 3c 0 0 1c 20 24 28 2c 2c 0 0 38 3c 0 0 1c 20 24 28 2c 2c 30 34 38
  //   3c 0 0 1c 20 24 28 2c 2c 30 34 38 3c 0 0 1c 20 24 28 2c 2c 30 34 38 3c 0 0 1c 20 24 28 2c 2c 30 34
  //   38 3c 40 44 0 0 14 18 1c 20 24 28 2c 2c 0 0 38 3c 0 0 1c 20 24 28 2c 2c 30 34 38 3c 0 0 1c 20 24 28
  //   2c 2c 0 0 38 3c 0 0 1c 20 24 28 2c 2c 30 34 38 3c 0 0 1c 20 24 28 2c 2c 30 34 38 3c 0 0 1c 20 24 28
  //   2c 2c 0 0 38 3c 0 0 1c 20 24 28 2c 2c 30 34 38 3c 40 44 0 0 14 18 1c 20 24 28 2c 2c 30 34 38 3c 0 0
  //   1c 20 24 28 2c 2c 0 0 38 3c 0 0 1c 20 24 28 2c 2c 30 34 38 3c 0 0 1c 20 24 28 2c 2c 30 34 38 3c 0 0
  //   1c 20 24 28 2c 2c 0 0 38 3c 0 0 1c 20 24 28 2c 2c 30 34 38 3c 40 44 0 0 14 18 1c 20 24 28 2c 2c 0 0
  //   38 3c 0 0 1c 20 24 28 2c 2c 30 34 38 3c 0 0 1c 20 24 28 2c 2c 0 0 38 3c 0 0 1c 20 24 28 2c 2c 0 0 38
  //   3c 0 0 1c 20 24 28 2c 2c 30 34 38 3c 40 44 0 0 14 18 1c 20 24 28 2c 2c 0 0 38 3c 0 0 1c 20 24 28 2c
  //   2c 0 0 38 3c 0 0 1c 20 24 28 2c 2c 0 0 38 3c 0 0 1c 20 24 28 2c 2c 30 34 38 3c 40 44 0 0 14 18 1c 20
  //   24 28 2c 2c 0 0 38 3c 0 0 1c 20 24 28 2c 2c 0 0 38 3c 0 0 1c 20 24 28 2c 2c 30 34 38 3c 40 44 0 0 14
  //   18 1c 20 24 28 2c 2c 0 0 38 3c 0 0 1c 20 24 28 2c 2c 30 34 38 3c 40 44 0 0 14 18 1c 20 24 28 2c 2c 0
  //   0 38 3c 40 44 48
  //   生成测试电路输出结果
  //   输出引脚
endmodule
